// Logisim project Bastian HW1_Q1.circ as structural Verilog: 1 circuit, main circuit main
module main (
  input  In0,
  input  In1,
  input  In2,
  input  In3,
  output out_5,
  output Out,
  output out_7,
  output out_8
);

  wire not_1_out, not_2_out, not_3_out, not_4_out;

  not not_1 (not_1_out, In0);
  not not_2 (not_2_out, In1);
  not not_3 (not_3_out, In2);
  not not_4 (not_4_out, In3);
  ExactlyOne xor_1 (.out(out_5), .in0(In0), .in1(In1), .in2(In2), .in3(In3));
  and and_1 (out_8, not_1_out, not_2_out, not_3_out, not_4_out);
  or or_1 (out_7, out_5, out_8);
  not not_5 (Out, out_7);

  // Notes on the sheet:
  //   Will be 1 iff exactly one input is 1
  //   Will be 1 iff all inputs are 0
  //   Will be 1 iff less than two inputs are 1
  //   Will be 1 iff two or more inputs are 1
endmodule
