// Logisim project Bastian HW1_Q2.circ as structural Verilog: 2 circuits, main circuit main
module \xor  (
  input  ln1,
  input  ln2,
  output Output
);

  wire transistor_1_out, transistor_4_out;

  Transistor transistor_1 (.in(1'b0), .out(transistor_1_out), .gate(ln1));
  Transistor transistor_2 (.in(transistor_1_out), .out(Output), .gate(ln2));
  Transistor #(.\type ("n")) transistor_3 (.in(transistor_4_out), .out(Output), .gate(ln1));
  Transistor #(.\type ("n")) transistor_4 (.in(1'b0), .out(transistor_4_out), .gate(ln2));
  Pull_Resistor #(.pull(1)) pull_resistor_1 (.node(Output));

  // Notes on the sheet:
  //   0 here if both inputs are 0
  //   0 here if both inputs are 1
  //   Flip the x to a 1 if either input is 1
endmodule

module main (
  input  in_1,
  input  in_2,
  input  in_3,
  input  in_4,
  input  in_5,
  input  in_6,
  input  in_7,
  input  in_8,
  output out_9,
  output out_10,
  output out_11,
  output out_12
);

  \xor  xor_1 (.ln1(in_1), .ln2(in_2), .Output(out_9));
  \xor  xor_2 (.ln1(in_3), .ln2(in_4), .Output(out_10));
  \xor  xor_3 (.ln1(in_5), .ln2(in_6), .Output(out_11));
  \xor  xor_4 (.ln1(in_7), .ln2(in_8), .Output(out_12));

  // Notes on the sheet:
  //   XOR Gate from Transistors
endmodule
