// Logisim project carter_bastian_hw10.circ as structural Verilog: 13 circuits, main circuit dpath
module ishim (
  input  req,
  input  [31:0] addr_in,
  input  reset,
  input  clock,
  input  fast_clock,
  input  [7:0] data_from_RAM,
  output [7:0] byte0,
  output [7:0] byte1,
  output [7:0] byte2,
  output [7:0] byte3,
  output [7:0] byte4,
  output [7:0] byte5,
  output ready,
  output RAMuse,
  output [31:0] RAMaddr,
  output RAMread
);

  wire decoder_1_out0, decoder_1_out1, decoder_1_out2, decoder_1_out3, decoder_1_out4, decoder_1_out5,
       decoder_1_out6, or_1_out;
  wire [2:0] _3bit_q;
  wire [31:0] adder_1_out, bit_extender_1_out;

  D_Flip_Flop d_ff_1 (.clk(clock), .D(req), .Q(RAMread), .Qn(ready), .preset(1'b0), .en(1'b1), .reset(or_1_out));
  Decoder #(.select(3), .disabled(0)) decoder_1 (
    .out0(decoder_1_out0), .out1(decoder_1_out1), .out2(decoder_1_out2), .out3(decoder_1_out3),
    .out4(decoder_1_out4), .out5(decoder_1_out5), .out6(decoder_1_out6), .sel(_3bit_q), .en(RAMread));  // open: out7
  Counter #(.width(3), .max('h7)) _3bit (
    .load(1'b0), .count(RAMread), .Q(_3bit_q), .clk(fast_clock), .clr(or_1_out));  // open: D, carry
  or or_1 (or_1_out, decoder_1_out6, reset);
  assign bit_extender_1_out = {{29{1'b0}}, _3bit_q};  // Bit_Extender bit_extender_1
  Adder #(.width(32)) adder_1 (.a(addr_in), .b(bit_extender_1_out), .out(adder_1_out), .cin(1'b0));  // open: cout
  assign RAMaddr = RAMread ? adder_1_out : 32'bz;  // Controlled_Buffer controlled_buffer_1
  Register register_1 (.D(data_from_RAM), .en(decoder_1_out0), .Q(byte0), .clk(fast_clock), .clr(reset));
  Register register_2 (.D(data_from_RAM), .en(decoder_1_out1), .Q(byte1), .clk(fast_clock), .clr(reset));
  Register register_3 (.D(data_from_RAM), .en(decoder_1_out2), .Q(byte2), .clk(fast_clock), .clr(reset));
  Register register_4 (.D(data_from_RAM), .en(decoder_1_out3), .Q(byte3), .clk(fast_clock), .clr(reset));
  Register register_5 (.D(data_from_RAM), .en(decoder_1_out4), .Q(byte4), .clk(fast_clock), .clr(reset));
  Register register_6 (.D(data_from_RAM), .en(decoder_1_out5), .Q(byte5), .clk(fast_clock), .clr(reset));

  assign RAMuse = RAMread;

  // Notes on the sheet:
  //   3-bit counter
endmodule

module dshim (
  input  [31:0] addr_in,
  input  [7:0] data_from_RAM,
  input  [31:0] DataIn,
  input  DMemWrite,
  input  req,
  input  reset,
  input  clock,
  input  fast_clock,
  output [31:0] DataOut,
  output [7:0] data_to_RAM,
  output RAMWrite,
  output RAMread,
  output RAMclk,
  output ready,
  output RAMuse,
  output [31:0] RAMaddr
);

  wire comparator_1_eq, d_ff_1_q, d_ff_1_qn, decoder_1_out0, decoder_1_out1, decoder_1_out2, decoder_1_out3,
       or_1_out;
  wire [1:0] bit_extender_2_out;
  wire [2:0] _3bit_q;
  wire [31:0] adder_1_out, bit_extender_1_out, register_1_q;

  assign bit_extender_1_out = {{29{1'b0}}, _3bit_q};  // Bit_Extender bit_extender_1
  D_Flip_Flop d_ff_1 (
    .clk(clock), .D(DMemWrite), .Q(d_ff_1_q), .Qn(d_ff_1_qn), .preset(1'b0), .en(1'b1), .reset(reset));
  D_Flip_Flop in_use (.clk(clock), .D(req), .Q(RAMuse), .Qn(ready), .preset(1'b0), .en(1'b1), .reset(or_1_out));
  Adder #(.width(32)) adder_1 (.a(addr_in), .b(bit_extender_1_out), .out(adder_1_out), .cin(1'b0));  // open: cout
  and and_1 (RAMWrite, RAMuse, d_ff_1_q);
  and and_2 (RAMread, d_ff_1_qn, RAMuse);
  Decoder #(.select(3), .disabled(0)) decoder_1 (
    .out0(decoder_1_out0), .out1(decoder_1_out1), .out2(decoder_1_out2), .out3(decoder_1_out3),
    .sel(_3bit_q), .en(RAMread));  // open: out4, out5, out6, out7
  Counter #(.width(3), .max('h7)) _3bit (
    .load(1'b0), .count(RAMuse), .Q(_3bit_q), .clk(fast_clock), .clr(or_1_out));  // open: D, carry
  or or_1 (or_1_out, comparator_1_eq, reset);
  Comparator #(.width(3)) comparator_1 (.a(_3bit_q), .b(3'b100), .eq(comparator_1_eq));  // open: gt, lt
  assign RAMaddr = RAMuse ? adder_1_out : 32'bz;  // Controlled_Buffer controlled_buffer_1
  Register #(.width(32), .trigger("high")) register_1 (
    .D(DataIn), .en(req), .Q(register_1_q), .clk(clock), .clr(reset));
  Bit_Extender #(.in_width(3), .out_width(2)) bit_extender_2 (.in(_3bit_q), .out(bit_extender_2_out));
  Multiplexer #(.select(2), .width(8)) multiplexer_1 (
    .in0(register_1_q[7:0]), .in1(register_1_q[15:8]), .in2(register_1_q[23:16]), .in3(register_1_q[31:24]),
    .out(data_to_RAM), .sel(bit_extender_2_out), .en(RAMWrite));
  Register register_2 (.D(data_from_RAM), .en(decoder_1_out0), .Q(DataOut[7:0]), .clk(fast_clock), .clr(reset));
  Register register_3 (.D(data_from_RAM), .en(decoder_1_out1), .Q(DataOut[15:8]), .clk(fast_clock), .clr(reset));
  Register register_4 (.D(data_from_RAM), .en(decoder_1_out2), .Q(DataOut[23:16]), .clk(fast_clock), .clr(reset));
  Register register_5 (.D(data_from_RAM), .en(decoder_1_out3), .Q(DataOut[31:24]), .clk(fast_clock), .clr(reset));
  and and_3 (RAMclk, fast_clock, RAMuse);

  // Notes on the sheet:
  //   writing?
  //   reading?
endmodule

module regwriter_box (
  input  [2:0] me,
  input  [2:0] dstE,
  input  reqE,
  input  [2:0] dstM,
  input  reqM,
  input  [31:0] valE,
  input  [31:0] valM,
  output [31:0] D0,
  output EN
);

  wire and_1_out, and_2_out, comparator_1_eq, comparator_2_eq;

  Comparator #(.width(3)) comparator_1 (.a(me), .b(dstE), .eq(comparator_1_eq));  // open: gt, lt
  Comparator #(.width(3)) comparator_2 (.a(me), .b(dstM), .eq(comparator_2_eq));  // open: gt, lt
  and and_1 (and_1_out, comparator_1_eq, reqE);
  and and_2 (and_2_out, comparator_2_eq, reqM);
  Multiplexer #(.width(32), .enable("false")) multiplexer_1 (.in0(valE), .in1(valM), .out(D0), .sel(and_2_out));
  or or_1 (EN, and_1_out, and_2_out);
endmodule

module regreader_box (
  input  [2:0] me,
  input  [2:0] srcA,
  input  [2:0] srcB,
  input  [31:0] Q,
  output [31:0] valA,
  output [31:0] valB
);

  wire comparator_1_eq, comparator_2_eq;

  Comparator #(.width(3)) comparator_1 (.a(me), .b(srcA), .eq(comparator_1_eq));  // open: gt, lt
  assign valA = comparator_1_eq ? Q : 32'bz;  // Controlled_Buffer controlled_buffer_1
  Comparator #(.width(3)) comparator_2 (.a(me), .b(srcB), .eq(comparator_2_eq));  // open: gt, lt
  assign valB = comparator_2_eq ? Q : 32'bz;  // Controlled_Buffer controlled_buffer_2
endmodule

module regwriter (
  input  [2:0] dstE,
  input  reqE,
  input  [2:0] dstM,
  input  reqM,
  input  [31:0] valE,
  input  [31:0] valM,
  input  clock,
  output [31:0] D0,
  output EN,
  output CLK,
  output [31:0] D1,
  output EN_2,
  output CLK_2,
  output [31:0] D2,
  output EN_3,
  output CLK_3,
  output [31:0] D3,
  output EN_4,
  output CLK_4,
  output [31:0] D4,
  output EN_5,
  output CLK_5,
  output [31:0] D5,
  output EN_6,
  output CLK_6,
  output [31:0] D6,
  output EN_7,
  output CLK_7,
  output [31:0] D7,
  output EN_8,
  output CLK_8
);

  regwriter_box regwriter_box_1 (
    .dstE(dstE), .reqE(reqE), .dstM(dstM), .reqM(reqM), .valE(valE), .valM(valM), .D0(D0), .EN(EN),
    .me(3'b000));
  regwriter_box regwriter_box_2 (
    .dstE(dstE), .reqE(reqE), .dstM(dstM), .reqM(reqM), .valE(valE), .valM(valM), .D0(D1), .EN(EN_2),
    .me(3'b001));
  regwriter_box regwriter_box_3 (
    .dstE(dstE), .reqE(reqE), .dstM(dstM), .reqM(reqM), .valE(valE), .valM(valM), .D0(D2), .EN(EN_3),
    .me(3'b010));
  regwriter_box regwriter_box_4 (
    .dstE(dstE), .reqE(reqE), .dstM(dstM), .reqM(reqM), .valE(valE), .valM(valM), .D0(D3), .EN(EN_4),
    .me(3'b011));
  regwriter_box regwriter_box_5 (
    .dstE(dstE), .reqE(reqE), .dstM(dstM), .reqM(reqM), .valE(valE), .valM(valM), .D0(D4), .EN(EN_5),
    .me(3'b100));
  regwriter_box regwriter_box_6 (
    .dstE(dstE), .reqE(reqE), .dstM(dstM), .reqM(reqM), .valE(valE), .valM(valM), .D0(D5), .EN(EN_6),
    .me(3'b101));
  regwriter_box regwriter_box_7 (
    .dstE(dstE), .reqE(reqE), .dstM(dstM), .reqM(reqM), .valE(valE), .valM(valM), .D0(D6), .EN(EN_7),
    .me(3'b110));
  regwriter_box regwriter_box_8 (
    .dstE(dstE), .reqE(reqE), .dstM(dstM), .reqM(reqM), .valE(valE), .valM(valM), .D0(D7), .EN(EN_8),
    .me(3'b111));

  assign CLK = clock;
  assign CLK_2 = clock;
  assign CLK_3 = clock;
  assign CLK_4 = clock;
  assign CLK_5 = clock;
  assign CLK_6 = clock;
  assign CLK_7 = clock;
  assign CLK_8 = clock;
endmodule

module regreader (
  input  [2:0] srcA,
  input  [2:0] srcB,
  input  [31:0] Q,
  input  [31:0] Q_2,
  input  [31:0] Q_3,
  input  reset,
  input  [31:0] Q_4,
  input  [31:0] Q_5,
  input  [31:0] Q_6,
  input  [31:0] Q_7,
  input  [31:0] Q_8,
  output CLR,
  output [31:0] valA,
  output [31:0] valB,
  output CLR_2,
  output CLR_3,
  output CLR_4,
  output CLR_5,
  output CLR_6,
  output CLR_7,
  output CLR_8
);

  regreader_box regreader_box_1 (.srcA(srcA), .srcB(srcB), .valA(valA), .valB(valB), .Q(Q), .me(3'b000));
  regreader_box regreader_box_2 (.srcA(srcA), .srcB(srcB), .valA(valA), .valB(valB), .Q(Q_2), .me(3'b001));
  regreader_box regreader_box_3 (.srcA(srcA), .srcB(srcB), .valA(valA), .valB(valB), .Q(Q_3), .me(3'b010));
  regreader_box regreader_box_4 (.srcA(srcA), .srcB(srcB), .valA(valA), .valB(valB), .Q(Q_4), .me(3'b011));
  regreader_box regreader_box_5 (.srcA(srcA), .srcB(srcB), .valA(valA), .valB(valB), .Q(Q_5), .me(3'b100));
  regreader_box regreader_box_6 (.srcA(srcA), .srcB(srcB), .valA(valA), .valB(valB), .Q(Q_6), .me(3'b101));
  regreader_box regreader_box_7 (.srcA(srcA), .srcB(srcB), .valA(valA), .valB(valB), .Q(Q_7), .me(3'b110));
  regreader_box regreader_box_8 (.srcA(srcA), .srcB(srcB), .valA(valA), .valB(valB), .Q(Q_8), .me(3'b111));

  assign CLR = reset;
  assign CLR_2 = reset;
  assign CLR_3 = reset;
  assign CLR_4 = reset;
  assign CLR_5 = reset;
  assign CLR_6 = reset;
  assign CLR_7 = reset;
  assign CLR_8 = reset;
endmodule

module dpath (
  input  Reset,
  output [7:0] out_2,
  output [31:0] out_3,
  output out_4,
  output [7:0] out_5
);

  wire aluBsel, aluOPsel, and_1_out, and_2_out, and_3_out, and_4_out, and_5_out, Clock_out, cnd_1_cnd,
       comparator_1_eq, comparator_2_eq, comparator_3_eq, comparator_4_eq, comparator_5_eq, comparator_6_gt,
       comparator_7_lt, controlled_buffer_2_out, d_ff_1_q, d_ff_1_qn, d_ff_2_q, D_RAMClock, D_RAMread,
       D_RAMuse, D_RAMWrite, DMemReady, DMemReq, DMemWrite, dstEsel, dstMreq, Fast_Clock_out, I_RAMread,
       I_RAMuse, IMemReady, IMemReq, io_1_kb_clear, io_1_kb_clock, io_1_tty_clear, io_1_tty_clock,
       io_1_tty_enable, keyboard_1_avail, ldCC, ldMAR, ldMDR, ldPC, MARsel, MDRsel, mmu_2_trap,
       multiplexer_8_out, or_1_out, or_2_out, or_3_out, or_4_out, pull_resistor_3_node, regreader_1_clr,
       regreader_1_clr_2, regreader_1_clr_3, regreader_1_clr_4, regreader_1_clr_5, regreader_1_clr_6,
       regreader_1_clr_7, regreader_1_clr_8, regwriter_1_clk, regwriter_1_clk_2, regwriter_1_clk_3,
       regwriter_1_clk_4, regwriter_1_clk_5, regwriter_1_clk_6, regwriter_1_clk_7, regwriter_1_clk_8,
       regwriter_1_en, regwriter_1_en_2, regwriter_1_en_3, regwriter_1_en_4, regwriter_1_en_5,
       regwriter_1_en_6, regwriter_1_en_7, regwriter_1_en_8, srcAsel, srcBsel, valCsel;
  wire [1:0] aluAsel, dstEreq, newPCsel, PCIncSel;
  wire [2:0] alu_1_cc, bit_extender_1_out, bit_extender_2_out, bit_extender_3_out, bit_extender_4_out, cc;
  wire [3:0] icode, ifun, isplit_1_ra, isplit_1_rb, multiplexer_5_out, multiplexer_6_out, multiplexer_7_out,
       multiplexer_11_out;
  wire [5:0] microseq_1_next_state, register_1_q;
  wire [6:0] io_1_out_14, keyboard_1_data;
  wire [7:0] D_Data_from_RAM, I_Data_from_RAM, ishim_1_byte0, ishim_1_byte1, ishim_1_byte2, ishim_1_byte3,
       ishim_1_byte4, ishim_1_byte5, ram_1_data;
  wire [15:0] mmu_2_out_10, mmu_2_out_10_2;
  wire [31:0] adder_1_out, alu_1_vale, dshim_1_dataout, eax_q, ebp_q, ebx_q, ecx_q, edi_q, edx_q, esi_q,
       esp_q, I_RAMAddr, isplit_1_d_v, isplit_1_dest, MAR_q, MDR_q, multiplexer_1_out, multiplexer_2_out,
       multiplexer_3_out, multiplexer_4_out, multiplexer_9_out, multiplexer_10_out, multiplexer_12_out,
       multiplexer_13_out, PC_q, regreader_1_vala, regreader_1_valb, regwriter_1_d0, regwriter_1_d1,
       regwriter_1_d2, regwriter_1_d3, regwriter_1_d4, regwriter_1_d5, regwriter_1_d6, regwriter_1_d7;
  wire [31:24] rom_1_data;

  Register #(.width(32)) PC (.D(multiplexer_2_out), .en(ldPC), .Q(PC_q), .clk(out_4), .clr(Reset));
  assign out_4 = d_ff_1_qn ? Clock_out : 1'bz;  // Controlled_Buffer controlled_buffer_1
  Clock #(.highDuration(16), .lowDuration(16)) Clock (.out(Clock_out));
  assign controlled_buffer_2_out = d_ff_1_qn ? Fast_Clock_out : 1'bz;  // Controlled_Buffer controlled_buffer_2
  Clock Fast_Clock (.out(Fast_Clock_out));
  Register #(.width(6), .trigger("falling")) register_1 (
    .D(microseq_1_next_state), .Q(register_1_q), .clk(out_4), .clr(Reset));  // open: en
  // Probe on IMemReq
  // Probe on PCIncSel
  // Probe on multiplexer_1_out
  Multiplexer #(.select(2), .width(32), .enable("false")) multiplexer_1 (
    .in0(32'h1), .in1(32'h2), .in2(32'h5), .in3(32'h6), .out(multiplexer_1_out), .sel(PCIncSel));
  // Probe on valCsel
  Adder #(.width(32)) adder_1 (.a(multiplexer_1_out), .b(PC_q), .out(adder_1_out));  // open: cin, cout
  CND cnd_1 (.ZSO(cc), .ifun(ifun), .CND(cnd_1_cnd));
  ishim ishim_1 (
    .req(IMemReq), .byte0(ishim_1_byte0), .byte1(ishim_1_byte1), .byte2(ishim_1_byte2), .addr_in(PC_q),
    .byte3(ishim_1_byte3), .byte4(ishim_1_byte4), .byte5(ishim_1_byte5), .ready(IMemReady), .reset(Reset),
    .clock(out_4), .fast_clock(controlled_buffer_2_out), .RAMuse(I_RAMuse), .RAMaddr(I_RAMAddr),
    .RAMread(I_RAMread), .data_from_RAM(I_Data_from_RAM));
  // Probe on srcAsel
  Multiplexer #(.select(2), .width(32), .enable("false")) multiplexer_2 (
    .in0(adder_1_out), .in1(multiplexer_4_out), .in2(dshim_1_dataout), .in3(multiplexer_3_out),
    .out(multiplexer_2_out), .sel(newPCsel));
  Multiplexer #(.width(32), .enable("false")) multiplexer_3 (
    .in0(adder_1_out), .in1(multiplexer_4_out), .out(multiplexer_3_out), .sel(cnd_1_cnd));
  isplit isplit_1 (
    .B0(ishim_1_byte0), .B1(ishim_1_byte1), .B2(ishim_1_byte2), .B3(ishim_1_byte3), .B4(ishim_1_byte4),
    .B5(ishim_1_byte5), .icode(icode), .ifun(ifun), .rA(isplit_1_ra), .rB(isplit_1_rb), .Dest(isplit_1_dest),
    .D_V(isplit_1_d_v));
  // Probe on srcBsel
  // Probe on dstEsel
  // Probe on icode
  // Probe on ifun
  Multiplexer #(.width(32), .enable("false")) multiplexer_4 (
    .in0(isplit_1_dest), .in1(isplit_1_d_v), .out(multiplexer_4_out), .sel(valCsel));
  // Probe on dstEreq
  // Probe on isplit_1_ra
  // Probe on isplit_1_rb
  // Probe on dstMreq
  ROM #(.addrWidth(6), .dataWidth(32)) rom_1 (
    .addr(register_1_q),
    .data({rom_1_data, IMemReq, PCIncSel, valCsel, srcAsel, srcBsel, dstEsel, dstEreq, dstMreq, aluAsel, aluBsel, aluOPsel, ldCC, MARsel, ldMAR, MDRsel, ldMDR, DMemReq, DMemWrite, newPCsel, ldPC}));  // open: sel
  Multiplexer #(.width(4), .enable("false")) multiplexer_5 (
    .in0(isplit_1_rb), .in1(4'b0100), .out(multiplexer_5_out), .sel(dstEsel));
  Multiplexer #(.width(4), .enable("false")) multiplexer_6 (
    .in0(isplit_1_ra), .in1(4'b0100), .out(multiplexer_6_out), .sel(srcAsel));
  Multiplexer #(.width(4), .enable("false")) multiplexer_7 (
    .in0(isplit_1_rb), .in1(4'b0100), .out(multiplexer_7_out), .sel(srcBsel));
  Comparator #(.width(4)) comparator_1 (.a(isplit_1_rb), .b(4'b1111), .eq(comparator_1_eq));  // open: gt, lt
  // Probe on aluAsel
  Bit_Extender #(.in_width(4), .out_width(3)) bit_extender_1 (.in(multiplexer_5_out), .out(bit_extender_1_out));
  Multiplexer #(.select(2), .enable("false")) multiplexer_8 (
    .in0(1'b0), .in1(1'b1), .in2(cnd_1_cnd), .out(multiplexer_8_out), .sel(dstEreq));  // open: in3
  Bit_Extender #(.in_width(4), .out_width(3)) bit_extender_2 (.in(isplit_1_ra), .out(bit_extender_2_out));
  Bit_Extender #(.in_width(4), .out_width(3)) bit_extender_3 (.in(multiplexer_6_out), .out(bit_extender_3_out));
  Bit_Extender #(.in_width(4), .out_width(3)) bit_extender_4 (.in(multiplexer_7_out), .out(bit_extender_4_out));
  // Probe on aluBsel
  Register #(.width(32)) eax (
    .D(regwriter_1_d0), .en(regwriter_1_en), .Q(eax_q), .clk(regwriter_1_clk), .clr(regreader_1_clr));
  regwriter regwriter_1 (
    .dstE(bit_extender_1_out), .reqE(multiplexer_8_out), .dstM(bit_extender_2_out), .reqM(dstMreq),
    .valE(alu_1_vale), .valM(dshim_1_dataout), .clock(out_4), .D0(regwriter_1_d0), .EN(regwriter_1_en),
    .CLK(regwriter_1_clk), .D1(regwriter_1_d1), .EN_2(regwriter_1_en_2), .CLK_2(regwriter_1_clk_2),
    .D2(regwriter_1_d2), .EN_3(regwriter_1_en_3), .CLK_3(regwriter_1_clk_3), .D3(regwriter_1_d3),
    .EN_4(regwriter_1_en_4), .CLK_4(regwriter_1_clk_4), .D4(regwriter_1_d4), .EN_5(regwriter_1_en_5),
    .CLK_5(regwriter_1_clk_5), .D5(regwriter_1_d5), .EN_6(regwriter_1_en_6), .CLK_6(regwriter_1_clk_6),
    .D6(regwriter_1_d6), .EN_7(regwriter_1_en_7), .CLK_7(regwriter_1_clk_7), .D7(regwriter_1_d7),
    .EN_8(regwriter_1_en_8), .CLK_8(regwriter_1_clk_8));
  Register #(.width(32)) ecx (
    .D(regwriter_1_d1), .en(regwriter_1_en_2), .Q(ecx_q), .clk(regwriter_1_clk_2), .clr(regreader_1_clr_2));
  Register #(.width(32)) edx (
    .D(regwriter_1_d2), .en(regwriter_1_en_3), .Q(edx_q), .clk(regwriter_1_clk_3), .clr(regreader_1_clr_3));
  Register #(.width(32)) ebx (
    .D(regwriter_1_d3), .en(regwriter_1_en_4), .Q(ebx_q), .clk(regwriter_1_clk_4), .clr(regreader_1_clr_4));
  Register #(.width(32)) esp (
    .D(regwriter_1_d4), .en(regwriter_1_en_5), .Q(esp_q), .clk(regwriter_1_clk_5), .clr(regreader_1_clr_5));
  Register #(.width(32)) ebp (
    .D(regwriter_1_d5), .en(regwriter_1_en_6), .Q(ebp_q), .clk(regwriter_1_clk_6), .clr(regreader_1_clr_6));
  Register #(.width(32)) esi (
    .D(regwriter_1_d6), .en(regwriter_1_en_7), .Q(esi_q), .clk(regwriter_1_clk_7), .clr(regreader_1_clr_7));
  Register #(.width(32)) edi (
    .D(regwriter_1_d7), .en(regwriter_1_en_8), .Q(edi_q), .clk(regwriter_1_clk_8), .clr(regreader_1_clr_8));
  // Probe on aluOPsel
  // Probe on ldCC
  regreader regreader_1 (
    .srcA(bit_extender_3_out), .srcB(bit_extender_4_out), .valA(regreader_1_vala), .valB(regreader_1_valb),
    .reset(Reset), .CLR(regreader_1_clr), .Q(eax_q), .CLR_2(regreader_1_clr_2), .Q_2(ecx_q),
    .CLR_3(regreader_1_clr_3), .Q_3(edx_q), .CLR_4(regreader_1_clr_4), .Q_4(ebx_q),
    .CLR_5(regreader_1_clr_5), .Q_5(esp_q), .CLR_6(regreader_1_clr_6), .Q_6(ebp_q),
    .CLR_7(regreader_1_clr_7), .Q_7(esi_q), .CLR_8(regreader_1_clr_8), .Q_8(edi_q));
  // Probe on regreader_1_vala
  // Probe on regreader_1_valb
  // Probe on multiplexer_4_out
  // Probe on MARsel
  // Probe on ldMAR
  microseq microseq_1 (
    .Current_State(register_1_q), .select(rom_1_data[25:24]), .icode(icode), .valN(rom_1_data[31:26]),
    .DMemReady(DMemReady), .IMemReady(IMemReady), .Next_State(microseq_1_next_state));
  Multiplexer #(.select(2), .width(32), .enable("false")) multiplexer_9 (
    .in0(regreader_1_vala), .in1(multiplexer_4_out), .in2(32'h4), .in3(32'hfffffffc),
    .out(multiplexer_9_out), .sel(aluAsel));
  // Probe on MDRsel
  Multiplexer #(.width(32), .enable("false")) multiplexer_10 (
    .in0(regreader_1_valb), .in1({32{1'b0}}), .out(multiplexer_10_out), .sel(aluBsel));
  alu alu_1 (
    .CC(alu_1_cc), .ALU_A(multiplexer_9_out), .valE(alu_1_vale), .ALU_B(multiplexer_10_out),
    .ALU_op(multiplexer_11_out));
  Multiplexer #(.width(4), .enable("false")) multiplexer_11 (
    .in0(4'b0000), .in1(ifun), .out(multiplexer_11_out), .sel(aluOPsel));
  // Probe on ldMDR
  // Probe on DMemReq
  // Probe on cc
  Register #(.width(3)) u_CC (.D(alu_1_cc), .en(ldCC), .Q(cc), .clk(out_4), .clr(Reset));
  // Probe on DMemWrite
  // Probe on adder_1_out
  // Probe on alu_1_vale
  Multiplexer #(.width(32), .enable("false")) multiplexer_12 (
    .in0(regreader_1_vala), .in1(adder_1_out), .out(multiplexer_12_out), .sel(MDRsel));
  Multiplexer #(.width(32), .enable("false")) multiplexer_13 (
    .in0(alu_1_vale), .in1(regreader_1_vala), .out(multiplexer_13_out), .sel(MARsel));
  // Probe on newPCsel
  Register #(.width(32)) MDR (.D(multiplexer_12_out), .en(ldMDR), .Q(MDR_q), .clk(out_4), .clr(Reset));
  Register #(.width(32)) MAR (.D(multiplexer_13_out), .en(ldMAR), .Q(MAR_q), .clk(out_4), .clr(Reset));
  // Probe on ldPC
  // Probe on dshim_1_dataout
  Comparator #(.width(4)) comparator_2 (.a(icode), .b(4'b1110), .eq(comparator_2_eq));  // open: gt, lt
  dshim dshim_1 (
    .DataOut(dshim_1_dataout), .addr_in(MAR_q), .data_from_RAM(D_Data_from_RAM), .DataIn(MDR_q),
    .data_to_RAM(out_2), .RAMWrite(D_RAMWrite), .DMemWrite(DMemWrite), .RAMread(D_RAMread), .req(DMemReq),
    .RAMclk(D_RAMClock), .ready(DMemReady), .reset(Reset), .clock(out_4),
    .fast_clock(controlled_buffer_2_out), .RAMuse(D_RAMuse), .RAMaddr(out_3));
  and and_1 (and_1_out, ~out_4, mmu_2_trap);  // AND_Gate
  or or_1 (or_1_out, or_3_out, and_1_out);
  Comparator #(.width(4)) comparator_3 (.a(4'b1100), .b(icode), .eq(comparator_3_eq));  // open: gt, lt
  Comparator #(.width(4)) comparator_4 (.a(icode), .b(4'b1101), .eq(comparator_4_eq));  // open: gt, lt
  D_Flip_Flop d_ff_1 (.clk(or_1_out), .D(1'b1), .Q(d_ff_1_q), .Qn(d_ff_1_qn));  // open: preset, en, reset
  and and_2 (and_2_out, comparator_3_eq, IMemReady, ~IMemReq);  // AND_Gate
  and and_3 (and_3_out, comparator_4_eq, IMemReady, ~IMemReq);  // AND_Gate
  MMU mmu_1 ();  // open: in_1, in_2, in_3, I_RAM_use, D_RAM_use, D_RAM_Write, RAM_clock, reset, privbit, out_10, TRAP
  LED led_1 (.in(d_ff_1_q));
  or or_2 (or_2_out, and_2_out, and_3_out);
  D_Flip_Flop d_ff_2 (.clk(or_2_out), .D(comparator_4_eq), .Q(d_ff_2_q), .reset(Reset));  // open: Qn, preset, en
  MMU mmu_2 (
    .in_1(I_RAMAddr), .in_2(out_3), .in_3(out_2), .I_RAM_use(I_RAMuse), .D_RAM_use(D_RAMuse),
    .D_RAM_Write(D_RAMWrite), .RAM_clock(D_RAMClock), .reset(Reset), .privbit(d_ff_2_q),
    .out_10({mmu_2_out_10_2, mmu_2_out_10}), .TRAP(mmu_2_trap));
  Pull_Resistor pull_resistor_1 (.node({mmu_2_out_10_2, mmu_2_out_10}));
  or or_3 (or_3_out, pull_resistor_3_node, and_4_out);
  Comparator #(.width(16)) comparator_5 (.a(mmu_2_out_10_2), .b({16{1'b0}}), .eq(comparator_5_eq));  // open: gt, lt
  Comparator #(.width(32), .mode("unsigned")) comparator_6 (
    .a({mmu_2_out_10_2, mmu_2_out_10}), .b(32'hffff), .gt(comparator_6_gt));  // open: eq, lt
  Comparator #(.width(32), .mode("unsigned")) comparator_7 (
    .a({mmu_2_out_10_2, mmu_2_out_10}), .b(32'hfffe00), .lt(comparator_7_lt));  // open: gt, eq
  and and_4 (and_4_out, comparator_6_gt, comparator_7_lt);
  RAM #(.addrWidth(16), .bus("separate")) ram_1 (
    .addr(mmu_2_out_10), .din(out_2), .data(ram_1_data), .str(D_RAMWrite), .sel(comparator_5_eq),
    .clk(D_RAMClock), .ld(or_4_out), .clr(Reset));
  or or_4 (or_4_out, D_RAMread, I_RAMread);
  Pull_Resistor pull_resistor_2 (.node(comparator_7_lt));
  Pull_Resistor pull_resistor_3 (.node(pull_resistor_3_node));
  Comparator #(.width(32), .mode("unsigned")) comparator_8 (
    .a({mmu_2_out_10_2, mmu_2_out_10}), .b(32'hfffe0f), .gt(pull_resistor_3_node));  // open: eq, lt
  and and_5 (and_5_out, ~d_ff_2_q, D_RAMClock);  // AND_Gate
  io io_1 (
    .RAM_Use(D_RAMuse), .in_4({mmu_2_out_10_2, mmu_2_out_10}), .in_5(out_2), .RAM_Read(D_RAMread),
    .RAM_Write(D_RAMWrite), .RAM_clock(and_5_out), .out_13(ram_1_data), .in_2(keyboard_1_data),
    .KB_Status(keyboard_1_avail), .KB_Clock(io_1_kb_clock), .out_14(io_1_out_14), .TTY_Clock(io_1_tty_clock),
    .reset(Reset), .KB_Clear(io_1_kb_clear), .TTY_Clear(io_1_tty_clear), .TTY_Enable(io_1_tty_enable));  // open: TTY_Ready
  Demultiplexer #(.select(2), .width(8)) demultiplexer_1 (
    .out1(D_Data_from_RAM), .out2(I_Data_from_RAM), .in(ram_1_data), .sel({I_RAMuse, D_RAMuse}));  // open: out0, out3, en
  Keyboard keyboard_1 (
    .clk(io_1_kb_clock), .clr(io_1_kb_clear), .avail(keyboard_1_avail), .data(keyboard_1_data));  // open: re
  TTY tty_1 (.data(io_1_out_14), .clk(io_1_tty_clock), .we(io_1_tty_enable), .clr(io_1_tty_clear));

  assign out_5 = out_2;

  // Other names for the same wires on the sheet: Clock = out_4; D_Data_to_RAM[7:0] = out_2; D_RAMAddr[31:0] = out_3

  // Notes on the sheet:
  //   Y86 Skeleton
  //   May 10, 2015
  //   Fetch
  //   BUG FIX
  //   connect to memory!
  //   valP
  //   valM
  //   Decode
  //   Control ROM
  //   contents of rom_1 (hex, n*v repeats v):
  //   3800000 1004000 1000005 46*0 1000001 1210801 1709801 27010b9 6705091 1208601 1400007 246b0fb a0ea195
  //   226b0b9 62ee191 1000003 1000003 11000000
  //   SWS and Taylor Cathcart and Vijay Kothari, based on a skeleton from Matt Kretchmar
  //   rB == F?
  //   Info about how to move
  //   to the next state
  //   Execute
  //   Control valves according to the current state
  //   Current State
  //   Next State Select
  //   valN
  //   Memory
  //   PC
  //   connect to memory (and io,
  //    pretending to be memory)
  //   If we get a memory trap,
  //   Stop the clock and set the red light
  //   privmode flip-flop
  //   2-bit Selector value
  //   selector = 01 => D RAM
  //   selector = 10 =>I Ram
  //   Split RAMaddr
  //   RAMaddr bits 0 - 9
  //   0x0 - 0xFFFF
  //   Memory Trap IF:
  //   1. Addr > ffff && Addr < fffe00 
  //   2. Addr > 00fe0f
  //   IO "Fake RAM"
endmodule

module RAM_testing (
  input  [9:0] in_1,
  input  [7:0] in_2,
  input  in_3,
  input  in_4,
  input  in_5,
  input  in_6,
  input  in_7,
  output [7:0] out_8
);

  RAM #(.addrWidth(10), .bus("separate")) ram_1 (
    .addr(in_1), .din(in_2), .data(out_8), .str(in_3), .sel(in_4), .clk(in_7), .ld(in_5), .clr(in_6));
  RAM #(.addrWidth(10), .bus("separate")) ram_2 ();  // open: addr, din, data, str, sel, clk, ld, clr
  RAM #(.addrWidth(10), .bus("separate")) ram_3 ();  // open: addr, din, data, str, sel, clk, ld, clr
endmodule

module isplit (
  input  [7:0] B0,
  input  [7:0] B1,
  input  [7:0] B2,
  input  [7:0] B3,
  input  [7:0] B4,
  input  [7:0] B5,
  output [3:0] icode,
  output [3:0] ifun,
  output [3:0] rA,
  output [3:0] rB,
  output [31:0] Dest,
  output [31:0] D_V
);


  assign D_V = {B5, B4, B3, B2};
  assign Dest = {B4, B3, B2, B1};
  assign icode = B0[7:4];
  assign ifun = B0[3:0];
  assign rA = B1[7:4];
  assign rB = B1[3:0];
endmodule

module alu (
  input  [31:0] ALU_A,
  input  [31:0] ALU_B,
  input  [3:0] ALU_op,
  output [2:0] CC,
  output [31:0] valE
);

  wire and_2_out, msb_1_msb, msb_2_msb, msb_3_msb, nor_1_out, xnor_1_out, xor_2_out;
  wire [31:0] adder_1_out, and_1_out, multiplexer_1_out, not_1_out, xor_1_out;

  assign not_1_out = ~ALU_A;  // NOT_Gate not_1, 32 bits wide
  assign and_1_out = ALU_A & ALU_B;  // AND_Gate and_1, 32 bits wide
  assign xor_1_out = ALU_A ^ ALU_B;  // XOR_Gate xor_1, 32 bits wide
  nor nor_1 (nor_1_out, ALU_op[2], ALU_op[3]);
  MSB msb_1 (.MSB(msb_1_msb), .Value(ALU_B));
  MSB msb_2 (.MSB(msb_2_msb), .Value(multiplexer_1_out));
  Multiplexer #(.width(32), .enable("false")) multiplexer_1 (
    .in0(ALU_A), .in1(not_1_out), .out(multiplexer_1_out), .sel(ALU_op[0]));
  xnor xnor_1 (xnor_1_out, msb_2_msb, msb_1_msb);
  xor xor_2 (xor_2_out, msb_2_msb, msb_3_msb);
  MSB msb_3 (.MSB(msb_3_msb), .Value(adder_1_out));
  Adder #(.width(32)) adder_1 (.a(multiplexer_1_out), .b(ALU_B), .out(adder_1_out), .cin(ALU_op[0]));  // open: cout
  Multiplexer #(.disabled(0), .enable("false")) multiplexer_2 (
    .in0(and_2_out), .in1(1'b0), .out(CC[0]), .sel(ALU_op[1]));
  and and_2 (and_2_out, xnor_1_out, xor_2_out);
  Comparator #(.width(32)) comparator_1 (.a({32{1'b0}}), .b(valE), .eq(CC[2]));  // open: gt, lt
  MSB msb_4 (.MSB(CC[1]), .Value(valE));
  Multiplexer #(.select(2), .width(32), .disabled(0)) multiplexer_3 (
    .in0(adder_1_out), .in1(adder_1_out), .in2(and_1_out), .in3(xor_1_out), .out(valE), .sel(ALU_op[1:0]),
    .en(nor_1_out));

  // Notes on the sheet:
  //   add
  //   sub
  //   32-bit and
  //   32-bit xor
  //   or if both inputs are positive and result is negatve
  //   if both inputs are negative and result is positve
  //   an overflow occurred
  //   if sub carry in = 1
  //   (Zero Bit, Signed Bit, Overflow Bit)
  //   add
  //   sub
  //   and
  //   xor
  //   op selector
  //   is legit op?
endmodule

module MSB (
  input  [31:0] Value,
  output MSB
);


  assign MSB = Value[31];
endmodule

module CND (
  input  [2:0] ZSO,
  input  [3:0] ifun,
  output CND
);

  wire not_1_out, not_2_out, not_3_out, not_4_out, or_1_out, xor_1_out;

  or or_1 (or_1_out, ZSO[2], xor_1_out);
  xor xor_1 (xor_1_out, ZSO[1], ZSO[0]);
  not not_1 (not_1_out, ZSO[2]);
  not not_2 (not_2_out, xor_1_out);
  not not_3 (not_3_out, or_1_out);
  Multiplexer #(.select(3), .disabled(0)) multiplexer_1 (
    .in0(1'b1), .in1(or_1_out), .in2(xor_1_out), .in3(ZSO[2]), .in4(not_1_out), .in5(not_2_out),
    .in6(not_3_out), .in7(1'b0), .out(CND), .sel(ifun[2:0]), .en(not_4_out));
  not not_4 (not_4_out, ifun[3]);

  // Notes on the sheet:
  //   Sample CND, from SWS
  //   always
  //   le
  //   l
  //   e
  //   ne
  //   ge
  //   g
endmodule

module MMU (
  input  [31:0] in_1,
  input  [31:0] in_2,
  input  [7:0] in_3,
  input  I_RAM_use,
  input  D_RAM_use,
  input  D_RAM_Write,
  input  RAM_clock,
  input  reset,
  input  privbit,
  output [31:0] out_10,
  output TRAP
);

  wire and_1_out, and_2_out, and_3_out, comparator_1_eq, comparator_2_eq, comparator_3_eq, comparator_4_eq,
       comparator_5_eq, comparator_6_eq, comparator_7_eq, comparator_8_eq, comparator_9_eq, comparator_10_eq,
       comparator_11_eq, comparator_12_eq, comparator_13_eq, comparator_14_eq, comparator_15_eq,
       comparator_16_eq, comparator_17_eq, comparator_17_gt, comparator_18_eq, or_1_out;
  wire [1:0] multiplexer_1_out_4;
  wire [7:0] multiplexer_1_out_2, multiplexer_1_out_3, multiplexer_1_out_5, register_1_q, register_2_q,
       register_3_q, register_4_q, register_5_q, register_6_q, register_7_q, register_8_q, register_9_q,
       register_10_q, register_11_q, register_12_q, register_13_q, register_14_q, register_15_q,
       register_16_q;
  wire [7:2] multiplexer_1_out;
  wire [31:0] multiplexer_2_out;

  or or_1 (or_1_out, D_RAM_use, I_RAM_use);
  Multiplexer #(.select(2), .width(32), .enable("false")) multiplexer_1 (
    .in1(in_1), .in2(in_2),
    .out({multiplexer_1_out_3, multiplexer_1_out_2, multiplexer_1_out, multiplexer_1_out_4, multiplexer_1_out_5}),
    .sel({D_RAM_use, I_RAM_use}));  // open: in0, in3
  Comparator #(.width(32), .mode("unsigned")) comparator_1 (
    .a({multiplexer_1_out_3, multiplexer_1_out_2, multiplexer_1_out, multiplexer_1_out_4, multiplexer_1_out_5}),
    .b(32'h2000), .eq(comparator_1_eq));  // open: gt, lt
  Comparator #(.width(32), .mode("unsigned")) comparator_2 (
    .a({multiplexer_1_out_3, multiplexer_1_out_2, multiplexer_1_out, multiplexer_1_out_4, multiplexer_1_out_5}),
    .b(32'h2001), .eq(comparator_2_eq));  // open: gt, lt
  Comparator #(.width(32), .mode("unsigned")) comparator_3 (
    .a({multiplexer_1_out_3, multiplexer_1_out_2, multiplexer_1_out, multiplexer_1_out_4, multiplexer_1_out_5}),
    .b(32'h2002), .eq(comparator_3_eq));  // open: gt, lt
  Comparator #(.width(32), .mode("unsigned")) comparator_4 (
    .a({multiplexer_1_out_3, multiplexer_1_out_2, multiplexer_1_out, multiplexer_1_out_4, multiplexer_1_out_5}),
    .b(32'h2003), .eq(comparator_4_eq));  // open: gt, lt
  Comparator #(.width(32), .mode("unsigned")) comparator_5 (
    .a({multiplexer_1_out_3, multiplexer_1_out_2, multiplexer_1_out, multiplexer_1_out_4, multiplexer_1_out_5}),
    .b(32'h2004), .eq(comparator_5_eq));  // open: gt, lt
  Comparator #(.width(32), .mode("unsigned")) comparator_6 (
    .a({multiplexer_1_out_3, multiplexer_1_out_2, multiplexer_1_out, multiplexer_1_out_4, multiplexer_1_out_5}),
    .b(32'h2005), .eq(comparator_6_eq));  // open: gt, lt
  Comparator #(.width(32), .mode("unsigned")) comparator_7 (
    .a({multiplexer_1_out_3, multiplexer_1_out_2, multiplexer_1_out, multiplexer_1_out_4, multiplexer_1_out_5}),
    .b(32'h6), .eq(comparator_7_eq));  // open: gt, lt
  Comparator #(.width(32), .mode("unsigned")) comparator_8 (
    .a({multiplexer_1_out_3, multiplexer_1_out_2, multiplexer_1_out, multiplexer_1_out_4, multiplexer_1_out_5}),
    .b(32'h2007), .eq(comparator_8_eq));  // open: gt, lt
  Comparator #(.width(32), .mode("unsigned")) comparator_9 (
    .a({multiplexer_1_out_3, multiplexer_1_out_2, multiplexer_1_out, multiplexer_1_out_4, multiplexer_1_out_5}),
    .b(32'h2008), .eq(comparator_9_eq));  // open: gt, lt
  Comparator #(.width(32), .mode("unsigned")) comparator_10 (
    .a({multiplexer_1_out_3, multiplexer_1_out_2, multiplexer_1_out, multiplexer_1_out_4, multiplexer_1_out_5}),
    .b(32'h2009), .eq(comparator_10_eq));  // open: gt, lt
  Comparator #(.width(32), .mode("unsigned")) comparator_11 (
    .a({multiplexer_1_out_3, multiplexer_1_out_2, multiplexer_1_out, multiplexer_1_out_4, multiplexer_1_out_5}),
    .b(32'h200a), .eq(comparator_11_eq));  // open: gt, lt
  Comparator #(.width(32), .mode("unsigned")) comparator_12 (
    .a({multiplexer_1_out_3, multiplexer_1_out_2, multiplexer_1_out, multiplexer_1_out_4, multiplexer_1_out_5}),
    .b(32'h200b), .eq(comparator_12_eq));  // open: gt, lt
  Comparator #(.width(32), .mode("unsigned")) comparator_13 (
    .a({multiplexer_1_out_3, multiplexer_1_out_2, multiplexer_1_out, multiplexer_1_out_4, multiplexer_1_out_5}),
    .b(32'h200c), .eq(comparator_13_eq));  // open: gt, lt
  Comparator #(.width(32), .mode("unsigned")) comparator_14 (
    .a({multiplexer_1_out_3, multiplexer_1_out_2, multiplexer_1_out, multiplexer_1_out_4, multiplexer_1_out_5}),
    .b(32'h200d), .eq(comparator_14_eq));  // open: gt, lt
  Comparator #(.width(32), .mode("unsigned")) comparator_15 (
    .a({multiplexer_1_out_3, multiplexer_1_out_2, multiplexer_1_out, multiplexer_1_out_4, multiplexer_1_out_5}),
    .b(32'h200e), .eq(comparator_15_eq));  // open: gt, lt
  Comparator #(.width(32), .mode("unsigned")) comparator_16 (
    .a({multiplexer_1_out_3, multiplexer_1_out_2, multiplexer_1_out, multiplexer_1_out_4, multiplexer_1_out_5}),
    .b(32'h200f), .eq(comparator_16_eq));  // open: gt, lt
  and and_1 (and_1_out, D_RAM_Write, ~privbit, RAM_clock);  // AND_Gate
  Register register_1 (.D(in_3), .en(comparator_4_eq), .Q(register_1_q), .clk(and_1_out), .clr(reset));
  Register register_2 (.D(in_3), .en(comparator_8_eq), .Q(register_2_q), .clk(and_1_out), .clr(reset));
  Register register_3 (.D(in_3), .en(comparator_12_eq), .Q(register_3_q), .clk(and_1_out), .clr(reset));
  Register register_4 (.D(in_3), .en(comparator_16_eq), .Q(register_4_q), .clk(and_1_out), .clr(reset));
  Register register_5 (.D(in_3), .en(comparator_3_eq), .Q(register_5_q), .clk(and_1_out), .clr(reset));
  Register register_6 (.D(in_3), .en(comparator_7_eq), .Q(register_6_q), .clk(and_1_out), .clr(reset));
  Register register_7 (.D(in_3), .en(comparator_11_eq), .Q(register_7_q), .clk(and_1_out), .clr(reset));
  Register register_8 (.D(in_3), .en(comparator_15_eq), .Q(register_8_q), .clk(and_1_out), .clr(reset));
  Register register_9 (.D(in_3), .en(comparator_2_eq), .Q(register_9_q), .clk(and_1_out), .clr(reset));
  Register register_10 (.D(in_3), .en(comparator_6_eq), .Q(register_10_q), .clk(and_1_out), .clr(reset));
  Register register_11 (.D(in_3), .en(comparator_10_eq), .Q(register_11_q), .clk(and_1_out), .clr(reset));
  Register register_12 (.D(in_3), .en(comparator_14_eq), .Q(register_12_q), .clk(and_1_out), .clr(reset));
  Register register_13 (.D(in_3), .en(comparator_1_eq), .Q(register_13_q), .clk(and_1_out), .clr(reset));
  Register register_14 (.D(in_3), .en(comparator_5_eq), .Q(register_14_q), .clk(and_1_out), .clr(reset));
  Register register_15 (.D(in_3), .en(comparator_9_eq), .Q(register_15_q), .clk(and_1_out), .clr(reset));
  Register register_16 (.D(in_3), .en(comparator_13_eq), .Q(register_16_q), .clk(and_1_out), .clr(reset));
  Multiplexer #(.select(2), .width(32), .enable("false")) multiplexer_2 (
    .in0({register_1_q, register_5_q, register_9_q, register_13_q}),
    .in1({register_2_q, register_6_q, register_10_q, register_14_q}),
    .in2({register_3_q, register_7_q, register_11_q, register_15_q}),
    .in3({register_4_q, register_8_q, register_12_q, register_16_q}), .out(multiplexer_2_out),
    .sel(multiplexer_1_out_4));
  Comparator #(.width(32), .mode("unsigned")) comparator_17 (
    .a({multiplexer_1_out_3, multiplexer_1_out_2, multiplexer_1_out, multiplexer_1_out_4, multiplexer_1_out_5}),
    .b(32'h400), .gt(comparator_17_gt), .eq(comparator_17_eq), .lt(comparator_17_eq));
  Comparator #(.mode("unsigned")) comparator_18 (
    .a(multiplexer_2_out[7:0]), .b({8{1'b0}}), .eq(comparator_18_eq));  // open: gt, lt
  Pull_Resistor pull_resistor_1 (.node({multiplexer_1_out_3, multiplexer_1_out_2, multiplexer_1_out, multiplexer_1_out_4, multiplexer_1_out_5}));
  and and_2 (and_2_out, comparator_18_eq, or_1_out, privbit);
  and and_3 (and_3_out, comparator_17_gt, privbit);
  Multiplexer #(.select(2), .width(32), .enable("false")) multiplexer_3 (
    .in0({multiplexer_1_out_3, multiplexer_1_out_2, multiplexer_1_out, multiplexer_1_out_4, multiplexer_1_out_5}),
    .in1({multiplexer_2_out[31:8], multiplexer_1_out_5}), .out(out_10), .sel({TRAP, privbit}));  // open: in2, in3
  or or_2 (TRAP, and_2_out, and_3_out);

  // Notes on the sheet:
  //   Data to RAM
  //   I RAM Addr
  //   D RAM Addr
  //   Input Addr
  //   Page Table
  //   Entry 1
  //   Entry 2
  //   Entry 3
  //   Entry 0
  //   Virtual Addr
  //   Physical Addr
  //   Throw Trap if Unprivileged and jump-table entry invalid
  //   Throw trap if unprivileged and trying to access mem past 0x400
endmodule
