// Logisim project carter_bastian_hw6_q2.circ as structural Verilog: 2 circuits, main circuit microseq
module microseq (
  input  [5:0] Current_State,
  input  [1:0] select,
  input  [3:0] icode,
  input  [5:0] valN,
  input  DMemReady,
  input  IMemReady,
  output [5:0] Next_State
);

  wire [5:0] multiplexer_1_out, multiplexer_2_out;

  Multiplexer #(.width(6)) multiplexer_1 (
    .in0(Current_State), .in1(valN), .out(multiplexer_1_out), .sel(DMemReady));  // open: en
  Multiplexer #(.width(6)) multiplexer_2 (
    .in0(Current_State), .in1({2'b11, icode}), .out(multiplexer_2_out), .sel(IMemReady));  // open: en
  Multiplexer #(.select(2), .width(6)) multiplexer_3 (
    .in0(Current_State), .in1(valN), .in2(multiplexer_1_out), .in3(multiplexer_2_out), .out(Next_State),
    .sel(select));  // open: en

  // Notes on the sheet:
  //   01 => valN
  //   00 => Current State
  //   10 => current state (if DMem = 0)
  //   OR valN (if DMem = 1)
  //   11 => currentState (if IMem = 0)
  //   OR "11"+icode (if IMem = 1)
endmodule

module microseq_Testing (
  input  [5:0] in_1,
  input  [1:0] in_2,
  input  [3:0] in_3,
  input  [5:0] in_4,
  input  in_5,
  input  in_6,
  output [5:0] out_7
);

  microseq microseq_1 (
    .Current_State(in_1), .select(in_2), .icode(in_3), .valN(in_4), .DMemReady(in_5), .IMemReady(in_6),
    .Next_State(out_7));
endmodule
