// Logisim project io-sample.circ as structural Verilog: 1 circuit, main circuit io
module io (
  input  KB_Status,
  input  [6:0] in_2,
  input  RAM_Use,
  input  [31:0] in_4,
  input  [7:0] in_5,
  input  RAM_Read,
  input  RAM_Write,
  input  TTY_Ready,
  input  RAM_clock,
  input  reset,
  output KB_Clock,
  output KB_Clear,
  output [7:0] out_13,
  output [6:0] out_14,
  output TTY_Enable,
  output TTY_Clock,
  output TTY_Clear
);

  wire and_2_out, and_3_out, and_4_out, and_5_out, and_6_out, and_8_out, comparator_1_eq, comparator_2_lt,
       comparator_3_eq, comparator_4_eq, comparator_5_eq, comparator_6_eq;
  wire [7:0] bit_extender_1_out, bit_extender_2_out, bit_extender_3_out, register_1_q, register_2_q,
       register_3_q, register_4_q;
  wire [31:0] and_1_out;

  assign and_1_out = in_4 & 32'hfffffff0;  // AND_Gate and_1, 32 bits wide
  and and_2 (and_2_out, RAM_Read, ~RAM_Write);  // AND_Gate
  and and_3 (and_3_out, ~RAM_Read, RAM_Write);  // AND_Gate
  Comparator #(.width(32)) comparator_1 (.a(and_1_out), .b(32'hfffe00), .eq(comparator_1_eq));  // open: gt, lt
  Comparator #(.width(32)) comparator_2 (.a(in_4), .b(32'hfffe0c), .lt(comparator_2_lt));  // open: gt, eq
  Comparator #(.width(32)) comparator_3 (.a(32'hfffe00), .b(in_4), .eq(comparator_3_eq));  // open: gt, lt
  and and_4 (and_4_out, comparator_3_eq, RAM_Use, and_2_out);
  Comparator #(.width(32)) comparator_4 (.a(32'hfffe04), .b(in_4), .eq(comparator_4_eq));  // open: gt, lt
  and and_5 (and_5_out, comparator_4_eq, RAM_Use, and_2_out);
  Comparator #(.width(32)) comparator_5 (.a(32'hfffe08), .b(in_4), .eq(comparator_5_eq));  // open: gt, lt
  and and_6 (and_6_out, comparator_5_eq, RAM_Use, and_2_out);
  Comparator #(.width(32)) comparator_6 (.a(32'hfffe0c), .b(in_4), .eq(comparator_6_eq));  // open: gt, lt
  and and_7 (TTY_Enable, comparator_6_eq, RAM_Use, and_3_out);
  and and_8 (and_8_out, comparator_1_eq, comparator_2_lt, ~and_4_out, ~and_5_out, ~and_6_out, RAM_Use, and_2_out);  // AND_Gate
  assign bit_extender_1_out = {{7{1'b0}}, KB_Status};  // Bit_Extender bit_extender_1
  assign bit_extender_2_out = {{1{1'b0}}, in_2};  // Bit_Extender bit_extender_2
  not not_1 (KB_Clock, and_5_out);
  assign bit_extender_3_out = {{7{1'b0}}, TTY_Ready};  // Bit_Extender bit_extender_3
  Register #(.trigger("high")) register_1 (
    .D(bit_extender_1_out), .en(1'b1), .Q(register_1_q), .clk(and_4_out));  // open: clr
  Register #(.trigger("high")) register_2 (
    .D(bit_extender_2_out), .en(1'b1), .Q(register_2_q), .clk(and_5_out));  // open: clr
  Register #(.trigger("high")) register_3 (
    .D(bit_extender_3_out), .en(1'b1), .Q(register_3_q), .clk(and_6_out));  // open: clr
  Register #(.trigger("high")) register_4 (.D(in_5), .en(1'b1), .Q(register_4_q), .clk(TTY_Enable));  // open: clr
  Bit_Extender #(.out_width(7)) bit_extender_4 (.in(register_4_q), .out(out_14));
  assign out_13 = and_8_out ? {8{1'b0}} : 8'bz;  // Controlled_Buffer controlled_buffer_1
  assign out_13 = and_4_out ? register_1_q : 8'bz;  // Controlled_Buffer controlled_buffer_2
  assign out_13 = and_5_out ? register_2_q : 8'bz;  // Controlled_Buffer controlled_buffer_3
  assign out_13 = and_6_out ? register_3_q : 8'bz;  // Controlled_Buffer controlled_buffer_4

  assign KB_Clear = reset;
  assign TTY_Clear = reset;
  assign TTY_Clock = RAM_clock;

  // Notes on the sheet:
  //   RAM Address
  //   Incoming Data
  //   RAM Exclusive Read
  //   RAM ExclusiveWrite
  //   valid read request
  //   to non-DDR byte
  //   that is zero
  //   read request
  //   to relevant
  //   byte of KBSR
  //   read request
  //   to relevant
  //   byte of KBDR
  //   read request
  //   to relevant
  //   byte of DSR
  //   write request
  //   to relevant
  //   byte of DDR
  //   Keyboard Status Register
  //   High-Level Triggered
  //   Keyboard Data Register
  //   High-Level Triggered
  //   Display Status Register
  //   High-Level Triggered
  //   Display Data Register
  //   High-Level Triggered
  //   KB Data
  //   Outgoing Data
  //   TTY Data
endmodule
