// Logisim project carter_bastian_hw2_q1.circ as structural Verilog: 5 circuits, main circuit main
module main (
  input  [3:0] Month,
  input  [3:0] in_2,
  input  [3:0] Day,
  input  [3:0] in_4,
  output Data_Output,
  output Error_Output_Bit
);

  wire and_1_out, and_2_out, and_3_out, day_1_invalid_day, day_1_out_4, day_1_out_5, error_1_out_2,
       error_2_out_2, error_3_out_2, error_4_out_2, month_1__30_day_month, month_1__31_day_month,
       month_1_out_3, nor_1_out;

  Error error_1 (.out_2(error_1_out_2), .in_1(Month));
  Error error_2 (.out_2(error_2_out_2), .in_1(in_2));
  Error error_3 (.out_2(error_3_out_2), .in_1(Day));
  or or_1 (Error_Output_Bit, error_1_out_2, error_2_out_2, error_3_out_2, error_4_out_2);
  Error error_4 (.out_2(error_4_out_2), .in_1(in_4));
  Month month_1 (
    .First_Digit___d1(Month), .in_2(in_2), .out_3(month_1_out_3), ._30_Day_Month(month_1__30_day_month),
    ._31_Day_Month(month_1__31_day_month));  // open: _28_Day_Month
  Day day_1 (
    .Digit_1___d1(Day), .Digit_2___d2(in_4), .Invalid_Day(day_1_invalid_day), .out_4(day_1_out_4),
    .out_5(day_1_out_5));  // open: Day___31
  and and_1 (and_1_out, month_1__31_day_month, nor_1_out);
  and and_2 (and_2_out, day_1_out_4, nor_1_out);
  nor nor_1 (nor_1_out, month_1_out_3, day_1_invalid_day, Error_Output_Bit);
  and and_3 (and_3_out, month_1__30_day_month, day_1_out_5, nor_1_out);
  or or_2 (Data_Output, and_1_out, and_2_out, and_3_out);

  // Notes on the sheet:
  //   Outputs 1 if we have an error
  //   1 means valid inputs
  //   28 or less days => valid date
  //   31 days in month => valid date
  //   Middle case:
  //   30-day month w/ 29-30 days
endmodule

module Error (
  input  [3:0] in_1,
  output out_2
);

  wire and_1_out, and_2_out, not_1_out, not_2_out, not_3_out, not_4_out, not_5_out, not_6_out;

  not not_1 (not_1_out, in_1[3]);
  not not_2 (not_2_out, in_1[2]);
  not not_3 (not_3_out, in_1[0]);
  not not_4 (not_4_out, in_1[1]);
  and and_1 (and_1_out, in_1[3], not_2_out, not_4_out, not_3_out);
  nor nor_1 (out_2, not_1_out, and_1_out, and_2_out);
  not not_5 (not_5_out, in_1[2]);
  not not_6 (not_6_out, in_1[1]);
  and and_2 (and_2_out, in_1[3], not_5_out, not_6_out, in_1[0]);

  // Notes on the sheet:
  //   BCD < 8
  //   BCD = 8
  //   Outputs 1 if none of the above conditions are true
  //   Tests if input is binary coded decimal
  //   BCD = 9
endmodule

module Month (
  input  [3:0] First_Digit___d1,
  input  [3:0] in_2,
  output out_3,
  output _28_Day_Month,
  output _30_Day_Month,
  output _31_Day_Month
);

  wire and_1_out, and_2_out, and_4_out, and_5_out, and_6_out, and_7_out, digit_decoder_1_second_digit_0,
       digit_decoder_1_second_digit_1, digit_decoder_1_second_digit_2, digit_decoder_1_second_digit_3,
       digit_decoder_1_second_digit_4, digit_decoder_1_second_digit_5, digit_decoder_1_second_digit_6,
       digit_decoder_1_second_digit_7, digit_decoder_1_second_digit_8, digit_decoder_1_second_digit_9,
       nor_1_out, nor_2_out, not_1_out, not_2_out, not_3_out, not_4_out, not_5_out, not_6_out, not_7_out,
       or_1_out, or_3_out, or_4_out;

  not not_1 (not_1_out, First_Digit___d1[3]);
  not not_2 (not_2_out, First_Digit___d1[2]);
  not not_3 (not_3_out, First_Digit___d1[1]);
  not not_4 (not_4_out, First_Digit___d1[0]);
  not not_5 (not_5_out, First_Digit___d1[3]);
  not not_6 (not_6_out, First_Digit___d1[2]);
  not not_7 (not_7_out, First_Digit___d1[1]);
  and and_1 (and_1_out, not_1_out, not_2_out, not_3_out, not_4_out);
  and and_2 (and_2_out, not_5_out, not_6_out, not_7_out, First_Digit___d1[0]);
  nor nor_1 (nor_1_out, and_1_out, and_2_out);
  digit_decoder digit_decoder_1 (
    .in_1(in_2), .Second_digit_0(digit_decoder_1_second_digit_0),
    .Second_Digit_1(digit_decoder_1_second_digit_1), .Second_Digit_2(digit_decoder_1_second_digit_2),
    .Second_Digit_3(digit_decoder_1_second_digit_3), .Second_Digit_4(digit_decoder_1_second_digit_4),
    .Second_Digit_5(digit_decoder_1_second_digit_5), .Second_Digit_6(digit_decoder_1_second_digit_6),
    .Second_Digit_7(digit_decoder_1_second_digit_7), .Second_Digit_8(digit_decoder_1_second_digit_8),
    .Second_Digit_9(digit_decoder_1_second_digit_9));
  and and_3 (_28_Day_Month, and_1_out, digit_decoder_1_second_digit_2);
  and and_4 (and_4_out, and_1_out, or_1_out);
  or or_1 (or_1_out, digit_decoder_1_second_digit_4, digit_decoder_1_second_digit_6, digit_decoder_1_second_digit_9);
  and and_5 (and_5_out, and_2_out, digit_decoder_1_second_digit_1);
  or or_2 (_30_Day_Month, and_5_out, and_4_out);
  or or_3 (or_3_out, digit_decoder_1_second_digit_1, digit_decoder_1_second_digit_3, digit_decoder_1_second_digit_5, digit_decoder_1_second_digit_7, digit_decoder_1_second_digit_8);
  and and_6 (and_6_out, and_1_out, or_3_out);
  or or_4 (or_4_out, digit_decoder_1_second_digit_0, digit_decoder_1_second_digit_2);
  or or_5 (_31_Day_Month, and_6_out, and_7_out);
  and and_7 (and_7_out, and_2_out, or_4_out);
  nor nor_2 (nor_2_out, _30_Day_Month, _28_Day_Month, _31_Day_Month);
  or or_6 (out_3, nor_1_out, nor_2_out);

  // Notes on the sheet:
  //   Second Digit = d2
  //   d2 = 0
  //   d2 = 1
  //   d2 > 1
  //   Feb = 28-day month
  //   30-day months with d1=0
  //   30-day months with d1=1
  //   31-day months with d1=0
  //   31-day months with d1=1
  //   Invalid Month
endmodule

module digit_decoder (
  input  [3:0] in_1,
  output Second_digit_0,
  output Second_Digit_1,
  output Second_Digit_2,
  output Second_Digit_3,
  output Second_Digit_4,
  output Second_Digit_5,
  output Second_Digit_6,
  output Second_Digit_7,
  output Second_Digit_8,
  output Second_Digit_9
);

  wire not_1_out, not_2_out, not_3_out, not_4_out, not_5_out, not_6_out, not_7_out, not_8_out, not_9_out,
       not_10_out, not_11_out, not_12_out, not_13_out, not_14_out, not_15_out, not_16_out, not_17_out,
       not_18_out, not_19_out, not_20_out, not_21_out, not_22_out, not_23_out, not_24_out, not_25_out;

  not not_1 (not_1_out, in_1[3]);
  not not_2 (not_2_out, in_1[2]);
  not not_3 (not_3_out, in_1[1]);
  not not_4 (not_4_out, in_1[0]);
  not not_5 (not_5_out, in_1[3]);
  not not_6 (not_6_out, in_1[2]);
  not not_7 (not_7_out, in_1[1]);
  not not_8 (not_8_out, in_1[3]);
  not not_9 (not_9_out, in_1[2]);
  not not_10 (not_10_out, in_1[0]);
  not not_11 (not_11_out, in_1[3]);
  not not_12 (not_12_out, in_1[2]);
  not not_13 (not_13_out, in_1[3]);
  not not_14 (not_14_out, in_1[1]);
  not not_15 (not_15_out, in_1[0]);
  not not_16 (not_16_out, in_1[3]);
  not not_17 (not_17_out, in_1[1]);
  not not_18 (not_18_out, in_1[3]);
  not not_19 (not_19_out, in_1[0]);
  not not_20 (not_20_out, in_1[3]);
  not not_21 (not_21_out, in_1[2]);
  not not_22 (not_22_out, in_1[1]);
  not not_23 (not_23_out, in_1[0]);
  not not_24 (not_24_out, in_1[2]);
  not not_25 (not_25_out, in_1[1]);
  and and_1 (Second_digit_0, not_1_out, not_2_out, not_3_out, not_4_out);
  and and_2 (Second_Digit_1, not_5_out, not_6_out, not_7_out, in_1[0]);
  and and_3 (Second_Digit_2, not_8_out, not_9_out, in_1[1], not_10_out);
  and and_4 (Second_Digit_3, not_11_out, not_12_out, in_1[1], in_1[0]);
  and and_5 (Second_Digit_4, not_13_out, in_1[2], not_14_out, not_15_out);
  and and_6 (Second_Digit_5, not_16_out, in_1[2], not_17_out, in_1[0]);
  and and_7 (Second_Digit_6, not_18_out, in_1[2], in_1[1], not_19_out);
  and and_8 (Second_Digit_7, not_20_out, in_1[2], in_1[1], in_1[0]);
  and and_9 (Second_Digit_8, in_1[3], not_21_out, not_22_out, not_23_out);
  and and_10 (Second_Digit_9, in_1[3], not_24_out, not_25_out, in_1[0]);

  // Notes on the sheet:
  //   Decodes a BCD into a Digit 0 - 9
endmodule

module Day (
  input  [3:0] Digit_1___d1,
  input  [3:0] Digit_2___d2,
  output Invalid_Day,
  output out_4,
  output out_5,
  output Day___31
);

  wire and_1_out, and_2_out, and_3_out, and_4_out, and_5_out, digit_decoder_1_second_digit_0,
       digit_decoder_1_second_digit_1, digit_decoder_1_second_digit_2, digit_decoder_1_second_digit_3,
       digit_decoder_2_second_digit_0, digit_decoder_2_second_digit_1, digit_decoder_2_second_digit_9,
       nor_1_out, not_1_out, not_2_out, or_1_out;

  digit_decoder digit_decoder_1 (
    .in_1(Digit_1___d1), .Second_digit_0(digit_decoder_1_second_digit_0),
    .Second_Digit_1(digit_decoder_1_second_digit_1), .Second_Digit_2(digit_decoder_1_second_digit_2),
    .Second_Digit_3(digit_decoder_1_second_digit_3));  // open: Second_Digit_4, Second_Digit_5, Second_Digit_6, Second_Digit_7, Second_Digit_8, Second_Digit_9
  digit_decoder digit_decoder_2 (
    .in_1(Digit_2___d2), .Second_digit_0(digit_decoder_2_second_digit_0),
    .Second_Digit_1(digit_decoder_2_second_digit_1), .Second_Digit_9(digit_decoder_2_second_digit_9));  // open: Second_Digit_2, Second_Digit_3, Second_Digit_4, Second_Digit_5, Second_Digit_6, Second_Digit_7, Second_Digit_8
  and and_1 (and_1_out, digit_decoder_1_second_digit_0, digit_decoder_2_second_digit_0);
  not not_1 (not_1_out, and_1_out);
  or or_1 (or_1_out, digit_decoder_1_second_digit_0, digit_decoder_1_second_digit_1);
  and and_2 (and_2_out, digit_decoder_1_second_digit_2, not_2_out);
  not not_2 (not_2_out, digit_decoder_2_second_digit_9);
  and and_3 (and_3_out, not_1_out, or_1_out);
  or or_2 (out_4, and_3_out, and_2_out);
  and and_4 (and_4_out, digit_decoder_1_second_digit_2, digit_decoder_2_second_digit_9);
  and and_5 (and_5_out, digit_decoder_1_second_digit_3, digit_decoder_2_second_digit_0);
  or or_3 (out_5, and_4_out, and_5_out);
  and and_6 (Day___31, digit_decoder_1_second_digit_3, digit_decoder_2_second_digit_1);
  nor nor_1 (nor_1_out, out_4, out_5, Day___31);
  or or_4 (Invalid_Day, nor_1_out, and_1_out);

  // Notes on the sheet:
  //   Day = 0
  //   day < 29
  //   Day = 29 or 30
endmodule
