// Logisim project carter_bastian_hw3_q1.circ as structural Verilog: 1 circuit, main circuit main
module main (
  input  in_1,
  input  data,
  input  in_3,
  input  enable,
  input  in_5,
  output Q,
  output Not_Q
);

  wire d_ff_1_q, d_ff_1_qn, nand_1_out, nand_2_out, not_1_out;

  nand nand_1 (nand_1_out, in_1, nand_2_out);
  nand nand_2 (nand_2_out, nand_1_out, data);
  D_Flip_Flop #(.trigger("high")) d_ff_1 (
    .clk(in_1), .D(nand_1_out), .Q(d_ff_1_q), .Qn(d_ff_1_qn), .preset(1'b0), .en(1'b1), .reset(1'b0));
  not not_1 (not_1_out, d_ff_1_qn);
  D_Flip_Flop #(.trigger("high")) d_ff_2 (
    .clk(d_ff_1_q), .D(not_1_out), .Q(Q), .Qn(Not_Q), .preset(in_3), .en(enable), .reset(in_5));

  // Notes on the sheet:
  //   clock
  //   This Nand gate blocks subsequent changes
  //   to value stored by first high-value flip-flop
  //   reset
  //   set
endmodule
