// Logisim project carter_bastian_hw3_q2-3.circ as structural Verilog: 3 circuits, main circuit q0: FF testing
module q0__FF_testing (
  input  in_1,
  input  in_2,
  input  in_3,
  input  in_4,
  input  in_5,
  output out_6,
  output out_7
);

  D_Flip_Flop d_ff_1 (.clk(in_1), .D(in_2), .Q(out_6), .Qn(out_7), .preset(in_3), .en(in_4), .reset(in_5));
endmodule

module q2__register_prologue (
  input  [3:0] enable,
  input  in_2,
  input  clock,
  input  reset,
  output [3:0] out_5
);

  Register #(.width(4)) register_1 (.D(enable), .en(in_2), .Q(out_5), .clk(clock), .clr(reset));

  // Notes on the sheet:
  //   I played with this.
endmodule

module q3__FF_to_Register (
  input  [3:0] in_1,
  input  enable,
  input  in_3,
  input  in_4,
  output [3:0] out_5
);

  Hex_Digit_Display hex_digit_display_1 (.value(in_1));  // open: dp
  D_Flip_Flop d_ff_1 (.clk(in_3), .D(in_1[0]), .Q(out_5[0]), .preset(1'b0), .en(enable), .reset(in_4));  // open: Qn
  D_Flip_Flop d_ff_2 (.clk(in_3), .D(in_1[1]), .Q(out_5[1]), .preset(1'b0), .en(enable), .reset(in_4));  // open: Qn
  D_Flip_Flop d_ff_3 (.clk(in_3), .D(in_1[2]), .Q(out_5[2]), .preset(1'b0), .en(enable), .reset(in_4));  // open: Qn
  D_Flip_Flop d_ff_4 (.clk(in_3), .D(in_1[3]), .Q(out_5[3]), .preset(1'b0), .en(enable), .reset(in_4));  // open: Qn
  Hex_Digit_Display hex_digit_display_2 (.value(out_5));  // open: dp

  // Notes on the sheet:
  //   clock
  //   reset
endmodule
