// Logisim project carter_bastian_hw3_q4.circ as structural Verilog: 3 circuits, main circuit regwriter
module hw3 (
  input  [31:0] valE,
  input  [31:0] valM,
  input  [2:0] dstE,
  input  reqE,
  input  [2:0] dstM,
  input  reqM,
  input  clock,
  input  [2:0] srcA,
  input  [2:0] srcB,
  input  clr,
  output [31:0] valA,
  output [31:0] valB
);

  wire regreader_1_clr, regreader_1_clr_2, regreader_1_clr_3, regreader_1_clr_4, regreader_1_clr_5,
       regreader_1_clr_6, regreader_1_clr_7, regreader_1_clr_8, regwriter_1_clk, regwriter_1_clk_2,
       regwriter_1_clk_3, regwriter_1_clk_4, regwriter_1_clk_5, regwriter_1_clk_6, regwriter_1_clk_7,
       regwriter_1_clk_8, regwriter_1_en, regwriter_1_en_2, regwriter_1_en_3, regwriter_1_en_4,
       regwriter_1_en_5, regwriter_1_en_6, regwriter_1_en_7, regwriter_1_en_8;
  wire [31:0] register_1_q, register_2_q, register_3_q, register_4_q, register_5_q, register_6_q,
       register_7_q, register_8_q, regwriter_1_d0, regwriter_1_d1, regwriter_1_d2, regwriter_1_d3,
       regwriter_1_d4, regwriter_1_d5, regwriter_1_d6, regwriter_1_d7;

  regwriter regwriter_1 (
    .dstE(dstE), .reqE(reqE), .dstM(dstM), .reqM(reqM), .valE(valE), .valM(valM), .clock(clock),
    .D0(regwriter_1_d0), .EN(regwriter_1_en), .CLK(regwriter_1_clk), .D1(regwriter_1_d1),
    .EN_2(regwriter_1_en_2), .CLK_2(regwriter_1_clk_2), .D2(regwriter_1_d2), .EN_3(regwriter_1_en_3),
    .CLK_3(regwriter_1_clk_3), .D3(regwriter_1_d3), .EN_4(regwriter_1_en_4), .CLK_4(regwriter_1_clk_4),
    .D4(regwriter_1_d4), .EN_5(regwriter_1_en_5), .CLK_5(regwriter_1_clk_5), .D5(regwriter_1_d5),
    .EN_6(regwriter_1_en_6), .CLK_6(regwriter_1_clk_6), .D6(regwriter_1_d6), .EN_7(regwriter_1_en_7),
    .CLK_7(regwriter_1_clk_7), .D7(regwriter_1_d7), .EN_8(regwriter_1_en_8), .CLK_8(regwriter_1_clk_8));
  Register #(.width(32)) register_1 (
    .D(regwriter_1_d0), .en(regwriter_1_en), .Q(register_1_q), .clk(regwriter_1_clk), .clr(regreader_1_clr));
  Register #(.width(32)) register_2 (
    .D(regwriter_1_d1), .en(regwriter_1_en_2), .Q(register_2_q), .clk(regwriter_1_clk_2),
    .clr(regreader_1_clr_2));
  Register #(.width(32)) register_3 (
    .D(regwriter_1_d2), .en(regwriter_1_en_3), .Q(register_3_q), .clk(regwriter_1_clk_3),
    .clr(regreader_1_clr_3));
  Register #(.width(32)) register_4 (
    .D(regwriter_1_d3), .en(regwriter_1_en_4), .Q(register_4_q), .clk(regwriter_1_clk_4),
    .clr(regreader_1_clr_4));
  Register #(.width(32)) register_5 (
    .D(regwriter_1_d4), .en(regwriter_1_en_5), .Q(register_5_q), .clk(regwriter_1_clk_5),
    .clr(regreader_1_clr_5));
  Register #(.width(32)) register_6 (
    .D(regwriter_1_d5), .en(regwriter_1_en_6), .Q(register_6_q), .clk(regwriter_1_clk_6),
    .clr(regreader_1_clr_6));
  Register #(.width(32)) register_7 (
    .D(regwriter_1_d6), .en(regwriter_1_en_7), .Q(register_7_q), .clk(regwriter_1_clk_7),
    .clr(regreader_1_clr_7));
  Register #(.width(32)) register_8 (
    .D(regwriter_1_d7), .en(regwriter_1_en_8), .Q(register_8_q), .clk(regwriter_1_clk_8),
    .clr(regreader_1_clr_8));
  regreader regreader_1 (
    .srcA(srcA), .srcB(srcB), .valA(valA), .valB(valB), .reset(clr), .CLR(regreader_1_clr), .Q(register_1_q),
    .CLR_2(regreader_1_clr_2), .Q_2(register_2_q), .CLR_3(regreader_1_clr_3), .Q_3(register_3_q),
    .CLR_4(regreader_1_clr_4), .Q_4(register_4_q), .CLR_5(regreader_1_clr_5), .Q_5(register_5_q),
    .CLR_6(regreader_1_clr_6), .Q_6(register_6_q), .CLR_7(regreader_1_clr_7), .Q_7(register_7_q),
    .CLR_8(regreader_1_clr_8), .Q_8(register_8_q));

  // Notes on the sheet:
  //   D0
  //   en0
  //   clk0
  //   D7
  //   en7
  //   clk7
  //   R0
  //   R1
  //   R2
  //   R3
  //   R4
  //   R5
  //   R6
  //   R7
  //   Q0
  //   clr0
  //   Q7
  //   clr7
endmodule

module regwriter (
  input  [2:0] dstE,
  input  reqE,
  input  [2:0] dstM,
  input  reqM,
  input  [31:0] valE,
  input  [31:0] valM,
  input  clock,
  output [31:0] D0,
  output EN,
  output CLK,
  output [31:0] D1,
  output EN_2,
  output CLK_2,
  output [31:0] D2,
  output EN_3,
  output CLK_3,
  output [31:0] D3,
  output EN_4,
  output CLK_4,
  output [31:0] D4,
  output EN_5,
  output CLK_5,
  output [31:0] D5,
  output EN_6,
  output CLK_6,
  output [31:0] D6,
  output EN_7,
  output CLK_7,
  output [31:0] D7,
  output EN_8,
  output CLK_8
);

  wire and_1_out, and_2_out, and_3_out, and_4_out, and_5_out, and_6_out, and_7_out, and_8_out, and_9_out,
       and_10_out, and_11_out, and_12_out, and_13_out, and_14_out, and_15_out, and_16_out, decoder_1_out0,
       decoder_1_out1, decoder_1_out2, decoder_1_out3, decoder_1_out4, decoder_1_out5, decoder_1_out6,
       decoder_1_out7, decoder_2_out0, decoder_2_out1, decoder_2_out2, decoder_2_out3, decoder_2_out4,
       decoder_2_out5, decoder_2_out6, decoder_2_out7;
  wire [2:2] comparator_1_eq;
  wire [31:0] demultiplexer_1_out0, demultiplexer_1_out1, demultiplexer_1_out2, demultiplexer_1_out3,
       demultiplexer_1_out4, demultiplexer_1_out5, demultiplexer_1_out6, demultiplexer_1_out7,
       demultiplexer_2_out0, demultiplexer_2_out1, demultiplexer_2_out2, demultiplexer_2_out3,
       demultiplexer_2_out4, demultiplexer_2_out5, demultiplexer_2_out6, demultiplexer_2_out7, or_1_out,
       or_2_out, or_3_out, or_4_out, or_5_out, or_6_out, or_7_out, or_8_out;

  Decoder #(.select(3)) decoder_1 (
    .out0(decoder_1_out0), .out1(decoder_1_out1), .out2(decoder_1_out2), .out3(decoder_1_out3),
    .out4(decoder_1_out4), .out5(decoder_1_out5), .out6(decoder_1_out6), .out7(decoder_1_out7), .sel(dstE));  // open: en
  Decoder #(.select(3)) decoder_2 (
    .out0(decoder_2_out0), .out1(decoder_2_out1), .out2(decoder_2_out2), .out3(decoder_2_out3),
    .out4(decoder_2_out4), .out5(decoder_2_out5), .out6(decoder_2_out6), .out7(decoder_2_out7), .sel(dstM));  // open: en
  Demultiplexer #(.select(3), .width(32)) demultiplexer_1 (
    .out0(demultiplexer_1_out0), .out1(demultiplexer_1_out1), .out2(demultiplexer_1_out2),
    .out3(demultiplexer_1_out3), .out4(demultiplexer_1_out4), .out5(demultiplexer_1_out5),
    .out6(demultiplexer_1_out6), .out7(demultiplexer_1_out7), .in(valE), .sel(dstE));  // open: en
  Demultiplexer #(.select(3), .width(32)) demultiplexer_2 (
    .out0(demultiplexer_2_out0), .out1(demultiplexer_2_out1), .out2(demultiplexer_2_out2),
    .out3(demultiplexer_2_out3), .out4(demultiplexer_2_out4), .out5(demultiplexer_2_out5),
    .out6(demultiplexer_2_out6), .out7(demultiplexer_2_out7), .in(valM), .sel(dstM));  // open: en
  Comparator #(.width(3)) comparator_1 (.a(dstE), .b(dstM), .eq(comparator_1_eq[2]));  // open: gt, lt
  assign or_1_out = demultiplexer_1_out0 | demultiplexer_2_out0;  // OR_Gate or_1, 32 bits wide
  and and_1 (and_1_out, reqE, decoder_1_out0);
  assign or_2_out = demultiplexer_1_out1 | demultiplexer_2_out1;  // OR_Gate or_2, 32 bits wide
  and and_2 (and_2_out, decoder_1_out1, reqE);
  assign or_3_out = demultiplexer_1_out2 | demultiplexer_2_out2;  // OR_Gate or_3, 32 bits wide
  and and_3 (and_3_out, decoder_1_out4, reqE);
  and and_4 (and_4_out, decoder_1_out5, reqE);
  and and_5 (and_5_out, decoder_1_out6, reqE);
  and and_6 (and_6_out, decoder_1_out7, reqE);
  and and_7 (and_7_out, reqM, decoder_2_out0);
  and and_8 (and_8_out, decoder_2_out1, reqM);
  and and_9 (and_9_out, decoder_1_out2, reqE);
  and and_10 (and_10_out, decoder_2_out2, reqM);
  assign or_4_out = demultiplexer_1_out3 | demultiplexer_2_out3;  // OR_Gate or_4, 32 bits wide
  and and_11 (and_11_out, decoder_1_out3, reqE);
  and and_12 (and_12_out, decoder_2_out3, reqM);
  assign or_5_out = demultiplexer_1_out4 | demultiplexer_2_out4;  // OR_Gate or_5, 32 bits wide
  and and_13 (and_13_out, decoder_2_out4, reqM);
  assign or_6_out = demultiplexer_1_out5 | demultiplexer_2_out5;  // OR_Gate or_6, 32 bits wide
  and and_14 (and_14_out, decoder_2_out5, reqM);
  assign or_7_out = demultiplexer_1_out6 | demultiplexer_2_out6;  // OR_Gate or_7, 32 bits wide
  and and_15 (and_15_out, decoder_2_out6, reqM);
  assign or_8_out = demultiplexer_1_out7 | demultiplexer_2_out7;  // OR_Gate or_8, 32 bits wide
  and and_16 (and_16_out, decoder_2_out7, reqM);
  or or_9 (EN, and_1_out, and_7_out);
  or or_10 (EN_2, and_2_out, and_8_out);
  or or_11 (EN_3, and_9_out, and_10_out);
  or or_12 (EN_4, and_11_out, and_12_out);
  or or_13 (EN_5, and_3_out, and_13_out);
  or or_14 (EN_6, and_4_out, and_14_out);
  or or_15 (EN_7, and_5_out, and_15_out);
  or or_16 (EN_8, and_6_out, and_16_out);
  Multiplexer #(.select(3), .width(32), .enable("false")) multiplexer_1 (
    .in0({32{1'b0}}), .in1(or_1_out), .in2(or_1_out), .in3(or_1_out), .in4({32{1'b0}}),
    .in5(demultiplexer_1_out0), .in6(demultiplexer_2_out0), .in7(demultiplexer_2_out0), .out(D0),
    .sel({comparator_1_eq[2], reqM, reqE}));
  Multiplexer #(.select(3), .width(32), .enable("false")) multiplexer_2 (
    .in0({32{1'b0}}), .in1(or_2_out), .in2(or_2_out), .in3(or_2_out), .in4({32{1'b0}}),
    .in5(demultiplexer_1_out1), .in6(demultiplexer_2_out1), .in7(demultiplexer_2_out1), .out(D1),
    .sel({comparator_1_eq[2], reqM, reqE}));
  Multiplexer #(.select(3), .width(32), .enable("false")) multiplexer_3 (
    .in0({32{1'b0}}), .in1(or_3_out), .in2(or_3_out), .in3(or_3_out), .in4({32{1'b0}}),
    .in5(demultiplexer_1_out2), .in6(demultiplexer_2_out2), .in7(demultiplexer_2_out2), .out(D2),
    .sel({comparator_1_eq[2], reqM, reqE}));
  Multiplexer #(.select(3), .width(32), .enable("false")) multiplexer_4 (
    .in0({32{1'b0}}), .in1(or_4_out), .in2(or_4_out), .in3(or_4_out), .in4({32{1'b0}}),
    .in5(demultiplexer_1_out3), .in6(demultiplexer_2_out3), .in7(demultiplexer_2_out3), .out(D3),
    .sel({comparator_1_eq[2], reqM, reqE}));
  Multiplexer #(.select(3), .width(32), .enable("false")) multiplexer_5 (
    .in0({32{1'b0}}), .in1(or_5_out), .in2(or_5_out), .in3(or_5_out), .in4({32{1'b0}}),
    .in5(demultiplexer_1_out4), .in6(demultiplexer_2_out4), .in7(demultiplexer_2_out4), .out(D4),
    .sel({comparator_1_eq[2], reqM, reqE}));
  Multiplexer #(.select(3), .width(32), .enable("false")) multiplexer_6 (
    .in0({32{1'b0}}), .in1(or_6_out), .in2(or_6_out), .in3(or_6_out), .in4({32{1'b0}}),
    .in5(demultiplexer_1_out5), .in6(demultiplexer_2_out5), .in7(demultiplexer_2_out5), .out(D5),
    .sel({comparator_1_eq[2], reqM, reqE}));
  Multiplexer #(.select(3), .width(32), .enable("false")) multiplexer_7 (
    .in0({32{1'b0}}), .in1(or_7_out), .in2(or_7_out), .in3(or_7_out), .in4({32{1'b0}}),
    .in5(demultiplexer_1_out6), .in6(demultiplexer_2_out6), .in7(demultiplexer_2_out6), .out(D6),
    .sel({comparator_1_eq[2], reqM, reqE}));
  Multiplexer #(.select(3), .width(32), .enable("false")) multiplexer_8 (
    .in0({32{1'b0}}), .in1(or_8_out), .in2(or_8_out), .in3(or_8_out), .in4({32{1'b0}}),
    .in5(demultiplexer_1_out7), .in6(demultiplexer_2_out7), .in7(demultiplexer_2_out7), .out(D7),
    .sel({comparator_1_eq[2], reqM, reqE}));

  assign CLK = clock;
  assign CLK_2 = clock;
  assign CLK_3 = clock;
  assign CLK_4 = clock;
  assign CLK_5 = clock;
  assign CLK_6 = clock;
  assign CLK_7 = clock;
  assign CLK_8 = clock;

  // Notes on the sheet:
  //   dstE Decoder
  //   dstM Decoder
  //   We OR together valE and valM
  //   unless dst values are equal
  //   I used an equality comparator
  //   we made one in class, so it's kosher
  //   Sends valE to the right place
  //   Sends ValM to the right place
  //   The Bit Selectors for our de-multiplexer
  //   Output is 0s or an input based on the DEMUX's Select bits
  //   Select bits decided by reqE and reqM inputs
  //   Enable if D0 is Selected by dstE or dstM
  //   AND the corresponding reqE/reqM input is on
  //   If reqE and reqM are enabled AND dstE = dstM
  //   then D0 = dstM
endmodule

module regreader (
  input  [2:0] srcA,
  input  [2:0] srcB,
  input  [31:0] Q,
  input  [31:0] Q_2,
  input  [31:0] Q_3,
  input  reset,
  input  [31:0] Q_4,
  input  [31:0] Q_5,
  input  [31:0] Q_6,
  input  [31:0] Q_7,
  input  [31:0] Q_8,
  output CLR,
  output [31:0] valA,
  output [31:0] valB,
  output CLR_2,
  output CLR_3,
  output CLR_4,
  output CLR_5,
  output CLR_6,
  output CLR_7,
  output CLR_8
);

  Multiplexer #(.select(3), .width(32), .enable("false")) multiplexer_1 (
    .in0(Q), .in1(Q_2), .in2(Q_3), .in3(Q_4), .in4(Q_5), .in5(Q_6), .in6(Q_7), .in7(Q_8), .out(valA),
    .sel(srcA));
  Multiplexer #(.select(3), .width(32), .enable("false")) multiplexer_2 (
    .in0(Q), .in1(Q_2), .in2(Q_3), .in3(Q_4), .in4(Q_5), .in5(Q_6), .in6(Q_7), .in7(Q_8), .out(valB),
    .sel(srcB));

  assign CLR = reset;
  assign CLR_2 = reset;
  assign CLR_3 = reset;
  assign CLR_4 = reset;
  assign CLR_5 = reset;
  assign CLR_6 = reset;
  assign CLR_7 = reset;
  assign CLR_8 = reset;

  // Notes on the sheet:
  //   Multiplexers to choose the right value
  //   for reg 0
  //   for reg 7
endmodule
