// Logisim project carter_bastian_hw4_q1.circ as structural Verilog: 8 circuits, main circuit ALU
module TESTING_ALU (
  input  [31:0] in_1,
  input  [31:0] in_2,
  input  [3:0] in_3,
  output [2:0] out_4,
  output [31:0] out_5,
  output [31:0] out_6,
  output [31:0] out_7,
  output [31:0] out_8,
  output [31:0] out_9
);

  ALU alu_1 (.in_1(in_1), .in_2(in_2), .aluOP(in_3), .out_5(out_5), .out_4(out_4));
  Adder #(.width(32)) adder_1 (.a(in_1), .b(in_2), .out(out_6));  // open: cin, cout
  Subtractor #(.width(32)) subtractor_1 (.a(in_1), .b(in_2), .out(out_7));  // open: bin, bout
  assign out_8 = in_1 & in_2;  // AND_Gate and_1, 32 bits wide
  assign out_9 = in_1 ^ in_2;  // XOR_Gate xor_1, 32 bits wide

  // Notes on the sheet:
  //   Inputs
  //   My Results
  //   LogiSim Addition Output
  //   Logisim Subtraction Output
  //   Logisim AND Output
  //   Logisim XOR Output
endmodule

module ALU (
  input  [31:0] in_1,
  input  [31:0] in_2,
  input  [3:0] aluOP,
  output [2:0] out_4,
  output [31:0] out_5
);

  wire and_2_out, and_3_out, and_4_out, and_5_out, and_6_out, and_7_out, and_8_out, and_9_out, cmp_2_out_3,
       cmp_2_out_4, cmp_2_out_5, cmp_3_out_3, cmp_3_out_5, decoder_1_out0, decoder_1_out1, or_2_out,
       or_3_out, or_5_out;
  wire [30:0] demultiplexer_1_out1;
  wire [31:0] adder_1_out, and_1_out, demultiplexer_1_out0, demultiplexer_1_out2, demultiplexer_1_out3,
       demultiplexer_2_out0, demultiplexer_2_out1, demultiplexer_2_out2, demultiplexer_2_out3,
       subtractor_1_out_3, xor_1_out;
  wire [31:31] demultiplexer_1_out1_2;

  Demultiplexer #(.select(4), .width(32)) demultiplexer_1 (
    .out0(demultiplexer_1_out0), .out1({demultiplexer_1_out1_2[31], demultiplexer_1_out1}),
    .out2(demultiplexer_1_out2), .out3(demultiplexer_1_out3), .in(in_1), .sel(aluOP));  // open: out4, out5, out6, out7, out8, out9, out10, out11, out12, out13, out14, out15, en
  Demultiplexer #(.select(4), .width(32)) demultiplexer_2 (
    .out0(demultiplexer_2_out0), .out1(demultiplexer_2_out1), .out2(demultiplexer_2_out2),
    .out3(demultiplexer_2_out3), .in(in_2), .sel(aluOP));  // open: out4, out5, out6, out7, out8, out9, out10, out11, out12, out13, out14, out15, en
  Decoder #(.select(4)) decoder_1 (
    .out0(decoder_1_out0), .out1(decoder_1_out1), .sel(aluOP));  // open: out2, out3, out4, out5, out6, out7, out8, out9, out10, out11, out12, out13, out14, out15, en
  Adder #(.width(32)) adder_1 (
    .a(demultiplexer_1_out0), .b(demultiplexer_2_out0), .out(adder_1_out));  // open: cin, cout
  subtractor subtractor_1 (
    .in_1({demultiplexer_1_out1_2[31], demultiplexer_1_out1}), .in_2(demultiplexer_2_out1),
    .out_3(subtractor_1_out_3));
  assign and_1_out = demultiplexer_1_out2 & demultiplexer_2_out2;  // AND_Gate and_1, 32 bits wide
  assign xor_1_out = demultiplexer_1_out3 ^ demultiplexer_2_out3;  // XOR_Gate xor_1, 32 bits wide
  assign {out_4[1], out_5[30:0]} = adder_1_out | subtractor_1_out_3 | and_1_out | xor_1_out;  // OR_Gate or_1, 32 bits wide
  and and_2 (and_2_out, demultiplexer_1_out0[31], decoder_1_out0, demultiplexer_2_out0[31]);
  and and_3 (and_3_out, ~demultiplexer_1_out0[31], decoder_1_out0, ~demultiplexer_2_out0[31]);  // AND_Gate
  cmp cmp_1 (.in_1({out_4[1], out_5[30:0]}), .in_2({32{1'b0}}), .out_4(out_4[2]));  // open: out_3, out_5
  and and_4 (and_4_out, or_2_out, and_2_out);
  and and_5 (and_5_out, cmp_2_out_5, and_3_out);
  cmp cmp_2 (
    .in_1({out_4[1], out_5[30:0]}), .in_2({32{1'b0}}), .out_3(cmp_2_out_3), .out_4(cmp_2_out_4),
    .out_5(cmp_2_out_5));
  or or_2 (or_2_out, cmp_2_out_4, cmp_2_out_3);
  or or_3 (or_3_out, and_4_out, and_5_out);
  or or_4 (out_4[0], or_3_out, or_5_out);
  and and_6 (and_6_out, demultiplexer_1_out1_2[31], decoder_1_out1, ~demultiplexer_2_out1[31]);  // AND_Gate
  and and_7 (and_7_out, ~demultiplexer_1_out1_2[31], decoder_1_out1, demultiplexer_2_out1[31]);  // AND_Gate
  and and_8 (and_8_out, cmp_3_out_3, and_6_out);
  and and_9 (and_9_out, and_7_out, cmp_3_out_5);
  or or_5 (or_5_out, and_8_out, and_9_out);
  cmp cmp_3 (
    .in_1({out_4[1], out_5[30:0]}), .in_2({32{1'b0}}), .out_3(cmp_3_out_3), .out_5(cmp_3_out_5));  // open: out_4

  assign out_5[31] = out_4[1];

  // Notes on the sheet:
  //   aluA
  //   aluB
  //   Multi-bit Adding Operation
  //   Custom Subtraction Operation
  //   Multi-Bit And
  //   Multi-Bit XOR
  //   OR-ing valE with 3 32-bit wires
  //   valued at all 0's => valE
  //   Test for Addition Overflow
  //   Z = Zero Value
  //   Overflow if both vals neg. and valE >= 0
  //   OR if both vals pos. and valE < 0
  //   AND make sure we're doing addition
  //   S = Sign Flag
  //   CC = Condition Code
  //   Overflow if:
  //   POS - NEG => NEG
  //   O = Overflow Flag
  //   Test for Subtraction Overflow
  //   OR NEG - POS => POS
  //   valE = aluA OP aluB
endmodule

module cmp (
  input  [31:0] in_1,
  input  [31:0] in_2,
  output out_3,
  output out_4,
  output out_5
);

  wire and_1_out, and_2_out, and_3_out, and_4_out, and_6_out, and_7_out, diff_case_cmp_1_less_than,
       diff_case_cmp_1_out_3, same_case_cmp_1_out_3, same_case_cmp_1_out_4, same_case_cmp_1_out_5, xnor_1_out;

  xnor xnor_1 (xnor_1_out, in_1[31], in_2[31]);
  and and_1 (and_1_out, 1'b1, ~xnor_1_out);  // AND_Gate
  and and_2 (and_2_out, 1'b1, xnor_1_out);
  diff_case_cmp diff_case_cmp_1 (
    .in_1(in_1), .in_2(in_2), .out_3(diff_case_cmp_1_out_3), .Less_Than(diff_case_cmp_1_less_than));
  same_case_cmp same_case_cmp_1 (
    .in_1(in_1), .in_2(in_2), .out_3(same_case_cmp_1_out_3), .out_4(same_case_cmp_1_out_4),
    .out_5(same_case_cmp_1_out_5));
  and and_3 (and_3_out, diff_case_cmp_1_out_3, and_1_out);
  and and_4 (and_4_out, same_case_cmp_1_out_3, and_2_out);
  and and_5 (out_4, and_2_out, same_case_cmp_1_out_4);
  and and_6 (and_6_out, diff_case_cmp_1_less_than, and_1_out);
  and and_7 (and_7_out, same_case_cmp_1_out_5, and_2_out);
  or or_1 (out_3, and_3_out, and_4_out);
  or or_2 (out_5, and_6_out, and_7_out);

  // Notes on the sheet:
  //   valA
  //   valB
  //   ValA
  //   ValB
  //   Different Case?
  //   Same Case?
  //   Diff case cmp
  //   same case cmp
  //   Different Case & Greater Than
  //   OR Same Case & Greater Than
  //   Same Case & Equal
  //   Different Case & Less Than
  //   OR Same Case & Less Than
endmodule

module same_case_cmp (
  input  [31:0] in_1,
  input  [31:0] in_2,
  output out_3,
  output out_4,
  output out_5
);

  wire and_1_out, and_2_out, and_3_out, byte_cmp_1_out_5, byte_cmp_1_out_6, byte_cmp_2_out_5,
       byte_cmp_2_out_6, byte_cmp_3_out_5, byte_cmp_3_out_6, not_1_out, not_2_out, not_3_out;

  byte_cmp byte_cmp_1 (
    .in_1(in_1[31:24]), .in_2(in_2[31:24]), .out_5(byte_cmp_1_out_5), .out_6(byte_cmp_1_out_6), .in_3(1'b0),
    .in_4(1'b0));  // open: out_7
  not not_1 (not_1_out, byte_cmp_1_out_6);
  byte_cmp byte_cmp_2 (
    .in_1(in_1[23:16]), .in_2(in_2[23:16]), .out_5(byte_cmp_2_out_5), .out_6(byte_cmp_2_out_6),
    .in_3(not_1_out), .in_4(and_1_out));  // open: out_7
  not not_2 (not_2_out, byte_cmp_2_out_6);
  and and_1 (and_1_out, not_1_out, byte_cmp_1_out_5);
  byte_cmp byte_cmp_3 (
    .in_1(in_1[15:8]), .in_2(in_2[15:8]), .out_5(byte_cmp_3_out_5), .out_6(byte_cmp_3_out_6),
    .in_3(not_2_out), .in_4(and_2_out));  // open: out_7
  and and_2 (and_2_out, not_2_out, byte_cmp_2_out_5);
  not not_3 (not_3_out, byte_cmp_3_out_6);
  and and_3 (and_3_out, not_3_out, byte_cmp_3_out_5);
  byte_cmp byte_cmp_4 (
    .in_1(in_1[7:0]), .in_2(in_2[7:0]), .out_5(out_3), .out_6(out_4), .out_7(out_5), .in_3(not_3_out),
    .in_4(and_3_out));

  // Notes on the sheet:
  //   A
  //   B
endmodule

module diff_case_cmp (
  input  [31:0] in_1,
  input  [31:0] in_2,
  output out_3,
  output Less_Than
);

  bit_cmp bit_cmp_1 (
    .A(in_1[31]), .B(in_2[31]), .A___B(Less_Than), .A___B_3(out_3), .Force_Output(1'b0), .in_4(1'b0));  // open: A___B_2

  // Notes on the sheet:
  //   A
  //   B
  //   Greater Than
endmodule

module byte_cmp (
  input  [7:0] in_1,
  input  [7:0] in_2,
  input  in_3,
  input  in_4,
  output out_5,
  output out_6,
  output out_7
);

  wire and_1_out, and_2_out, and_3_out, and_4_out, and_5_out, and_6_out, and_7_out, bit_cmp_1_a___b,
       bit_cmp_1_a___b_2, bit_cmp_2_a___b, bit_cmp_2_a___b_2, bit_cmp_3_a___b, bit_cmp_3_a___b_2,
       bit_cmp_4_a___b, bit_cmp_4_a___b_2, bit_cmp_5_a___b, bit_cmp_5_a___b_2, bit_cmp_6_a___b,
       bit_cmp_6_a___b_2, bit_cmp_7_a___b, bit_cmp_7_a___b_2, not_1_out, not_2_out, not_3_out, not_4_out,
       not_5_out, not_6_out, not_7_out;

  bit_cmp bit_cmp_1 (
    .A(in_1[7]), .B(in_2[7]), .A___B(bit_cmp_1_a___b), .A___B_2(bit_cmp_1_a___b_2), .Force_Output(in_3),
    .in_4(in_4));  // open: A___B_3
  not not_1 (not_1_out, bit_cmp_1_a___b_2);
  and and_1 (and_1_out, not_1_out, bit_cmp_1_a___b);
  bit_cmp bit_cmp_2 (
    .A(in_1[6]), .B(in_2[6]), .A___B(bit_cmp_2_a___b), .A___B_2(bit_cmp_2_a___b_2), .Force_Output(not_1_out),
    .in_4(and_1_out));  // open: A___B_3
  not not_2 (not_2_out, bit_cmp_2_a___b_2);
  bit_cmp bit_cmp_3 (
    .A(in_1[5]), .B(in_2[5]), .A___B(bit_cmp_3_a___b), .A___B_2(bit_cmp_3_a___b_2), .Force_Output(not_2_out),
    .in_4(and_2_out));  // open: A___B_3
  and and_2 (and_2_out, not_2_out, bit_cmp_2_a___b);
  not not_3 (not_3_out, bit_cmp_3_a___b_2);
  bit_cmp bit_cmp_4 (
    .A(in_1[4]), .B(in_2[4]), .A___B(bit_cmp_4_a___b), .A___B_2(bit_cmp_4_a___b_2), .Force_Output(not_3_out),
    .in_4(and_3_out));  // open: A___B_3
  not not_4 (not_4_out, bit_cmp_4_a___b_2);
  and and_3 (and_3_out, not_3_out, bit_cmp_3_a___b);
  and and_4 (and_4_out, not_4_out, bit_cmp_4_a___b);
  bit_cmp bit_cmp_5 (
    .A(in_1[3]), .B(in_2[3]), .A___B(bit_cmp_5_a___b), .A___B_2(bit_cmp_5_a___b_2), .Force_Output(not_4_out),
    .in_4(and_4_out));  // open: A___B_3
  not not_5 (not_5_out, bit_cmp_5_a___b_2);
  bit_cmp bit_cmp_6 (
    .A(in_1[2]), .B(in_2[2]), .A___B(bit_cmp_6_a___b), .A___B_2(bit_cmp_6_a___b_2), .Force_Output(not_5_out),
    .in_4(and_5_out));  // open: A___B_3
  and and_5 (and_5_out, not_5_out, bit_cmp_5_a___b);
  not not_6 (not_6_out, bit_cmp_6_a___b_2);
  and and_6 (and_6_out, not_6_out, bit_cmp_6_a___b);
  bit_cmp bit_cmp_7 (
    .A(in_1[1]), .B(in_2[1]), .A___B(bit_cmp_7_a___b), .A___B_2(bit_cmp_7_a___b_2), .Force_Output(not_6_out),
    .in_4(and_6_out));  // open: A___B_3
  not not_7 (not_7_out, bit_cmp_7_a___b_2);
  bit_cmp bit_cmp_8 (
    .A(in_1[0]), .B(in_2[0]), .A___B(out_5), .A___B_2(out_6), .A___B_3(out_7), .Force_Output(not_7_out),
    .in_4(and_7_out));
  and and_7 (and_7_out, not_7_out, bit_cmp_7_a___b);

  // Notes on the sheet:
  //   Force Output?
  //   Force Greather-Than?
endmodule

module bit_cmp (
  input  A,
  input  B,
  input  Force_Output,
  input  in_4,
  output A___B,
  output A___B_2,
  output A___B_3
);

  wire and_1_out, and_2_out, and_5_out, or_1_out, xnor_1_out;

  and and_1 (and_1_out, A, ~B);  // AND_Gate
  xnor xnor_1 (xnor_1_out, A, B);
  or or_1 (or_1_out, and_1_out, and_2_out);
  and and_2 (and_2_out, Force_Output, in_4);
  and and_3 (A___B_2, xnor_1_out, ~Force_Output);  // AND_Gate
  and and_4 (A___B, or_1_out, ~and_5_out);  // AND_Gate
  and and_5 (and_5_out, Force_Output, ~in_4);  // AND_Gate
  and and_6 (A___B_3, ~A___B, ~A___B_2);  // AND_Gate

  // Notes on the sheet:
  //   Force Greater-Than
endmodule

module subtractor (
  input  [31:0] in_1,
  input  [31:0] in_2,
  output [31:0] out_3
);

  wire [31:0] adder_1_out, not_1_out;

  assign not_1_out = ~in_2;  // NOT_Gate not_1, 32 bits wide
  Adder #(.width(32)) adder_1 (.a(in_1), .b(not_1_out), .out(adder_1_out));  // open: cin, cout
  Adder #(.width(32)) adder_2 (.a(adder_1_out), .b(32'h1), .out(out_3));  // open: cin, cout
endmodule
