// Logisim project carter_bastian_hw4_q2-3.circ as structural Verilog: 7 circuits, main circuit q2
module q2 (
  input  in_1,
  input  [31:0] in_2,
  input  in_3,
  input  in_4,
  input  in_5,
  input  [7:0] in_6,
  output [7:0] byte_0,
  output [7:0] byte_1,
  output [7:0] byte_2,
  output [7:0] byte_3,
  output [7:0] byte_4,
  output [7:0] byte_5,
  output ready,
  output [31:0] out_14,
  output out_15,
  output RAMread
);

  wire and_1_out, and_2_out, and_3_out, and_4_out, and_5_out, and_6_out, and_7_out, decoder_1_out0,
       decoder_1_out1, decoder_1_out2, decoder_1_out3, decoder_1_out4, decoder_1_out5, decoder_1_out6,
       decoder_1_out7, decoder_1_out8, decoder_1_out9, decoder_1_out10, decoder_1_out11, decoder_1_out12,
       decoder_1_out13, decoder_1_out14, decoder_1_out15, decoder_2_out0, decoder_2_out1, decoder_2_out2,
       decoder_2_out3, decoder_2_out4, decoder_2_out5, not_1_out, not_2_out, not_3_out, not_4_out, not_5_out,
       not_6_out, not_7_out, not_8_out, not_9_out, not_10_out, not_11_out, not_12_out, not_13_out,
       not_14_out, not_15_out, not_16_out, not_19_out, or_1_out, pull_resistor_8_node, pull_resistor_9_node,
       tiny_diode_23__0_z_out;
  wire [2:0] pull_resistor_3_node, pull_resistor_6_node;
  wire [3:0] pull_resistor_12_node, register_1_q;
  wire [7:0] demultiplexer_1_out0, demultiplexer_1_out1, demultiplexer_1_out2, demultiplexer_1_out3,
       demultiplexer_1_out4, demultiplexer_1_out5;

  and and_1 (and_1_out, in_1, in_4);
  or or_1 (or_1_out, ~decoder_1_out0, and_1_out);  // OR_Gate
  Decoder #(.select(4)) decoder_1 (
    .out0(decoder_1_out0), .out1(decoder_1_out1), .out2(decoder_1_out2), .out3(decoder_1_out3),
    .out4(decoder_1_out4), .out5(decoder_1_out5), .out6(decoder_1_out6), .out7(decoder_1_out7),
    .out8(decoder_1_out8), .out9(decoder_1_out9), .out10(decoder_1_out10), .out11(decoder_1_out11),
    .out12(decoder_1_out12), .out13(decoder_1_out13), .out14(decoder_1_out14), .out15(decoder_1_out15),
    .sel(register_1_q));  // open: en
  Register #(.width(4)) register_1 (.D(pull_resistor_12_node), .en(or_1_out), .Q(register_1_q), .clk(in_5), .clr(in_3));
  Address_Incrementer address_incrementer_1 (.in_1(in_2), .out_3(out_14), .in_2(pull_resistor_3_node));
  Pull_Resistor #(.pull(1)) pull_resistor_1 (.node(pull_resistor_3_node[2]));
  not not_1 (not_1_out, decoder_1_out0);
  Tiny_Diode tiny_diode_1 (._0_1_in(not_2_out), ._0_Z_out(pull_resistor_3_node[2]));
  not not_2 (not_2_out, decoder_1_out1);
  not not_3 (not_3_out, decoder_1_out2);
  Tiny_Diode tiny_diode_2 (._0_1_in(not_4_out), ._0_Z_out(pull_resistor_3_node[2]));
  not not_4 (not_4_out, decoder_1_out3);
  not not_5 (not_5_out, decoder_1_out4);
  Tiny_Diode tiny_diode_3 (._0_1_in(not_6_out), ._0_Z_out(pull_resistor_3_node[2]));
  not not_6 (not_6_out, decoder_1_out5);
  not not_7 (not_7_out, decoder_1_out6);
  Tiny_Diode tiny_diode_4 (._0_1_in(not_8_out), ._0_Z_out(pull_resistor_3_node[2]));
  not not_8 (not_8_out, decoder_1_out7);
  not not_9 (not_9_out, decoder_1_out8);
  not not_10 (not_10_out, decoder_1_out9);
  not not_11 (not_11_out, decoder_1_out10);
  not not_12 (not_12_out, decoder_1_out11);
  not not_13 (not_13_out, decoder_1_out12);
  not not_14 (not_14_out, decoder_1_out13);
  not not_15 (not_15_out, decoder_1_out14);
  not not_16 (not_16_out, decoder_1_out15);
  Pull_Resistor #(.pull(1)) pull_resistor_2 (.node(pull_resistor_3_node[1]));
  Pull_Resistor #(.pull(1)) pull_resistor_3 (.node(pull_resistor_3_node[0]));
  Tiny_Diode tiny_diode_5 (._0_1_in(not_2_out), ._0_Z_out(pull_resistor_3_node[0]));
  Tiny_Diode tiny_diode_6 (._0_1_in(not_2_out), ._0_Z_out(pull_resistor_3_node[1]));
  Tiny_Diode tiny_diode_7 (._0_1_in(not_4_out), ._0_Z_out(pull_resistor_3_node[1]));
  Tiny_Diode tiny_diode_8 (._0_1_in(not_6_out), ._0_Z_out(pull_resistor_3_node[0]));
  Tiny_Diode tiny_diode_9 (._0_1_in(not_10_out), ._0_Z_out(pull_resistor_3_node[1]));
  Tiny_Diode tiny_diode_10 (._0_1_in(not_10_out), ._0_Z_out(pull_resistor_3_node[0]));
  Tiny_Diode tiny_diode_11 (._0_1_in(not_12_out), ._0_Z_out(pull_resistor_3_node[1]));
  Pull_Resistor #(.pull(1)) pull_resistor_4 (.node(pull_resistor_6_node[2]));
  Tiny_Diode tiny_diode_12 (._0_1_in(not_3_out), ._0_Z_out(pull_resistor_6_node[2]));
  Tiny_Diode tiny_diode_13 (._0_1_in(not_5_out), ._0_Z_out(pull_resistor_6_node[2]));
  Tiny_Diode tiny_diode_14 (._0_1_in(not_7_out), ._0_Z_out(pull_resistor_6_node[2]));
  Tiny_Diode tiny_diode_15 (._0_1_in(not_9_out), ._0_Z_out(pull_resistor_6_node[2]));
  Pull_Resistor #(.pull(1)) pull_resistor_5 (.node(pull_resistor_6_node[1]));
  Pull_Resistor #(.pull(1)) pull_resistor_6 (.node(pull_resistor_6_node[0]));
  Tiny_Diode tiny_diode_16 (._0_1_in(not_3_out), ._0_Z_out(pull_resistor_6_node[1]));
  Tiny_Diode tiny_diode_17 (._0_1_in(not_3_out), ._0_Z_out(pull_resistor_6_node[0]));
  Tiny_Diode tiny_diode_18 (._0_1_in(not_5_out), ._0_Z_out(pull_resistor_6_node[1]));
  Tiny_Diode tiny_diode_19 (._0_1_in(not_7_out), ._0_Z_out(pull_resistor_6_node[0]));
  Tiny_Diode tiny_diode_20 (._0_1_in(not_11_out), ._0_Z_out(pull_resistor_6_node[0]));
  Tiny_Diode tiny_diode_21 (._0_1_in(not_11_out), ._0_Z_out(pull_resistor_6_node[1]));
  Tiny_Diode tiny_diode_22 (._0_1_in(not_13_out), ._0_Z_out(pull_resistor_6_node[1]));
  Tiny_Diode tiny_diode_23 (._0_1_in(not_2_out), ._0_Z_out(tiny_diode_23__0_z_out));
  Tiny_Diode tiny_diode_24 (._0_1_in(not_3_out), ._0_Z_out(tiny_diode_23__0_z_out));
  Tiny_Diode tiny_diode_25 (._0_1_in(not_4_out), ._0_Z_out(tiny_diode_23__0_z_out));
  Tiny_Diode tiny_diode_26 (._0_1_in(not_5_out), ._0_Z_out(tiny_diode_23__0_z_out));
  Tiny_Diode tiny_diode_27 (._0_1_in(not_6_out), ._0_Z_out(tiny_diode_23__0_z_out));
  Tiny_Diode tiny_diode_28 (._0_1_in(not_7_out), ._0_Z_out(tiny_diode_23__0_z_out));
  Tiny_Diode tiny_diode_29 (._0_1_in(not_8_out), ._0_Z_out(tiny_diode_23__0_z_out));
  Tiny_Diode tiny_diode_30 (._0_1_in(not_9_out), ._0_Z_out(tiny_diode_23__0_z_out));
  Tiny_Diode tiny_diode_31 (._0_1_in(not_10_out), ._0_Z_out(tiny_diode_23__0_z_out));
  Tiny_Diode tiny_diode_32 (._0_1_in(not_11_out), ._0_Z_out(tiny_diode_23__0_z_out));
  Tiny_Diode tiny_diode_33 (._0_1_in(not_12_out), ._0_Z_out(tiny_diode_23__0_z_out));
  Tiny_Diode tiny_diode_34 (._0_1_in(not_13_out), ._0_Z_out(tiny_diode_23__0_z_out));
  not not_17 (out_15, tiny_diode_23__0_z_out);
  Pull_Resistor #(.pull(1)) pull_resistor_7 (.node(tiny_diode_23__0_z_out));
  Pull_Resistor #(.pull(1)) pull_resistor_8 (.node(pull_resistor_8_node));
  Tiny_Diode tiny_diode_35 (._0_1_in(not_3_out), ._0_Z_out(pull_resistor_8_node));
  Tiny_Diode tiny_diode_36 (._0_1_in(not_5_out), ._0_Z_out(pull_resistor_8_node));
  Tiny_Diode tiny_diode_37 (._0_1_in(not_7_out), ._0_Z_out(pull_resistor_8_node));
  Tiny_Diode tiny_diode_38 (._0_1_in(not_9_out), ._0_Z_out(pull_resistor_8_node));
  Tiny_Diode tiny_diode_39 (._0_1_in(not_11_out), ._0_Z_out(pull_resistor_8_node));
  Tiny_Diode tiny_diode_40 (._0_1_in(not_13_out), ._0_Z_out(pull_resistor_8_node));
  not not_18 (RAMread, pull_resistor_8_node);
  Pull_Resistor #(.pull(1)) pull_resistor_9 (.node(pull_resistor_9_node));
  Tiny_Diode tiny_diode_41 (._0_1_in(not_1_out), ._0_Z_out(pull_resistor_9_node));
  Tiny_Diode tiny_diode_42 (._0_1_in(not_1_out), ._0_Z_out(pull_resistor_12_node[3]));
  Tiny_Diode tiny_diode_43 (._0_1_in(not_2_out), ._0_Z_out(pull_resistor_12_node[3]));
  Tiny_Diode tiny_diode_44 (._0_1_in(not_3_out), ._0_Z_out(pull_resistor_12_node[3]));
  Tiny_Diode tiny_diode_45 (._0_1_in(not_4_out), ._0_Z_out(pull_resistor_12_node[3]));
  Tiny_Diode tiny_diode_46 (._0_1_in(not_5_out), ._0_Z_out(pull_resistor_12_node[3]));
  Tiny_Diode tiny_diode_47 (._0_1_in(not_6_out), ._0_Z_out(pull_resistor_12_node[3]));
  Tiny_Diode tiny_diode_48 (._0_1_in(not_7_out), ._0_Z_out(pull_resistor_12_node[3]));
  Tiny_Diode tiny_diode_49 (._0_1_in(not_14_out), ._0_Z_out(pull_resistor_9_node));
  Tiny_Diode tiny_diode_50 (._0_1_in(not_15_out), ._0_Z_out(pull_resistor_9_node));
  Tiny_Diode tiny_diode_51 (._0_1_in(not_16_out), ._0_Z_out(pull_resistor_12_node[3]));
  Tiny_Diode tiny_diode_52 (._0_1_in(not_16_out), ._0_Z_out(pull_resistor_9_node));
  Pull_Resistor #(.pull(1)) pull_resistor_10 (.node(pull_resistor_12_node[3]));
  Pull_Resistor #(.pull(1)) pull_resistor_11 (.node(pull_resistor_12_node[2]));
  Tiny_Diode tiny_diode_53 (._0_1_in(not_1_out), ._0_Z_out(pull_resistor_12_node[1]));
  Tiny_Diode tiny_diode_54 (._0_1_in(not_1_out), ._0_Z_out(pull_resistor_12_node[2]));
  Tiny_Diode tiny_diode_55 (._0_1_in(not_2_out), ._0_Z_out(pull_resistor_12_node[2]));
  Tiny_Diode tiny_diode_56 (._0_1_in(not_3_out), ._0_Z_out(pull_resistor_12_node[2]));
  Tiny_Diode tiny_diode_57 (._0_1_in(not_4_out), ._0_Z_out(pull_resistor_12_node[1]));
  Tiny_Diode tiny_diode_58 (._0_1_in(not_5_out), ._0_Z_out(pull_resistor_12_node[1]));
  Tiny_Diode tiny_diode_59 (._0_1_in(not_8_out), ._0_Z_out(pull_resistor_12_node[2]));
  Tiny_Diode tiny_diode_60 (._0_1_in(not_8_out), ._0_Z_out(pull_resistor_12_node[1]));
  Tiny_Diode tiny_diode_61 (._0_1_in(not_9_out), ._0_Z_out(pull_resistor_12_node[2]));
  Tiny_Diode tiny_diode_62 (._0_1_in(not_9_out), ._0_Z_out(pull_resistor_12_node[1]));
  Tiny_Diode tiny_diode_63 (._0_1_in(not_10_out), ._0_Z_out(pull_resistor_12_node[2]));
  Tiny_Diode tiny_diode_64 (._0_1_in(not_11_out), ._0_Z_out(pull_resistor_12_node[2]));
  Tiny_Diode tiny_diode_65 (._0_1_in(not_12_out), ._0_Z_out(pull_resistor_12_node[1]));
  Tiny_Diode tiny_diode_66 (._0_1_in(not_13_out), ._0_Z_out(pull_resistor_12_node[1]));
  Tiny_Diode tiny_diode_67 (._0_1_in(not_16_out), ._0_Z_out(pull_resistor_12_node[1]));
  Tiny_Diode tiny_diode_68 (._0_1_in(not_16_out), ._0_Z_out(pull_resistor_12_node[2]));
  Pull_Resistor #(.pull(1)) pull_resistor_12 (.node(pull_resistor_12_node[0]));
  Pull_Resistor #(.pull(1)) pull_resistor_13 (.node(pull_resistor_12_node[1]));
  Tiny_Diode tiny_diode_69 (._0_1_in(not_2_out), ._0_Z_out(pull_resistor_12_node[0]));
  Tiny_Diode tiny_diode_70 (._0_1_in(not_4_out), ._0_Z_out(pull_resistor_12_node[0]));
  Tiny_Diode tiny_diode_71 (._0_1_in(not_6_out), ._0_Z_out(pull_resistor_12_node[0]));
  Tiny_Diode tiny_diode_72 (._0_1_in(not_8_out), ._0_Z_out(pull_resistor_12_node[0]));
  Tiny_Diode tiny_diode_73 (._0_1_in(not_10_out), ._0_Z_out(pull_resistor_12_node[0]));
  Tiny_Diode tiny_diode_74 (._0_1_in(not_12_out), ._0_Z_out(pull_resistor_12_node[0]));
  Tiny_Diode tiny_diode_75 (._0_1_in(not_14_out), ._0_Z_out(pull_resistor_12_node[0]));
  Tiny_Diode tiny_diode_76 (._0_1_in(not_16_out), ._0_Z_out(pull_resistor_12_node[0]));
  not not_19 (not_19_out, pull_resistor_8_node);
  Decoder #(.select(3)) decoder_2 (
    .out0(decoder_2_out0), .out1(decoder_2_out1), .out2(decoder_2_out2), .out3(decoder_2_out3),
    .out4(decoder_2_out4), .out5(decoder_2_out5), .sel(pull_resistor_6_node));  // open: out6, out7, en
  Demultiplexer #(.select(3), .width(8)) demultiplexer_1 (
    .out0(demultiplexer_1_out0), .out1(demultiplexer_1_out1), .out2(demultiplexer_1_out2),
    .out3(demultiplexer_1_out3), .out4(demultiplexer_1_out4), .out5(demultiplexer_1_out5), .in(in_6),
    .sel(pull_resistor_6_node));  // open: out6, out7, en
  and and_2 (and_2_out, decoder_2_out0, not_19_out);
  and and_3 (and_3_out, decoder_2_out1, not_19_out);
  and and_4 (and_4_out, decoder_2_out2, not_19_out);
  and and_5 (and_5_out, decoder_2_out3, not_19_out);
  and and_6 (and_6_out, decoder_2_out4, not_19_out);
  and and_7 (and_7_out, decoder_2_out5, not_19_out);
  Register register_2 (.D(demultiplexer_1_out0), .en(and_2_out), .Q(byte_0), .clk(in_5), .clr(in_3));
  Register register_3 (.D(demultiplexer_1_out1), .en(and_3_out), .Q(byte_1), .clk(in_5), .clr(in_3));
  Register register_4 (.D(demultiplexer_1_out2), .en(and_4_out), .Q(byte_2), .clk(in_5), .clr(in_3));
  Register register_5 (.D(demultiplexer_1_out3), .en(and_5_out), .Q(byte_3), .clk(in_5), .clr(in_3));
  Register register_6 (.D(demultiplexer_1_out4), .en(and_6_out), .Q(byte_4), .clk(in_5), .clr(in_3));
  Register register_7 (.D(demultiplexer_1_out5), .en(and_7_out), .Q(byte_5), .clk(in_5), .clr(in_3));
  not not_20 (ready, pull_resistor_9_node);

  // Notes on the sheet:
  //   addr
  //   req
  //   s2
  //   reset
  //   addr Bit Selectors (s0-s2)
  //   s0
  //   clock
  //   s2
  //   fast clock
  //   reg bit selectors
  //   RAMuse
  //   s0
  //   RAMuse
  //   RAMread
  //   RAMaddr
  //   ready
  //   State Selectors
  //   Next state
  //   data from RAM
  //   0. Starting State
  //   1. Request first Bit
  //   2. Read in first bit
  //   3. Request Second bit
  //   4. Read in Second bit
  //   5. Request third bit
  //   6. read in third bit
  //   7. Request fourth bit
  //   8. Read in fourth bit
  //   9. Request fifth bit
  //   10. Read in fifth bit
  //   11. Request sixth bit
  //   12. Read in sixth bit
  //   13 - 14. wait
  //   15. Return to starting state 
  //   Updated by fast clock
  //   IF RAMread = 1 & Decoder selected that register
endmodule

module TESTING_q2 (
  input  in_1,
  input  [31:0] in_2,
  input  in_3,
  input  in_4,
  input  in_5,
  input  [9:0] in_6,
  input  in_7,
  input  [7:0] in_8,
  output [7:0] out_9,
  output [7:0] out_10,
  output [7:0] out_11,
  output [7:0] out_12,
  output [7:0] out_13,
  output [7:0] out_14,
  output out_15,
  output out_16,
  output out_17
);

  wire [7:0] ram_1_data;
  wire [9:0] bit_extender_1_out;
  wire [31:0] q2_1_out_14;

  q2 q2_1 (
    .in_2(in_2), .byte_0(out_9), .byte_1(out_10), .byte_2(out_11), .byte_3(out_12), .byte_4(out_13),
    .byte_5(out_14), .ready(out_15), .in_1(in_1), .in_3(in_3), .in_4(in_4), .in_5(in_5), .out_15(out_16),
    .out_14(q2_1_out_14), .RAMread(out_17), .in_6(ram_1_data));
  Bit_Extender #(.in_width(32), .out_width(10)) bit_extender_1 (.in(q2_1_out_14), .out(bit_extender_1_out));
  RAM #(.addrWidth(10), .bus("separate")) ram_1 (
    .addr(bit_extender_1_out), .din(in_8), .data(ram_1_data), .clk(in_7));  // open: str, sel, ld, clr

  // Notes on the sheet:
  //   Manual Address Input
  //   Manually For testing
  //   Manual Value Input
  //   RAM for Testing
endmodule

module q3 (
  input  [31:0] in_1,
  input  req,
  input  [31:0] in_3,
  input  DMemRead,
  input  DMemWrite,
  input  in_6,
  input  in_7,
  input  in_8,
  input  [7:0] in_9,
  output [31:0] out_10,
  output ready,
  output [31:0] out_12,
  output out_13,
  output [7:0] out_14,
  output out_15,
  output out_16,
  output out_17
);

  wire and_1_out, decoder_1_out0, decoder_1_out1, decoder_1_out2, decoder_1_out3, decoder_1_out4,
       decoder_1_out5, decoder_1_out6, decoder_1_out7, decoder_1_out8, decoder_1_out9, decoder_1_out10,
       decoder_1_out11, decoder_1_out12, decoder_1_out13, decoder_1_out14, decoder_1_out15,
       demultiplexer_2_out0, demultiplexer_2_out1, demultiplexer_2_out2, demultiplexer_2_out3, not_1_out,
       not_2_out, not_3_out, not_4_out, not_5_out, not_6_out, not_7_out, not_8_out, not_9_out, not_10_out,
       not_11_out, not_12_out, not_13_out, not_14_out, not_15_out, not_16_out, not_18_out, not_19_out,
       not_20_out, or_1_out, pull_resistor_7_node, pull_resistor_8_node, pull_resistor_9_node,
       pull_resistor_10_node, pull_resistor_11_node;
  wire [2:0] pull_resistor_5_node, tiny_diode_10__0_z_out;
  wire [3:0] pull_resistor_14_node, register_1_q;
  wire [7:0] demultiplexer_1_out0, demultiplexer_1_out1, demultiplexer_1_out2, demultiplexer_1_out3;

  and and_1 (and_1_out, req, in_7);
  or or_1 (or_1_out, ~decoder_1_out0, and_1_out);  // OR_Gate
  Decoder #(.select(4)) decoder_1 (
    .out0(decoder_1_out0), .out1(decoder_1_out1), .out2(decoder_1_out2), .out3(decoder_1_out3),
    .out4(decoder_1_out4), .out5(decoder_1_out5), .out6(decoder_1_out6), .out7(decoder_1_out7),
    .out8(decoder_1_out8), .out9(decoder_1_out9), .out10(decoder_1_out10), .out11(decoder_1_out11),
    .out12(decoder_1_out12), .out13(decoder_1_out13), .out14(decoder_1_out14), .out15(decoder_1_out15),
    .sel(register_1_q));  // open: en
  word2bytes word2bytes_1 (.in_1(in_1), .Ouput__Byte(out_14), .in_2(pull_resistor_5_node));
  Register #(.width(4)) register_1 (.D(pull_resistor_14_node), .en(or_1_out), .Q(register_1_q), .clk(in_8), .clr(in_6));
  Address_Incrementer address_incrementer_1 (.in_1(in_3), .out_3(out_12), .in_2(tiny_diode_10__0_z_out));
  not not_1 (not_1_out, decoder_1_out0);
  not not_2 (not_2_out, decoder_1_out1);
  not not_3 (not_3_out, decoder_1_out2);
  not not_4 (not_4_out, decoder_1_out3);
  not not_5 (not_5_out, decoder_1_out4);
  not not_6 (not_6_out, decoder_1_out5);
  not not_7 (not_7_out, decoder_1_out6);
  not not_8 (not_8_out, decoder_1_out7);
  not not_9 (not_9_out, decoder_1_out8);
  not not_10 (not_10_out, decoder_1_out9);
  not not_11 (not_11_out, decoder_1_out10);
  not not_12 (not_12_out, decoder_1_out11);
  not not_13 (not_13_out, decoder_1_out12);
  not not_14 (not_14_out, decoder_1_out13);
  not not_15 (not_15_out, decoder_1_out14);
  not not_16 (not_16_out, decoder_1_out15);
  Pull_Resistor #(.pull(1)) pull_resistor_1 (.node(tiny_diode_10__0_z_out[2]));
  Tiny_Diode tiny_diode_1 (._0_1_in(not_2_out), ._0_Z_out(tiny_diode_10__0_z_out[2]));
  Tiny_Diode tiny_diode_2 (._0_1_in(not_4_out), ._0_Z_out(tiny_diode_10__0_z_out[2]));
  Tiny_Diode tiny_diode_3 (._0_1_in(not_6_out), ._0_Z_out(tiny_diode_10__0_z_out[2]));
  Tiny_Diode tiny_diode_4 (._0_1_in(not_7_out), ._0_Z_out(tiny_diode_10__0_z_out[2]));
  Tiny_Diode tiny_diode_5 (._0_1_in(not_9_out), ._0_Z_out(tiny_diode_10__0_z_out[2]));
  Tiny_Diode tiny_diode_6 (._0_1_in(not_10_out), ._0_Z_out(tiny_diode_10__0_z_out[2]));
  Tiny_Diode tiny_diode_7 (._0_1_in(not_11_out), ._0_Z_out(tiny_diode_10__0_z_out[2]));
  Tiny_Diode tiny_diode_8 (._0_1_in(not_13_out), ._0_Z_out(tiny_diode_10__0_z_out[2]));
  Pull_Resistor #(.pull(1)) pull_resistor_2 (.node(tiny_diode_10__0_z_out[1]));
  Tiny_Diode tiny_diode_9 (._0_1_in(not_2_out), ._0_Z_out(tiny_diode_10__0_z_out[1]));
  Tiny_Diode tiny_diode_10 (._0_1_in(not_2_out), ._0_Z_out(tiny_diode_10__0_z_out[0]));
  Tiny_Diode tiny_diode_11 (._0_1_in(not_4_out), ._0_Z_out(tiny_diode_10__0_z_out[0]));
  Tiny_Diode tiny_diode_12 (._0_1_in(not_4_out), ._0_Z_out(tiny_diode_10__0_z_out[1]));
  Tiny_Diode tiny_diode_13 (._0_1_in(not_6_out), ._0_Z_out(tiny_diode_10__0_z_out[1]));
  Tiny_Diode tiny_diode_14 (._0_1_in(not_7_out), ._0_Z_out(tiny_diode_10__0_z_out[1]));
  Tiny_Diode tiny_diode_15 (._0_1_in(not_9_out), ._0_Z_out(tiny_diode_10__0_z_out[0]));
  Tiny_Diode tiny_diode_16 (._0_1_in(not_10_out), ._0_Z_out(tiny_diode_10__0_z_out[0]));
  Pull_Resistor #(.pull(1)) pull_resistor_3 (.node(tiny_diode_10__0_z_out[0]));
  Pull_Resistor #(.pull(1)) pull_resistor_4 (.node(pull_resistor_5_node[2]));
  Tiny_Diode tiny_diode_17 (._0_1_in(not_3_out), ._0_Z_out(pull_resistor_5_node[2]));
  Tiny_Diode tiny_diode_18 (._0_1_in(not_4_out), ._0_Z_out(pull_resistor_5_node[2]));
  Tiny_Diode tiny_diode_19 (._0_1_in(not_6_out), ._0_Z_out(pull_resistor_5_node[2]));
  Tiny_Diode tiny_diode_20 (._0_1_in(not_7_out), ._0_Z_out(pull_resistor_5_node[2]));
  Tiny_Diode tiny_diode_21 (._0_1_in(not_9_out), ._0_Z_out(pull_resistor_5_node[2]));
  Tiny_Diode tiny_diode_22 (._0_1_in(not_10_out), ._0_Z_out(pull_resistor_5_node[2]));
  Tiny_Diode tiny_diode_23 (._0_1_in(not_12_out), ._0_Z_out(pull_resistor_5_node[2]));
  Tiny_Diode tiny_diode_24 (._0_1_in(not_13_out), ._0_Z_out(pull_resistor_5_node[2]));
  Pull_Resistor #(.pull(1)) pull_resistor_5 (.node(pull_resistor_5_node[0]));
  Pull_Resistor #(.pull(1)) pull_resistor_6 (.node(pull_resistor_5_node[1]));
  Tiny_Diode tiny_diode_25 (._0_1_in(not_3_out), ._0_Z_out(pull_resistor_5_node[0]));
  Tiny_Diode tiny_diode_26 (._0_1_in(not_3_out), ._0_Z_out(pull_resistor_5_node[1]));
  Tiny_Diode tiny_diode_27 (._0_1_in(not_4_out), ._0_Z_out(pull_resistor_5_node[0]));
  Tiny_Diode tiny_diode_28 (._0_1_in(not_4_out), ._0_Z_out(pull_resistor_5_node[1]));
  Tiny_Diode tiny_diode_29 (._0_1_in(not_6_out), ._0_Z_out(pull_resistor_5_node[1]));
  Tiny_Diode tiny_diode_30 (._0_1_in(not_7_out), ._0_Z_out(pull_resistor_5_node[1]));
  Tiny_Diode tiny_diode_31 (._0_1_in(not_9_out), ._0_Z_out(pull_resistor_5_node[0]));
  Tiny_Diode tiny_diode_32 (._0_1_in(not_10_out), ._0_Z_out(pull_resistor_5_node[0]));
  not not_17 (out_13, pull_resistor_7_node);
  Pull_Resistor #(.pull(1)) pull_resistor_7 (.node(pull_resistor_7_node));
  Tiny_Diode tiny_diode_33 (._0_1_in(not_2_out), ._0_Z_out(pull_resistor_7_node));
  Tiny_Diode tiny_diode_34 (._0_1_in(not_3_out), ._0_Z_out(pull_resistor_7_node));
  Tiny_Diode tiny_diode_35 (._0_1_in(not_4_out), ._0_Z_out(pull_resistor_7_node));
  Tiny_Diode tiny_diode_36 (._0_1_in(not_5_out), ._0_Z_out(pull_resistor_7_node));
  Tiny_Diode tiny_diode_37 (._0_1_in(not_6_out), ._0_Z_out(pull_resistor_7_node));
  Tiny_Diode tiny_diode_38 (._0_1_in(not_7_out), ._0_Z_out(pull_resistor_7_node));
  Tiny_Diode tiny_diode_39 (._0_1_in(not_8_out), ._0_Z_out(pull_resistor_7_node));
  Tiny_Diode tiny_diode_40 (._0_1_in(not_9_out), ._0_Z_out(pull_resistor_7_node));
  Tiny_Diode tiny_diode_41 (._0_1_in(not_10_out), ._0_Z_out(pull_resistor_7_node));
  Tiny_Diode tiny_diode_42 (._0_1_in(not_11_out), ._0_Z_out(pull_resistor_7_node));
  Tiny_Diode tiny_diode_43 (._0_1_in(not_12_out), ._0_Z_out(pull_resistor_7_node));
  Tiny_Diode tiny_diode_44 (._0_1_in(not_13_out), ._0_Z_out(pull_resistor_7_node));
  Tiny_Diode tiny_diode_45 (._0_1_in(not_14_out), ._0_Z_out(pull_resistor_7_node));
  Pull_Resistor #(.pull(1)) pull_resistor_8 (.node(pull_resistor_8_node));
  Tiny_Diode tiny_diode_46 (._0_1_in(not_3_out), ._0_Z_out(pull_resistor_8_node));
  Tiny_Diode tiny_diode_47 (._0_1_in(not_6_out), ._0_Z_out(pull_resistor_8_node));
  Tiny_Diode tiny_diode_48 (._0_1_in(not_9_out), ._0_Z_out(pull_resistor_8_node));
  Tiny_Diode tiny_diode_49 (._0_1_in(not_12_out), ._0_Z_out(pull_resistor_8_node));
  Pull_Resistor #(.pull(1)) pull_resistor_9 (.node(pull_resistor_9_node));
  Tiny_Diode tiny_diode_50 (._0_1_in(not_5_out), ._0_Z_out(pull_resistor_9_node));
  Tiny_Diode tiny_diode_51 (._0_1_in(not_8_out), ._0_Z_out(pull_resistor_9_node));
  Tiny_Diode tiny_diode_52 (._0_1_in(not_11_out), ._0_Z_out(pull_resistor_9_node));
  Tiny_Diode tiny_diode_53 (._0_1_in(not_14_out), ._0_Z_out(pull_resistor_9_node));
  not not_18 (not_18_out, pull_resistor_8_node);
  and and_2 (out_15, not_18_out, DMemRead);
  Pull_Resistor #(.pull(1)) pull_resistor_10 (.node(pull_resistor_10_node));
  Tiny_Diode tiny_diode_54 (._0_1_in(not_5_out), ._0_Z_out(pull_resistor_10_node));
  Tiny_Diode tiny_diode_55 (._0_1_in(not_8_out), ._0_Z_out(pull_resistor_10_node));
  Tiny_Diode tiny_diode_56 (._0_1_in(not_11_out), ._0_Z_out(pull_resistor_10_node));
  Tiny_Diode tiny_diode_57 (._0_1_in(not_14_out), ._0_Z_out(pull_resistor_10_node));
  not not_19 (not_19_out, pull_resistor_9_node);
  and and_3 (out_16, not_19_out, DMemWrite);
  Pull_Resistor #(.pull(1)) pull_resistor_11 (.node(pull_resistor_11_node));
  Tiny_Diode tiny_diode_58 (._0_1_in(not_1_out), ._0_Z_out(pull_resistor_11_node));
  Tiny_Diode tiny_diode_59 (._0_1_in(not_15_out), ._0_Z_out(pull_resistor_11_node));
  Tiny_Diode tiny_diode_60 (._0_1_in(not_16_out), ._0_Z_out(pull_resistor_11_node));
  not not_20 (not_20_out, pull_resistor_10_node);
  and and_4 (out_17, not_20_out, DMemWrite);
  Pull_Resistor #(.pull(1)) pull_resistor_12 (.node(pull_resistor_14_node[3]));
  Pull_Resistor #(.pull(1)) pull_resistor_13 (.node(pull_resistor_14_node[2]));
  Tiny_Diode tiny_diode_61 (._0_1_in(not_1_out), ._0_Z_out(pull_resistor_14_node[2]));
  Tiny_Diode tiny_diode_62 (._0_1_in(not_1_out), ._0_Z_out(pull_resistor_14_node[3]));
  Tiny_Diode tiny_diode_63 (._0_1_in(not_2_out), ._0_Z_out(pull_resistor_14_node[2]));
  Tiny_Diode tiny_diode_64 (._0_1_in(not_2_out), ._0_Z_out(pull_resistor_14_node[3]));
  Tiny_Diode tiny_diode_65 (._0_1_in(not_3_out), ._0_Z_out(pull_resistor_14_node[3]));
  Tiny_Diode tiny_diode_66 (._0_1_in(not_3_out), ._0_Z_out(pull_resistor_14_node[2]));
  Tiny_Diode tiny_diode_67 (._0_1_in(not_4_out), ._0_Z_out(pull_resistor_14_node[3]));
  Tiny_Diode tiny_diode_68 (._0_1_in(not_5_out), ._0_Z_out(pull_resistor_14_node[3]));
  Tiny_Diode tiny_diode_69 (._0_1_in(not_6_out), ._0_Z_out(pull_resistor_14_node[3]));
  Tiny_Diode tiny_diode_70 (._0_1_in(not_7_out), ._0_Z_out(pull_resistor_14_node[3]));
  Tiny_Diode tiny_diode_71 (._0_1_in(not_8_out), ._0_Z_out(pull_resistor_14_node[2]));
  Tiny_Diode tiny_diode_72 (._0_1_in(not_9_out), ._0_Z_out(pull_resistor_14_node[2]));
  Tiny_Diode tiny_diode_73 (._0_1_in(not_10_out), ._0_Z_out(pull_resistor_14_node[2]));
  Tiny_Diode tiny_diode_74 (._0_1_in(not_11_out), ._0_Z_out(pull_resistor_14_node[2]));
  Tiny_Diode tiny_diode_75 (._0_1_in(not_16_out), ._0_Z_out(pull_resistor_14_node[3]));
  Tiny_Diode tiny_diode_76 (._0_1_in(not_16_out), ._0_Z_out(pull_resistor_14_node[2]));
  Pull_Resistor #(.pull(1)) pull_resistor_14 (.node(pull_resistor_14_node[0]));
  Pull_Resistor #(.pull(1)) pull_resistor_15 (.node(pull_resistor_14_node[1]));
  Tiny_Diode tiny_diode_77 (._0_1_in(not_1_out), ._0_Z_out(pull_resistor_14_node[1]));
  Tiny_Diode tiny_diode_78 (._0_1_in(not_2_out), ._0_Z_out(pull_resistor_14_node[0]));
  Tiny_Diode tiny_diode_79 (._0_1_in(not_4_out), ._0_Z_out(pull_resistor_14_node[1]));
  Tiny_Diode tiny_diode_80 (._0_1_in(not_4_out), ._0_Z_out(pull_resistor_14_node[0]));
  Tiny_Diode tiny_diode_81 (._0_1_in(not_5_out), ._0_Z_out(pull_resistor_14_node[1]));
  Tiny_Diode tiny_diode_82 (._0_1_in(not_6_out), ._0_Z_out(pull_resistor_14_node[0]));
  Tiny_Diode tiny_diode_83 (._0_1_in(not_8_out), ._0_Z_out(pull_resistor_14_node[1]));
  Tiny_Diode tiny_diode_84 (._0_1_in(not_8_out), ._0_Z_out(pull_resistor_14_node[0]));
  Tiny_Diode tiny_diode_85 (._0_1_in(not_9_out), ._0_Z_out(pull_resistor_14_node[1]));
  Tiny_Diode tiny_diode_86 (._0_1_in(not_10_out), ._0_Z_out(pull_resistor_14_node[0]));
  Tiny_Diode tiny_diode_87 (._0_1_in(not_12_out), ._0_Z_out(pull_resistor_14_node[0]));
  Tiny_Diode tiny_diode_88 (._0_1_in(not_12_out), ._0_Z_out(pull_resistor_14_node[1]));
  Tiny_Diode tiny_diode_89 (._0_1_in(not_13_out), ._0_Z_out(pull_resistor_14_node[1]));
  Tiny_Diode tiny_diode_90 (._0_1_in(not_14_out), ._0_Z_out(pull_resistor_14_node[0]));
  Tiny_Diode tiny_diode_91 (._0_1_in(not_16_out), ._0_Z_out(pull_resistor_14_node[0]));
  Tiny_Diode tiny_diode_92 (._0_1_in(not_16_out), ._0_Z_out(pull_resistor_14_node[1]));
  Demultiplexer #(.select(3), .width(8)) demultiplexer_1 (
    .out0(demultiplexer_1_out0), .out1(demultiplexer_1_out1), .out2(demultiplexer_1_out2),
    .out3(demultiplexer_1_out3), .in(in_9), .sel(pull_resistor_5_node));  // open: out4, out5, out6, out7, en
  Demultiplexer #(.select(3)) demultiplexer_2 (
    .out0(demultiplexer_2_out0), .out1(demultiplexer_2_out1), .out2(demultiplexer_2_out2),
    .out3(demultiplexer_2_out3), .in(out_15), .sel(pull_resistor_5_node));  // open: out4, out5, out6, out7, en
  Register register_2 (.D(demultiplexer_1_out0), .en(demultiplexer_2_out0), .Q(out_10[31:24]), .clk(in_8), .clr(in_6));
  Register register_3 (.D(demultiplexer_1_out1), .en(demultiplexer_2_out1), .Q(out_10[23:16]), .clk(in_8), .clr(in_6));
  Register register_4 (.D(demultiplexer_1_out2), .en(demultiplexer_2_out2), .Q(out_10[15:8]), .clk(in_8), .clr(in_6));
  Register register_5 (.D(demultiplexer_1_out3), .en(demultiplexer_2_out3), .Q(out_10[7:0]), .clk(in_8), .clr(in_6));
  not not_21 (ready, pull_resistor_11_node);

  // Notes on the sheet:
  //   data in
  //   addr
  //   s2
  //   reset
  //   clock
  //   addr Bit Selectors (s0-s2)
  //   fast clock
  //   s0
  //   s2
  //   reg bit selectors
  //   s0
  //   RAMuse
  //   RAMaddr
  //   RAMuse
  //   RAMread
  //   Data to RAM
  //   RAMwrite
  //   RAMread
  //   RAMclk
  //   RAMwrite
  //   ready
  //   RAMclock
  //   Next state
  //   State Selectors
  //   0. Starting State
  //   1. Request first byte
  //   2. Read in first byte
  //   3. Write first byte
  //   4. Request in Second byte
  //   5. Read in second byte
  //   6. Write second byte
  //   7. Request third byte
  //   8. Read in third byte
  //   9. Write third byte
  //   10. Request fourth byte
  //   11. Read in fourth byte
  //   12. Write third byte
  //   13 - 14. wait
  //   15. Return to starting state 
  //   Data from RAM
  //   Send Data to the Right Place
  //   Enable the Right Register
endmodule

module TESTING_q3 (
  input  in_1,
  input  in_2,
  input  in_3,
  input  [31:0] in_4,
  input  [31:0] in_5,
  input  in_6,
  input  in_7,
  input  in_8,
  input  [31:0] in_9,
  input  Manual_Ram_Clock,
  input  [7:0] in_11,
  output [31:0] out_12,
  output out_13,
  output out_14,
  output out_15
);

  wire q3_1_out_16, q3_1_out_17;
  wire [7:0] q3_1_out_14, ram_1_data;
  wire [9:0] bit_extender_1_out;
  wire [31:0] q3_1_out_12;

  Bit_Extender #(.in_width(32), .out_width(10)) bit_extender_1 (.in(q3_1_out_12), .out(bit_extender_1_out));
  q3 q3_1 (
    .in_1(in_4), .in_3(in_5), .DMemRead(in_2), .DMemWrite(in_3), .ready(out_13), .req(in_1), .in_6(in_6),
    .in_7(in_7), .in_8(in_8), .out_13(out_14), .out_12(q3_1_out_12), .out_14(q3_1_out_14), .out_15(out_15),
    .out_16(q3_1_out_16), .out_17(q3_1_out_17), .in_9(ram_1_data), .out_10(out_12));
  RAM #(.addrWidth(10), .bus("separate")) ram_1 (
    .addr(bit_extender_1_out), .din(q3_1_out_14), .data(ram_1_data), .str(q3_1_out_16), .clk(q3_1_out_17));  // open: sel, ld, clr

  // Notes on the sheet:
  //   Manual Address Input
  //   Manual Data Input
  //   RAM for Testing
endmodule

module Tiny_Diode (
  input  _0_1_in,
  output _0_Z_out
);

  wire not_1_out, pull_resistor_1_node;

  Pull_Resistor #(.pull(1)) pull_resistor_1 (.node(pull_resistor_1_node));
  buf buffer_1 (pull_resistor_1_node, _0_1_in);
  assign _0_Z_out = not_1_out ? pull_resistor_1_node : 1'bz;  // Controlled_Buffer controlled_buffer_1
  not not_1 (not_1_out, pull_resistor_1_node);
endmodule

module Address_Incrementer (
  input  [31:0] in_1,
  input  [2:0] in_2,
  output [31:0] out_3
);

  wire [31:0] adder_1_out, adder_2_out, adder_3_out, adder_4_out, adder_5_out, adder_6_out, adder_7_out;

  Adder #(.width(32)) adder_1 (.a({32{1'b0}}), .b(in_1), .out(adder_1_out));  // open: cin, cout
  Adder #(.width(32)) adder_2 (.a(32'h1), .b(in_1), .out(adder_2_out));  // open: cin, cout
  Adder #(.width(32)) adder_3 (.a(32'h2), .b(in_1), .out(adder_3_out));  // open: cin, cout
  Adder #(.width(32)) adder_4 (.a(32'h3), .b(in_1), .out(adder_4_out));  // open: cin, cout
  Adder #(.width(32)) adder_5 (.a(32'h4), .b(in_1), .out(adder_5_out));  // open: cin, cout
  Adder #(.width(32)) adder_6 (.a(32'h5), .b(in_1), .out(adder_6_out));  // open: cin, cout
  Adder #(.width(32)) adder_7 (.a(32'h6), .b(in_1), .out(adder_7_out));  // open: cin, cout
  Multiplexer #(.select(3), .width(32)) multiplexer_1 (
    .in0(adder_1_out), .in1(adder_2_out), .in2(adder_3_out), .in3(adder_4_out), .in4(adder_5_out),
    .in5(adder_6_out), .in6(adder_7_out), .out(out_3), .sel(in_2));  // open: in7, en

  // Notes on the sheet:
  //   INPUT: addr N
  //   INPUT: INC
  //   OUTPUT: addr N + INC
  //   INC=7 => hanging wires
endmodule

module word2bytes (
  input  [31:0] in_1,
  input  [2:0] in_2,
  output [7:0] Ouput__Byte
);

  Multiplexer #(.select(3), .width(8)) multiplexer_1 (
    .in0(in_1[31:24]), .in1(in_1[23:16]), .in2(in_1[15:8]), .in3(in_1[7:0]), .out(Ouput__Byte), .sel(in_2));  // open: in4, in5, in6, in7, en

  // Notes on the sheet:
  //   Input: Data Word
  //   Selecting a byte greate than 3
  //   causes hanging output
  //   Input: Selector (0-3)
endmodule
