// Logisim project carter_bastian_hw5_q1.circ as structural Verilog: 2 circuits, main circuit CND
module CND (
  input  [2:0] Condition_Codes,
  input  [3:0] ifun,
  output Cnd_CC_ifun
);

  wire and_1_out, and_2_out, and_3_out, and_4_out, and_5_out, and_6_out, and_7_out, and_8_out,
       decoder_1_out0, decoder_1_out1, decoder_1_out2, decoder_1_out3, decoder_1_out4, decoder_1_out5,
       decoder_1_out6, or_1_out, xor_1_out, xor_2_out, xor_3_out, xor_4_out;

  Decoder #(.select(4)) decoder_1 (
    .out0(decoder_1_out0), .out1(decoder_1_out1), .out2(decoder_1_out2), .out3(decoder_1_out3),
    .out4(decoder_1_out4), .out5(decoder_1_out5), .out6(decoder_1_out6), .sel(ifun));  // open: out7, out8, out9, out10, out11, out12, out13, out14, out15, en
  or or_1 (or_1_out, Condition_Codes[2], xor_1_out);
  xor xor_1 (xor_1_out, Condition_Codes[1], Condition_Codes[0]);
  xor xor_2 (xor_2_out, Condition_Codes[1], Condition_Codes[0]);
  xor xor_3 (xor_3_out, Condition_Codes[1], Condition_Codes[0]);
  and and_1 (and_1_out, ~Condition_Codes[2], ~xor_4_out);  // AND_Gate
  xor xor_4 (xor_4_out, Condition_Codes[1], Condition_Codes[0]);
  and and_2 (and_2_out, decoder_1_out0, 1'b1);
  and and_3 (and_3_out, or_1_out, decoder_1_out1);
  and and_4 (and_4_out, xor_2_out, decoder_1_out2);
  and and_5 (and_5_out, Condition_Codes[2], decoder_1_out3);
  and and_6 (and_6_out, ~Condition_Codes[2], decoder_1_out4);  // AND_Gate
  and and_7 (and_7_out, ~xor_3_out, decoder_1_out5);  // AND_Gate
  and and_8 (and_8_out, and_1_out, decoder_1_out6);
  or or_2 (Cnd_CC_ifun, and_2_out, and_3_out, and_4_out, and_5_out, and_6_out, and_7_out, and_8_out);

  // Notes on the sheet:
  //   Z/S/O
  //   0 = unconditional
  //   1 = less than or equal to
  //   2 = less than
  //   3 = equal to
  //   4 = not-equal to
  //   5 = greater than or equal to
  //   6 =  greater than
  //   condition codes
  //   O
  //   S
  //   Z
  //   ifun val
  //   0
  //   6
  //   (S xor O) | Z
  //   S xor O
  //   Z
  //   ~Z
  //   ~(S xor O)
  //   ~(S xor O) & ~Z
endmodule

module CND_testing (
  input  [2:0] in_1,
  input  [3:0] in_2,
  output out_3
);

  CND cnd_1 (.Condition_Codes(in_1), .ifun(in_2), .Cnd_CC_ifun(out_3));
endmodule
