// Logisim project carter_bastian_hw6_q1.circ as structural Verilog: 2 circuits, main circuit io testing
module io_testing (
  input  [31:0] in_1,
  input  [7:0] in_2,
  input  in_3,
  input  in_4,
  input  in_5,
  input  Manual_Clock,
  output [31:0] out_7
);

  wire io_1_kbd_clock, io_1_out_11, keyboard_1_avail, undriven;
  wire [6:0] io_1_tty_data, keyboard_1_data;

  io io_1 (
    .in_3(in_1), .in_4(in_2), .out_9(out_7), .TTY_data(io_1_tty_data), .out_11(io_1_out_11),
    .kbd_clock(io_1_kbd_clock), .kbd_status(keyboard_1_avail), .kbd_input(keyboard_1_data), .in_5(in_3),
    .in_6(in_4), .Clock(Manual_Clock));
  Keyboard keyboard_1 (.clk(io_1_kbd_clock), .avail(keyboard_1_avail), .data(keyboard_1_data));  // open: re, clr
  TTY #(.rows(1)) tty_1 (.data(io_1_tty_data), .clk(io_1_out_11), .we(undriven), .clr(in_5));
endmodule

module io (
  input  kbd_status,
  input  [6:0] kbd_input,
  input  [31:0] in_3,
  input  [7:0] in_4,
  input  in_5,
  input  in_6,
  input  Clock,
  output kbd_clock,
  output [31:0] out_9,
  output [6:0] TTY_data,
  output out_11
);

  wire comparator_1_eq, not_1_out, not_2_out;
  wire [3:0] decoder_1_out0;
  wire [31:0] and_1_out, multiplexer_1_out, register_1_q, register_2_q, register_3_q;
  wire [31:7] register_4_q;

  assign and_1_out = 32'hfffff0 & in_3;  // AND_Gate and_1, 32 bits wide
  Decoder #(.select(4)) decoder_1 (
    .out0(decoder_1_out0[0]), .out4(decoder_1_out0[1]), .out8(decoder_1_out0[2]), .out12(decoder_1_out0[3]),
    .sel(in_3[3:0]));  // open: out1, out2, out3, out5, out6, out7, out9, out10, out11, out13, out14, out15, en
  Comparator #(.width(32)) comparator_1 (.a(32'hfffe00), .b(and_1_out), .eq(comparator_1_eq));  // open: gt, lt
  Register #(.width(32), .trigger("high")) register_1 (
    .D({{31{1'b0}}, kbd_status}), .Q(register_1_q), .clk(1'b1));  // open: en, clr
  Register #(.width(32)) register_2 (.D({{25{1'b0}}, kbd_input}), .Q(register_2_q), .clk(Clock));  // open: en, clr
  Register #(.width(32), .trigger("high")) register_3 (.D(32'h1), .Q(register_3_q), .clk(1'b1));  // open: en, clr
  Register #(.width(32)) register_4 (
    .D({{24{1'b0}}, in_4}), .Q({register_4_q, TTY_data}), .clk(Clock));  // open: en, clr
  not not_1 (not_1_out, in_5);
  and and_2 (kbd_clock, not_1_out, Clock);
  not not_2 (not_2_out, in_5);
  Multiplexer #(.select(4), .width(32)) multiplexer_1 (
    .in1(register_1_q), .in2(register_2_q), .in4(register_3_q), .in8({register_4_q, TTY_data}),
    .out(multiplexer_1_out), .sel(decoder_1_out0), .en(in_6));  // open: in0, in3, in5, in6, in7, in9, in10, in11, in12, in13, in14, in15
  assign out_9 = comparator_1_eq ? multiplexer_1_out : 32'bz;  // Controlled_Buffer controlled_buffer_1
  and and_3 (out_11, Clock, not_2_out);

  // Notes on the sheet:
  //   Address
  //   Data
  //   Data in to get written to DDR
  //   Which Register are we Addressing?
  //   Are we being spoken to?
  //   KBSR
  //   KBDR
  //   DSR
  //   DDR
  //   KBSR
  //   Write
  //   KBDR
  //   Read
  //   DSR
  //   DDR
  //   No Output if
  //   We're not addressing
  //   this RAM
  //   Output
  //   TTY Clock
endmodule
