// Logisim project y86-uarch-skeleton-original.circ as structural Verilog: 11 circuits, main circuit dpath
module ishim (
  input  req,
  input  [31:0] addr_in,
  input  reset,
  input  clock,
  input  fast_clock,
  input  [7:0] data_from_RAM,
  output [7:0] byte0,
  output [7:0] byte1,
  output [7:0] byte2,
  output [7:0] byte3,
  output [7:0] byte4,
  output [7:0] byte5,
  output ready,
  output RAMuse,
  output [31:0] RAMaddr,
  output RAMread
);

  wire decoder_1_out0, decoder_1_out1, decoder_1_out2, decoder_1_out3, decoder_1_out4, decoder_1_out5,
       decoder_1_out6, or_1_out;
  wire [2:0] _3bit_q;
  wire [31:0] adder_1_out, bit_extender_1_out;

  D_Flip_Flop d_ff_1 (.clk(clock), .D(req), .Q(RAMread), .Qn(ready), .preset(1'b0), .en(1'b1), .reset(or_1_out));
  Decoder #(.select(3), .disabled(0)) decoder_1 (
    .out0(decoder_1_out0), .out1(decoder_1_out1), .out2(decoder_1_out2), .out3(decoder_1_out3),
    .out4(decoder_1_out4), .out5(decoder_1_out5), .out6(decoder_1_out6), .sel(_3bit_q), .en(RAMread));  // open: out7
  Counter #(.width(3), .max('h7)) _3bit (
    .load(1'b0), .count(RAMread), .Q(_3bit_q), .clk(fast_clock), .clr(or_1_out));  // open: D, carry
  or or_1 (or_1_out, decoder_1_out6, reset);
  assign bit_extender_1_out = {{29{1'b0}}, _3bit_q};  // Bit_Extender bit_extender_1
  Adder #(.width(32)) adder_1 (.a(addr_in), .b(bit_extender_1_out), .out(adder_1_out), .cin(1'b0));  // open: cout
  assign RAMaddr = RAMread ? adder_1_out : 32'bz;  // Controlled_Buffer controlled_buffer_1
  Register register_1 (.D(data_from_RAM), .en(decoder_1_out0), .Q(byte0), .clk(fast_clock), .clr(reset));
  Register register_2 (.D(data_from_RAM), .en(decoder_1_out1), .Q(byte1), .clk(fast_clock), .clr(reset));
  Register register_3 (.D(data_from_RAM), .en(decoder_1_out2), .Q(byte2), .clk(fast_clock), .clr(reset));
  Register register_4 (.D(data_from_RAM), .en(decoder_1_out3), .Q(byte3), .clk(fast_clock), .clr(reset));
  Register register_5 (.D(data_from_RAM), .en(decoder_1_out4), .Q(byte4), .clk(fast_clock), .clr(reset));
  Register register_6 (.D(data_from_RAM), .en(decoder_1_out5), .Q(byte5), .clk(fast_clock), .clr(reset));

  assign RAMuse = RAMread;

  // Notes on the sheet:
  //   3-bit counter
endmodule

module dshim (
  input  [31:0] addr_in,
  input  [7:0] data_from_RAM,
  input  [31:0] DataIn,
  input  DMemWrite,
  input  req,
  input  reset,
  input  clock,
  input  fast_clock,
  output [31:0] DataOut,
  output [7:0] data_to_RAM,
  output RAMWrite,
  output RAMread,
  output RAMclk,
  output ready,
  output RAMuse,
  output [31:0] RAMaddr
);

  wire comparator_1_eq, d_ff_1_q, d_ff_1_qn, decoder_1_out0, decoder_1_out1, decoder_1_out2, decoder_1_out3,
       or_1_out;
  wire [1:0] bit_extender_2_out;
  wire [2:0] _3bit_q;
  wire [31:0] adder_1_out, bit_extender_1_out, register_1_q;

  assign bit_extender_1_out = {{29{1'b0}}, _3bit_q};  // Bit_Extender bit_extender_1
  D_Flip_Flop d_ff_1 (
    .clk(clock), .D(DMemWrite), .Q(d_ff_1_q), .Qn(d_ff_1_qn), .preset(1'b0), .en(1'b1), .reset(reset));
  D_Flip_Flop in_use (.clk(clock), .D(req), .Q(RAMuse), .Qn(ready), .preset(1'b0), .en(1'b1), .reset(or_1_out));
  Adder #(.width(32)) adder_1 (.a(addr_in), .b(bit_extender_1_out), .out(adder_1_out), .cin(1'b0));  // open: cout
  and and_1 (RAMWrite, RAMuse, d_ff_1_q);
  and and_2 (RAMread, d_ff_1_qn, RAMuse);
  Decoder #(.select(3), .disabled(0)) decoder_1 (
    .out0(decoder_1_out0), .out1(decoder_1_out1), .out2(decoder_1_out2), .out3(decoder_1_out3),
    .sel(_3bit_q), .en(RAMread));  // open: out4, out5, out6, out7
  Counter #(.width(3), .max('h7)) _3bit (
    .load(1'b0), .count(RAMuse), .Q(_3bit_q), .clk(fast_clock), .clr(or_1_out));  // open: D, carry
  or or_1 (or_1_out, comparator_1_eq, reset);
  Comparator #(.width(3)) comparator_1 (.a(_3bit_q), .b(3'b100), .eq(comparator_1_eq));  // open: gt, lt
  assign RAMaddr = RAMuse ? adder_1_out : 32'bz;  // Controlled_Buffer controlled_buffer_1
  Register #(.width(32)) register_1 (.D(DataIn), .en(req), .Q(register_1_q), .clk(clock), .clr(reset));
  Bit_Extender #(.in_width(3), .out_width(2)) bit_extender_2 (.in(_3bit_q), .out(bit_extender_2_out));
  Multiplexer #(.select(2), .width(8)) multiplexer_1 (
    .in0(register_1_q[7:0]), .in1(register_1_q[15:8]), .in2(register_1_q[23:16]), .in3(register_1_q[31:24]),
    .out(data_to_RAM), .sel(bit_extender_2_out), .en(RAMWrite));
  Register register_2 (.D(data_from_RAM), .en(decoder_1_out0), .Q(DataOut[7:0]), .clk(fast_clock), .clr(reset));
  Register register_3 (.D(data_from_RAM), .en(decoder_1_out1), .Q(DataOut[15:8]), .clk(fast_clock), .clr(reset));
  Register register_4 (.D(data_from_RAM), .en(decoder_1_out2), .Q(DataOut[23:16]), .clk(fast_clock), .clr(reset));
  Register register_5 (.D(data_from_RAM), .en(decoder_1_out3), .Q(DataOut[31:24]), .clk(fast_clock), .clr(reset));
  and and_3 (RAMclk, fast_clock, RAMuse);

  // Notes on the sheet:
  //   writing?
  //   reading?
endmodule

module regwriter_box (
  input  [2:0] me,
  input  [2:0] dstE,
  input  reqE,
  input  [2:0] dstM,
  input  reqM,
  input  [31:0] valE,
  input  [31:0] valM,
  output [31:0] D0,
  output EN
);

  wire and_1_out, and_2_out, comparator_1_eq, comparator_2_eq;

  Comparator #(.width(3)) comparator_1 (.a(me), .b(dstE), .eq(comparator_1_eq));  // open: gt, lt
  Comparator #(.width(3)) comparator_2 (.a(me), .b(dstM), .eq(comparator_2_eq));  // open: gt, lt
  and and_1 (and_1_out, comparator_1_eq, reqE);
  and and_2 (and_2_out, comparator_2_eq, reqM);
  Multiplexer #(.width(32), .enable("false")) multiplexer_1 (.in0(valE), .in1(valM), .out(D0), .sel(and_2_out));
  or or_1 (EN, and_1_out, and_2_out);
endmodule

module regreader_box (
  input  [2:0] me,
  input  [2:0] srcA,
  input  [2:0] srcB,
  input  [31:0] Q,
  output [31:0] valA,
  output [31:0] valB
);

  wire comparator_1_eq, comparator_2_eq;

  Comparator #(.width(3)) comparator_1 (.a(me), .b(srcA), .eq(comparator_1_eq));  // open: gt, lt
  assign valA = comparator_1_eq ? Q : 32'bz;  // Controlled_Buffer controlled_buffer_1
  Comparator #(.width(3)) comparator_2 (.a(me), .b(srcB), .eq(comparator_2_eq));  // open: gt, lt
  assign valB = comparator_2_eq ? Q : 32'bz;  // Controlled_Buffer controlled_buffer_2
endmodule

module regwriter (
  input  [2:0] dstE,
  input  reqE,
  input  [2:0] dstM,
  input  reqM,
  input  [31:0] valE,
  input  [31:0] valM,
  input  clock,
  output [31:0] D0,
  output EN,
  output CLK,
  output [31:0] D1,
  output EN_2,
  output CLK_2,
  output [31:0] D2,
  output EN_3,
  output CLK_3,
  output [31:0] D3,
  output EN_4,
  output CLK_4,
  output [31:0] D4,
  output EN_5,
  output CLK_5,
  output [31:0] D5,
  output EN_6,
  output CLK_6,
  output [31:0] D6,
  output EN_7,
  output CLK_7,
  output [31:0] D7,
  output EN_8,
  output CLK_8
);

  regwriter_box regwriter_box_1 (
    .dstE(dstE), .reqE(reqE), .dstM(dstM), .reqM(reqM), .valE(valE), .valM(valM), .D0(D0), .EN(EN),
    .me(3'b000));
  regwriter_box regwriter_box_2 (
    .dstE(dstE), .reqE(reqE), .dstM(dstM), .reqM(reqM), .valE(valE), .valM(valM), .D0(D1), .EN(EN_2),
    .me(3'b001));
  regwriter_box regwriter_box_3 (
    .dstE(dstE), .reqE(reqE), .dstM(dstM), .reqM(reqM), .valE(valE), .valM(valM), .D0(D2), .EN(EN_3),
    .me(3'b010));
  regwriter_box regwriter_box_4 (
    .dstE(dstE), .reqE(reqE), .dstM(dstM), .reqM(reqM), .valE(valE), .valM(valM), .D0(D3), .EN(EN_4),
    .me(3'b011));
  regwriter_box regwriter_box_5 (
    .dstE(dstE), .reqE(reqE), .dstM(dstM), .reqM(reqM), .valE(valE), .valM(valM), .D0(D4), .EN(EN_5),
    .me(3'b100));
  regwriter_box regwriter_box_6 (
    .dstE(dstE), .reqE(reqE), .dstM(dstM), .reqM(reqM), .valE(valE), .valM(valM), .D0(D5), .EN(EN_6),
    .me(3'b101));
  regwriter_box regwriter_box_7 (
    .dstE(dstE), .reqE(reqE), .dstM(dstM), .reqM(reqM), .valE(valE), .valM(valM), .D0(D6), .EN(EN_7),
    .me(3'b110));
  regwriter_box regwriter_box_8 (
    .dstE(dstE), .reqE(reqE), .dstM(dstM), .reqM(reqM), .valE(valE), .valM(valM), .D0(D7), .EN(EN_8),
    .me(3'b111));

  assign CLK = clock;
  assign CLK_2 = clock;
  assign CLK_3 = clock;
  assign CLK_4 = clock;
  assign CLK_5 = clock;
  assign CLK_6 = clock;
  assign CLK_7 = clock;
  assign CLK_8 = clock;
endmodule

module regreader (
  input  [2:0] srcA,
  input  [2:0] srcB,
  input  [31:0] Q,
  input  [31:0] Q_2,
  input  [31:0] Q_3,
  input  reset,
  input  [31:0] Q_4,
  input  [31:0] Q_5,
  input  [31:0] Q_6,
  input  [31:0] Q_7,
  input  [31:0] Q_8,
  output CLR,
  output [31:0] valA,
  output [31:0] valB,
  output CLR_2,
  output CLR_3,
  output CLR_4,
  output CLR_5,
  output CLR_6,
  output CLR_7,
  output CLR_8
);

  regreader_box regreader_box_1 (.srcA(srcA), .srcB(srcB), .valA(valA), .valB(valB), .Q(Q), .me(3'b000));
  regreader_box regreader_box_2 (.srcA(srcA), .srcB(srcB), .valA(valA), .valB(valB), .Q(Q_2), .me(3'b001));
  regreader_box regreader_box_3 (.srcA(srcA), .srcB(srcB), .valA(valA), .valB(valB), .Q(Q_3), .me(3'b010));
  regreader_box regreader_box_4 (.srcA(srcA), .srcB(srcB), .valA(valA), .valB(valB), .Q(Q_4), .me(3'b011));
  regreader_box regreader_box_5 (.srcA(srcA), .srcB(srcB), .valA(valA), .valB(valB), .Q(Q_5), .me(3'b100));
  regreader_box regreader_box_6 (.srcA(srcA), .srcB(srcB), .valA(valA), .valB(valB), .Q(Q_6), .me(3'b101));
  regreader_box regreader_box_7 (.srcA(srcA), .srcB(srcB), .valA(valA), .valB(valB), .Q(Q_7), .me(3'b110));
  regreader_box regreader_box_8 (.srcA(srcA), .srcB(srcB), .valA(valA), .valB(valB), .Q(Q_8), .me(3'b111));

  assign CLR = reset;
  assign CLR_2 = reset;
  assign CLR_3 = reset;
  assign CLR_4 = reset;
  assign CLR_5 = reset;
  assign CLR_6 = reset;
  assign CLR_7 = reset;
  assign CLR_8 = reset;
endmodule

module dpath (
  input  Reset,
  output out_2
);

  wire cnd_1_cnd, comparator_1_eq, D_RAMClock, D_RAMread, D_RAMuse, D_RAMWrite, DMemReady, Fast_Clock_out,
       I_RAMread, I_RAMuse, IMemReady, multiplexer_8_out, or_1_out, regreader_1_clr, regreader_1_clr_2,
       regreader_1_clr_3, regreader_1_clr_4, regreader_1_clr_5, regreader_1_clr_6, regreader_1_clr_7,
       regreader_1_clr_8, regwriter_1_clk, regwriter_1_clk_2, regwriter_1_clk_3, regwriter_1_clk_4,
       regwriter_1_clk_5, regwriter_1_clk_6, regwriter_1_clk_7, regwriter_1_clk_8, regwriter_1_en,
       regwriter_1_en_2, regwriter_1_en_3, regwriter_1_en_4, regwriter_1_en_5, regwriter_1_en_6,
       regwriter_1_en_7, regwriter_1_en_8;
  wire [2:0] alu_1_cc, bit_extender_1_out, bit_extender_2_out, bit_extender_3_out, bit_extender_4_out, cc;
  wire [3:0] icode, ifun, isplit_1_ra, isplit_1_rb, multiplexer_5_out, multiplexer_6_out, multiplexer_7_out,
       multiplexer_11_out;
  wire [7:0] D_Data_from_RAM, D_Data_to_RAM, I_Data_from_RAM, ishim_1_byte0, ishim_1_byte1, ishim_1_byte2,
       ishim_1_byte3, ishim_1_byte4, ishim_1_byte5;
  wire [31:0] adder_1_out, alu_1_vale, D_RAMAddr, dshim_1_dataout, eax_q, ebp_q, ebx_q, ecx_q, edi_q, edx_q,
       esi_q, esp_q, I_RAMAddr, isplit_1_d_v, isplit_1_dest, MAR_q, MDR_q, multiplexer_1_out,
       multiplexer_2_out, multiplexer_3_out, multiplexer_4_out, multiplexer_9_out, multiplexer_10_out,
       multiplexer_12_out, multiplexer_13_out, PC_q, regreader_1_vala, regreader_1_valb, regwriter_1_d0,
       regwriter_1_d1, regwriter_1_d2, regwriter_1_d3, regwriter_1_d4, regwriter_1_d5, regwriter_1_d6,
       regwriter_1_d7;

  Register #(.width(32)) PC (.D(multiplexer_2_out), .en(1'b0), .Q(PC_q), .clk(out_2), .clr(Reset));
  Clock #(.highDuration(16), .lowDuration(16)) Clock (.out(out_2));
  Clock Fast_Clock (.out(Fast_Clock_out));
  // Probe on 1'b0
  // Probe on 2'b00
  // Probe on multiplexer_1_out
  Multiplexer #(.select(2), .width(32), .enable("false")) multiplexer_1 (
    .in0(32'h1), .in1(32'h2), .in2(32'h5), .in3(32'h6), .out(multiplexer_1_out), .sel(2'b00));
  // Probe on 1'b0
  Adder #(.width(32)) adder_1 (.a(multiplexer_1_out), .b(PC_q), .out(adder_1_out));  // open: cin, cout
  CND cnd_1 (.ZSO(cc), .ifun(ifun), .CND(cnd_1_cnd));
  ishim ishim_1 (
    .req(1'b0), .byte0(ishim_1_byte0), .byte1(ishim_1_byte1), .byte2(ishim_1_byte2), .addr_in(PC_q),
    .byte3(ishim_1_byte3), .byte4(ishim_1_byte4), .byte5(ishim_1_byte5), .ready(IMemReady), .reset(Reset),
    .clock(out_2), .fast_clock(Fast_Clock_out), .RAMuse(I_RAMuse), .RAMaddr(I_RAMAddr), .RAMread(I_RAMread),
    .data_from_RAM(I_Data_from_RAM));
  // Probe on 1'b0
  Multiplexer #(.select(2), .width(32), .enable("false")) multiplexer_2 (
    .in0(adder_1_out), .in1(multiplexer_4_out), .in2(dshim_1_dataout), .in3(multiplexer_3_out),
    .out(multiplexer_2_out), .sel(2'b00));
  Multiplexer #(.width(32), .enable("false")) multiplexer_3 (
    .in0(adder_1_out), .in1(multiplexer_4_out), .out(multiplexer_3_out), .sel(cnd_1_cnd));
  isplit isplit_1 (
    .B0(ishim_1_byte0), .B1(ishim_1_byte1), .B2(ishim_1_byte2), .B3(ishim_1_byte3), .B4(ishim_1_byte4),
    .B5(ishim_1_byte5), .icode(icode), .ifun(ifun), .rA(isplit_1_ra), .rB(isplit_1_rb), .Dest(isplit_1_dest),
    .D_V(isplit_1_d_v));
  // Probe on 1'b0
  // Probe on 1'b0
  // Probe on icode
  // Probe on ifun
  Multiplexer #(.width(32), .enable("false")) multiplexer_4 (
    .in0(isplit_1_dest), .in1(isplit_1_d_v), .out(multiplexer_4_out), .sel(1'b0));
  // Probe on 2'b00
  // Probe on isplit_1_ra
  // Probe on isplit_1_rb
  // Probe on 1'b0
  Multiplexer #(.width(4), .enable("false")) multiplexer_5 (
    .in0(isplit_1_rb), .out(multiplexer_5_out), .sel(1'b0));  // open: in1
  Multiplexer #(.width(4), .enable("false")) multiplexer_6 (
    .in0(isplit_1_ra), .in1(4'b0100), .out(multiplexer_6_out), .sel(1'b0));
  Multiplexer #(.width(4), .enable("false")) multiplexer_7 (
    .in0(isplit_1_rb), .in1(4'b0100), .out(multiplexer_7_out), .sel(1'b0));
  Comparator #(.width(4)) comparator_1 (.a(isplit_1_rb), .b(4'b1111), .eq(comparator_1_eq));  // open: gt, lt
  // Probe on 2'b00
  Bit_Extender #(.in_width(4), .out_width(3)) bit_extender_1 (.in(multiplexer_5_out), .out(bit_extender_1_out));
  Multiplexer #(.select(2), .enable("false")) multiplexer_8 (
    .in0(1'b0), .in1(1'b1), .in2(cnd_1_cnd), .out(multiplexer_8_out), .sel(2'b00));  // open: in3
  Bit_Extender #(.in_width(4), .out_width(3)) bit_extender_2 (.in(isplit_1_ra), .out(bit_extender_2_out));
  Bit_Extender #(.in_width(4), .out_width(3)) bit_extender_3 (.in(multiplexer_6_out), .out(bit_extender_3_out));
  Bit_Extender #(.in_width(4), .out_width(3)) bit_extender_4 (.in(multiplexer_7_out), .out(bit_extender_4_out));
  // Probe on 1'b0
  regwriter regwriter_1 (
    .dstE(bit_extender_1_out), .reqE(multiplexer_8_out), .dstM(bit_extender_2_out), .reqM(1'b0),
    .valE(alu_1_vale), .valM(dshim_1_dataout), .clock(out_2), .D0(regwriter_1_d0), .EN(regwriter_1_en),
    .CLK(regwriter_1_clk), .D1(regwriter_1_d1), .EN_2(regwriter_1_en_2), .CLK_2(regwriter_1_clk_2),
    .D2(regwriter_1_d2), .EN_3(regwriter_1_en_3), .CLK_3(regwriter_1_clk_3), .D3(regwriter_1_d3),
    .EN_4(regwriter_1_en_4), .CLK_4(regwriter_1_clk_4), .D4(regwriter_1_d4), .EN_5(regwriter_1_en_5),
    .CLK_5(regwriter_1_clk_5), .D5(regwriter_1_d5), .EN_6(regwriter_1_en_6), .CLK_6(regwriter_1_clk_6),
    .D6(regwriter_1_d6), .EN_7(regwriter_1_en_7), .CLK_7(regwriter_1_clk_7), .D7(regwriter_1_d7),
    .EN_8(regwriter_1_en_8), .CLK_8(regwriter_1_clk_8));
  Register #(.width(32)) eax (
    .D(regwriter_1_d0), .en(regwriter_1_en), .Q(eax_q), .clk(regwriter_1_clk), .clr(regreader_1_clr));
  Register #(.width(32)) ecx (
    .D(regwriter_1_d1), .en(regwriter_1_en_2), .Q(ecx_q), .clk(regwriter_1_clk_2), .clr(regreader_1_clr_2));
  Register #(.width(32)) edx (
    .D(regwriter_1_d2), .en(regwriter_1_en_3), .Q(edx_q), .clk(regwriter_1_clk_3), .clr(regreader_1_clr_3));
  Register #(.width(32)) ebx (
    .D(regwriter_1_d3), .en(regwriter_1_en_4), .Q(ebx_q), .clk(regwriter_1_clk_4), .clr(regreader_1_clr_4));
  Register #(.width(32)) esp (
    .D(regwriter_1_d4), .en(regwriter_1_en_5), .Q(esp_q), .clk(regwriter_1_clk_5), .clr(regreader_1_clr_5));
  Register #(.width(32)) ebp (
    .D(regwriter_1_d5), .en(regwriter_1_en_6), .Q(ebp_q), .clk(regwriter_1_clk_6), .clr(regreader_1_clr_6));
  Register #(.width(32)) esi (
    .D(regwriter_1_d6), .en(regwriter_1_en_7), .Q(esi_q), .clk(regwriter_1_clk_7), .clr(regreader_1_clr_7));
  Register #(.width(32)) edi (
    .D(regwriter_1_d7), .en(regwriter_1_en_8), .Q(edi_q), .clk(regwriter_1_clk_8), .clr(regreader_1_clr_8));
  // Probe on 1'b0
  // Probe on 1'b0
  regreader regreader_1 (
    .srcA(bit_extender_3_out), .srcB(bit_extender_4_out), .valA(regreader_1_vala), .valB(regreader_1_valb),
    .reset(Reset), .CLR(regreader_1_clr), .Q(eax_q), .CLR_2(regreader_1_clr_2), .Q_2(ecx_q),
    .CLR_3(regreader_1_clr_3), .Q_3(edx_q), .CLR_4(regreader_1_clr_4), .Q_4(ebx_q),
    .CLR_5(regreader_1_clr_5), .Q_5(esp_q), .CLR_6(regreader_1_clr_6), .Q_6(ebp_q),
    .CLR_7(regreader_1_clr_7), .Q_7(esi_q), .CLR_8(regreader_1_clr_8), .Q_8(edi_q));
  // Probe on regreader_1_vala
  // Probe on regreader_1_valb
  // Probe on multiplexer_4_out
  // Probe on 1'b0
  // Probe on 1'b0
  Multiplexer #(.select(2), .width(32), .enable("false")) multiplexer_9 (
    .in0(regreader_1_vala), .in1(multiplexer_4_out), .in2(32'h4), .in3(32'hfffffffc),
    .out(multiplexer_9_out), .sel(2'b00));
  or or_1 (or_1_out, 1'b0, comparator_1_eq);
  // Probe on 1'b0
  alu alu_1 (
    .CC(alu_1_cc), .ALU_A(multiplexer_9_out), .valE(alu_1_vale), .ALU_B(multiplexer_10_out),
    .ALU_op(multiplexer_11_out));
  Multiplexer #(.width(32), .enable("false")) multiplexer_10 (
    .in0(regreader_1_valb), .in1({32{1'b0}}), .out(multiplexer_10_out), .sel(or_1_out));
  Multiplexer #(.width(4), .enable("false")) multiplexer_11 (
    .in0(4'b0000), .in1(ifun), .out(multiplexer_11_out), .sel(1'b0));
  // Probe on 1'b0
  // Probe on 1'b0
  // Probe on cc
  Register #(.width(3)) u_CC (.D(alu_1_cc), .en(1'b0), .Q(cc), .clk(out_2), .clr(Reset));
  // Probe on 1'b0
  // Probe on adder_1_out
  // Probe on alu_1_vale
  Multiplexer #(.width(32), .enable("false")) multiplexer_12 (
    .in0(regreader_1_vala), .in1(adder_1_out), .out(multiplexer_12_out), .sel(1'b0));
  Multiplexer #(.width(32), .enable("false")) multiplexer_13 (
    .in0(alu_1_vale), .in1(regreader_1_vala), .out(multiplexer_13_out), .sel(1'b0));
  // Probe on 2'b00
  Register #(.width(32)) MDR (.D(multiplexer_12_out), .en(1'b0), .Q(MDR_q), .clk(out_2), .clr(Reset));
  Register #(.width(32)) MAR (.D(multiplexer_13_out), .en(1'b0), .Q(MAR_q), .clk(out_2), .clr(Reset));
  // Probe on 1'b0
  // Probe on dshim_1_dataout
  dshim dshim_1 (
    .DataOut(dshim_1_dataout), .addr_in(MAR_q), .data_from_RAM(D_Data_from_RAM), .DataIn(MDR_q),
    .data_to_RAM(D_Data_to_RAM), .RAMWrite(D_RAMWrite), .DMemWrite(1'b0), .RAMread(D_RAMread), .req(1'b0),
    .RAMclk(D_RAMClock), .ready(DMemReady), .reset(Reset), .clock(out_2), .fast_clock(Fast_Clock_out),
    .RAMuse(D_RAMuse), .RAMaddr(D_RAMAddr));

  // Other names for the same wires on the sheet: Clock = out_2

  // Notes on the sheet:
  //   Y86 Skeleton
  //   May 10, 2015
  //   Fetch
  //   BUG FIX
  //   connect to memory!
  //   valP
  //   valM
  //   Decode
  //   SWS and Taylor Cathcart and Vijay Kothari, based on a skeleton from Matt Kretchmar
  //   rB == F?
  //   Execute
  //   replace this with your FSM!
  //   Memory
  //   PC
  //   connect to memory (and io,
  //    pretending to be memory)
endmodule

module isplit (
  input  [7:0] B0,
  input  [7:0] B1,
  input  [7:0] B2,
  input  [7:0] B3,
  input  [7:0] B4,
  input  [7:0] B5,
  output [3:0] icode,
  output [3:0] ifun,
  output [3:0] rA,
  output [3:0] rB,
  output [31:0] Dest,
  output [31:0] D_V
);


  assign D_V = {B5, B4, B3, B2};
  assign Dest = {B4, B3, B2, B1};
  assign icode = B0[7:4];
  assign ifun = B0[3:0];
  assign rA = B1[7:4];
  assign rB = B1[3:0];
endmodule

module alu (
  input  [31:0] ALU_A,
  input  [31:0] ALU_B,
  input  [3:0] ALU_op,
  output [2:0] CC,
  output [31:0] valE
);

  wire and_2_out, msb_1_msb, msb_2_msb, msb_3_msb, nor_1_out, xnor_1_out, xor_2_out;
  wire [31:0] adder_1_out, and_1_out, multiplexer_1_out, not_1_out, xor_1_out;

  assign not_1_out = ~ALU_A;  // NOT_Gate not_1, 32 bits wide
  assign and_1_out = ALU_A & ALU_B;  // AND_Gate and_1, 32 bits wide
  assign xor_1_out = ALU_A ^ ALU_B;  // XOR_Gate xor_1, 32 bits wide
  nor nor_1 (nor_1_out, ALU_op[2], ALU_op[3]);
  MSB msb_1 (.MSB(msb_1_msb), .Value(multiplexer_1_out));
  MSB msb_2 (.MSB(msb_2_msb), .Value(ALU_B));
  Multiplexer #(.width(32), .enable("false")) multiplexer_1 (
    .in0(ALU_A), .in1(not_1_out), .out(multiplexer_1_out), .sel(ALU_op[0]));
  xnor xnor_1 (xnor_1_out, msb_1_msb, msb_2_msb);
  xor xor_2 (xor_2_out, msb_1_msb, msb_3_msb);
  MSB msb_3 (.MSB(msb_3_msb), .Value(adder_1_out));
  Adder #(.width(32)) adder_1 (.a(multiplexer_1_out), .b(ALU_B), .out(adder_1_out), .cin(ALU_op[0]));  // open: cout
  Multiplexer #(.disabled(0), .enable("false")) multiplexer_2 (
    .in0(and_2_out), .in1(1'b0), .out(CC[0]), .sel(ALU_op[1]));
  and and_2 (and_2_out, xnor_1_out, xor_2_out);
  Comparator #(.width(32)) comparator_1 (.a({32{1'b0}}), .b(valE), .eq(CC[2]));  // open: gt, lt
  MSB msb_4 (.MSB(CC[1]), .Value(valE));
  Multiplexer #(.select(2), .width(32), .disabled(0)) multiplexer_3 (
    .in0(adder_1_out), .in1(adder_1_out), .in2(and_1_out), .in3(xor_1_out), .out(valE), .sel(ALU_op[1:0]),
    .en(nor_1_out));

  // Notes on the sheet:
  //   add
  //   sub
  //   32-bit and
  //   32-bit xor
  //   or if both inputs are positive and result is negatve
  //   if both inputs are negative and result is positve
  //   an overflow occurred
  //   if sub carry in = 1
  //   (Zero Bit, Signed Bit, Overflow Bit)
  //   add
  //   sub
  //   and
  //   xor
  //   op selector
  //   is legit op?
endmodule

module MSB (
  input  [31:0] Value,
  output MSB
);


  assign MSB = Value[31];
endmodule

module CND (
  input  [2:0] ZSO,
  input  [3:0] ifun,
  output CND
);

  wire not_1_out, not_2_out, not_3_out, not_4_out, or_1_out, xor_1_out;

  or or_1 (or_1_out, ZSO[2], xor_1_out);
  xor xor_1 (xor_1_out, ZSO[1], ZSO[0]);
  not not_1 (not_1_out, ZSO[2]);
  not not_2 (not_2_out, xor_1_out);
  not not_3 (not_3_out, or_1_out);
  Multiplexer #(.select(3), .disabled(0)) multiplexer_1 (
    .in0(1'b1), .in1(or_1_out), .in2(xor_1_out), .in3(ZSO[2]), .in4(not_1_out), .in5(not_2_out),
    .in6(not_3_out), .in7(1'b0), .out(CND), .sel(ifun[2:0]), .en(not_4_out));
  not not_4 (not_4_out, ifun[3]);

  // Notes on the sheet:
  //   Sample CND, from SWS
  //   always
  //   le
  //   l
  //   e
  //   ne
  //   ge
  //   g
endmodule
