// Logisim project democircs.circ as structural Verilog: 5 circuits, main circuit basic0
module basic0 (
  output out_1,
  output out_2
);

  Pull_Resistor #(.pull(1)) pull_resistor_1 (.node(out_2));

  assign out_1 = 1'b1;
endmodule

module trandemo (
  input  in_1,
  input  in_2,
  input  in_3,
  input  in_4,
  input  in_5,
  input  in_6,
  output out_7,
  output out_8,
  output out_9,
  output out_10
);

  Transistor transistor_1 (.in(in_3), .out(out_7), .gate(in_1));
  Transistor transistor_2 (.in(1'b1), .out(out_10), .gate(in_5));
  Transistor #(.\type ("n")) transistor_3 (.in(in_4), .out(out_8), .gate(in_2));
  Transistor #(.\type ("n")) transistor_4 (.in(1'b0), .out(out_9), .gate(in_6));

  // Notes on the sheet:
  //   p-type
  //   p-type
  //   n-type
  //   n-type
  //   (in LogiSim)
  //   (in the real world)
endmodule

module logic0 (
  input  NOT,
  output out_2
);

  not not_1 (out_2, NOT);

  // Notes on the sheet:
  //   (aka "inverter")
endmodule

module logic1 (
  input  in_1,
  input  in_2,
  output out_3,
  output out_4,
  output out_5,
  output out_6,
  output out_7,
  output out_8,
  output out_9
);

  wire and_2_out, or_2_out;

  or or_1 (out_3, in_1, in_2);
  or or_2 (or_2_out, in_1, in_2);
  // NOR_Gate nor_1 has open pins: in0=in_1, in1=in_2, out=open
  // NOT_Gate not_1 has open pins: in=or_2_out, out=open
  // AND_Gate and_1 has open pins: in0=in_1, in1=in_2, out=open
  and and_2 (and_2_out, in_1, in_2);
  // NOT_Gate not_2 has open pins: in=and_2_out, out=open
  // NAND_Gate nand_1 has open pins: in0=in_1, in1=in_2, out=open
  // XOR_Gate xor_1 has open pins: in0=in_1, in1=in_2, out=open

  // Notes on the sheet:
  //   OR/NOR
  //   AND/NAND
  //   XOR
endmodule

module logic2 (
  input  in_1,
  input  in_2,
  input  in_3,
  input  in_4,
  input  in_5
);

  wire or_1_out;

  // Probe on or_1_out
  or or_1 (or_1_out, in_1, in_2, in_3, in_4, in_5);
  // AND_Gate and_1 has open pins: in0=in_1, in1=in_2, in2=in_3, in3=in_4, in4=in_5, out=open
  // Probe on nothing
endmodule
