// Logisim project diode.circ as structural Verilog: 2 circuits, main circuit diode
module main (
  input  in_1,
  output out_2,
  output out_3,
  output out_4
);

  diode diode_1 (._0_1_in(in_1), ._0_Z_out(out_3));
  diode diode_2 (._0_1_in(1'b0), ._0_Z_out(out_4));

  assign out_2 = in_1;

  // Notes on the sheet:
  //   (sws's rough logisim simulation of a diode.)
endmodule

module diode (
  input  _0_1_in,
  output _0_Z_out
);

  wire not_1_out, pull_resistor_1_node;

  Pull_Resistor #(.pull(1)) pull_resistor_1 (.node(pull_resistor_1_node));
  buf buffer_1 (pull_resistor_1_node, _0_1_in);
  assign _0_Z_out = not_1_out ? pull_resistor_1_node : 1'bz;  // Controlled_Buffer controlled_buffer_1
  not not_1 (not_1_out, pull_resistor_1_node);
endmodule
