// Logisim project dlaw.circ as structural Verilog: 1 circuit, main circuit main
module main (
  input  A,
  input  B,
  output out_3,
  output out_4,
  output Q,
  output out_6,
  output out_7
);

  not not_1 (out_3, A);
  and and_1 (out_4, out_3, out_6);
  not not_2 (out_6, B);
  or or_1 (out_7, A, B);
  not not_3 (Q, out_4);
endmodule
