// Logisim project fineprint3.circ as structural Verilog: 8 circuits, main circuit main
module _8_or (
  input  in_1,
  input  in_2,
  output out_3,
  output out_4,
  output out_5,
  output out_6,
  output out_7,
  output out_8
);

  nand nand_1 (out_3, in_1, in_2);
  or or_1 (out_6, out_3, out_3, out_3, out_3, out_3, out_3, out_3, out_3, 1'b0, 1'b0, 1'b0, 1'b0, 1'b0, 1'b0, 1'b0, 1'b0, 1'b0, 1'b0, 1'b0, 1'b0, 1'b0, 1'b0, 1'b0, 1'b0, 1'b0, 1'b0, 1'b0, 1'b0, 1'b0, 1'b0, 1'b0, 1'b0);

  assign out_4 = out_3;
  assign out_5 = 1'b0;
  assign out_7 = 1'b0;
  assign out_8 = 1'b0;

  // Notes on the sheet:
  //   Simplified View
endmodule

module _16_or (
  input  in_1,
  input  in_2,
  output out_3,
  output out_4,
  output out_5,
  output out_6,
  output out_7,
  output out_8
);

  nand nand_1 (out_3, in_1, in_2);
  or or_1 (out_6, out_3, out_3, out_3, out_3, out_3, out_3, out_3, out_3, out_3, out_3, out_3, out_3, out_3, out_3, out_3, out_3, 1'b0, 1'b0, 1'b0, 1'b0, 1'b0, 1'b0, 1'b0, 1'b0, 1'b0, 1'b0, 1'b0, 1'b0, 1'b0, 1'b0, 1'b0, 1'b0);

  assign out_4 = out_3;
  assign out_5 = out_3;
  assign out_7 = 1'b0;
  assign out_8 = 1'b0;

  // Notes on the sheet:
  //   Simplified View
endmodule

module _24_or (
  input  in_1,
  input  in_2,
  output out_3,
  output out_4,
  output out_5,
  output out_6,
  output out_7,
  output out_8
);

  nand nand_1 (out_3, in_1, in_2);
  or or_1 (out_6, out_3, out_3, out_3, out_3, out_3, out_3, out_3, out_3, out_3, out_3, out_3, out_3, out_3, out_3, out_3, out_3, out_3, out_3, out_3, out_3, out_3, out_3, out_3, out_3, 1'b0, 1'b0, 1'b0, 1'b0, 1'b0, 1'b0, 1'b0, 1'b0);

  assign out_4 = out_3;
  assign out_5 = out_3;
  assign out_7 = out_3;
  assign out_8 = 1'b0;

  // Notes on the sheet:
  //   Simplified View
endmodule

module _32_or (
  input  in_1,
  input  in_2,
  output out_3,
  output out_4,
  output out_5,
  output out_6,
  output out_7,
  output out_8
);

  nand nand_1 (out_3, in_1, in_2);
  or or_1 (out_6, out_3, out_3, out_3, out_3, out_3, out_3, out_3, out_3, out_3, out_3, out_3, out_3, out_3, out_3, out_3, out_3, out_3, out_3, out_3, out_3, out_3, out_3, out_3, out_3, out_3, out_3, out_3, out_3, out_3, out_3, out_3, out_3);

  assign out_4 = out_3;
  assign out_5 = out_3;
  assign out_7 = out_3;
  assign out_8 = out_3;

  // Notes on the sheet:
  //   Simplified View
endmodule

module main (
  input  in_1,
  input  in_2,
  input  _2,
  input  _4,
  input  _6,
  input  _8,
  output _1,
  output _15,
  output _14,
  output _12,
  output _10
);

  wire nand_1_out, not_1_out, not_3_out, or_1_out;

  Pull_Resistor #(.pull(1)) pull_resistor_1 ();  // open: node
  LED #(.active("false")) led_1 (.in(nand_1_out));
  nand nand_1 (nand_1_out, in_1, in_2);
  Pull_Resistor #(.pull(1)) pull_resistor_2 ();  // open: node
  LED #(.active("false")) led_2 (.in(not_1_out));
  not not_1 (not_1_out, nand_1_out);
  not not_2 (_1, not_1_out);
  simulated_SPDT_switch simulated_spdt_switch_1 (.throw1(_1), .throw0(1'b0), .pole(_15), .control(_2));
  simulated_SPDT_switch simulated_spdt_switch_2 (.throw1(_1), .throw0(1'b0), .pole(_14), .control(_4));
  simulated_SPDT_switch simulated_spdt_switch_3 (.throw1(_1), .throw0(1'b0), .pole(_12), .control(_6));
  simulated_SPDT_switch simulated_spdt_switch_4 (.throw1(_1), .throw0(1'b0), .pole(_10), .control(_8));
  or or_1 (or_1_out, _15, _15, _15, _15, _15, _15, _15, _15, _14, _14, _14, _14, _14, _14, _14, _14, _12, _12, _12, _12, _12, _12, _12, _12, _10, _10, _10, _10, _10, _10, _10, _10);
  Pull_Resistor #(.pull(1)) pull_resistor_3 ();  // open: node
  LED #(.active("false")) led_3 (.in(or_1_out));
  not not_3 (not_3_out, or_1_out);
  Pull_Resistor #(.pull(1)) pull_resistor_4 ();  // open: node
  LED #(.active("false")) led_4 (.in(not_3_out));

  // Notes on the sheet:
  //   "0"
  //   "1"
  //   Simplified View
  //   16
  //   3
  //   13
  //   5
  //   11
  //   7
  //   9
  //   "0"
  //   "1"
endmodule

module or_tree (
  input  in_1,
  input  in_2,
  input  _2,
  input  _4,
  input  _6,
  input  _8
);

  wire IC2_2_out, IC2_3_out, IC2_4_out, IC2_out, IC3_2_out, IC3_3_out, IC3_4_out, IC3_out, IC4_2_out,
       IC4_3_out, IC4_4_out, IC4_out, IC5_2_out, IC5_3_out, IC5_4_out, IC5_out, IC6_2_out, IC6_3_out,
       IC6_4_out, IC6_out, IC7_2_out, IC7_3_out, IC7_4_out, IC7_out, IC8_2_out, IC8_3_out, IC8_4_out,
       IC8_out, IC9_2_out, IC9_3_out, IC9_out, nand_1_out, nand_2_out, simulated_spdt_switch_1_pole,
       simulated_spdt_switch_2_pole, simulated_spdt_switch_3_pole, simulated_spdt_switch_4_pole;

  nand nand_1 (nand_1_out, in_1, in_2);
  simulated_SPDT_switch simulated_spdt_switch_1 (
    .throw1(nand_1_out), .throw0(1'b0), .pole(simulated_spdt_switch_1_pole), .control(_2));
  simulated_SPDT_switch simulated_spdt_switch_2 (
    .throw1(nand_1_out), .throw0(1'b0), .pole(simulated_spdt_switch_2_pole), .control(_4));
  simulated_SPDT_switch simulated_spdt_switch_3 (
    .throw1(nand_1_out), .throw0(1'b0), .pole(simulated_spdt_switch_3_pole), .control(_6));
  simulated_SPDT_switch simulated_spdt_switch_4 (
    .throw1(nand_1_out), .throw0(1'b0), .pole(simulated_spdt_switch_4_pole), .control(_8));
  or IC2 (IC2_out, simulated_spdt_switch_1_pole, simulated_spdt_switch_1_pole);
  or IC2_2 (IC2_2_out, simulated_spdt_switch_1_pole, simulated_spdt_switch_1_pole);
  or IC2_3 (IC2_3_out, simulated_spdt_switch_1_pole, simulated_spdt_switch_1_pole);
  or IC2_4 (IC2_4_out, simulated_spdt_switch_1_pole, simulated_spdt_switch_1_pole);
  or IC3 (IC3_out, simulated_spdt_switch_2_pole, simulated_spdt_switch_2_pole);
  or IC3_2 (IC3_2_out, simulated_spdt_switch_2_pole, simulated_spdt_switch_2_pole);
  or IC3_3 (IC3_3_out, simulated_spdt_switch_2_pole, simulated_spdt_switch_2_pole);
  or IC3_4 (IC3_4_out, simulated_spdt_switch_2_pole, simulated_spdt_switch_2_pole);
  or IC4 (IC4_out, simulated_spdt_switch_3_pole, simulated_spdt_switch_3_pole);
  or IC4_2 (IC4_2_out, simulated_spdt_switch_3_pole, simulated_spdt_switch_3_pole);
  or IC4_3 (IC4_3_out, simulated_spdt_switch_3_pole, simulated_spdt_switch_3_pole);
  or IC4_4 (IC4_4_out, simulated_spdt_switch_3_pole, simulated_spdt_switch_3_pole);
  or IC5 (IC5_out, simulated_spdt_switch_4_pole, simulated_spdt_switch_4_pole);
  or IC5_2 (IC5_2_out, simulated_spdt_switch_4_pole, simulated_spdt_switch_4_pole);
  or IC5_3 (IC5_3_out, simulated_spdt_switch_4_pole, simulated_spdt_switch_4_pole);
  or IC5_4 (IC5_4_out, simulated_spdt_switch_4_pole, simulated_spdt_switch_4_pole);
  or IC6 (IC6_out, IC2_out, IC2_2_out);
  or IC6_2 (IC6_2_out, IC2_3_out, IC2_4_out);
  or IC6_3 (IC6_3_out, IC3_out, IC3_2_out);
  or IC6_4 (IC6_4_out, IC3_3_out, IC3_4_out);
  or IC7 (IC7_out, IC4_out, IC4_2_out);
  or IC7_2 (IC7_2_out, IC4_3_out, IC4_4_out);
  or IC7_3 (IC7_3_out, IC5_out, IC5_2_out);
  or IC7_4 (IC7_4_out, IC5_3_out, IC5_4_out);
  or IC8 (IC8_out, IC6_out, IC6_2_out);
  or IC8_2 (IC8_2_out, IC6_3_out, IC6_4_out);
  or IC8_3 (IC8_3_out, IC7_out, IC7_2_out);
  or IC8_4 (IC8_4_out, IC7_3_out, IC7_4_out);
  or IC9 (IC9_out, IC8_out, IC8_2_out);
  or IC9_2 (IC9_2_out, IC8_3_out, IC8_4_out);
  Pull_Resistor #(.pull(1)) pull_resistor_1 ();  // open: node
  LED #(.active("false")) led_1 (.in(IC9_3_out));
  or IC9_3 (IC9_3_out, IC9_out, IC9_2_out);
  Pull_Resistor #(.pull(1)) pull_resistor_2 ();  // open: node
  LED #(.active("false")) led_2 (.in(nand_2_out));
  nand nand_2 (nand_2_out, IC9_3_out, IC9_3_out);

  // Notes on the sheet:
  //   DIP switch
  //   1
  //   15
  //   16
  //   top to bottom on board
  //   left = "1" position
  //   3
  //   14
  //   13
  //   5
  //   12
  //   11
  //   7
  //   10
  //   9
  //   1
  //   2
  //   4
  //   5
  //   13
  //   12
  //   10
  //   9
  //   1
  //   2
  //   4
  //   5
  //   13
  //   12
  //   10
  //   9
  //   1
  //   2
  //   4
  //   5
  //   13
  //   12
  //   10
  //   9
  //   1
  //   2
  //   4
  //   5
  //   13
  //   12
  //   10
  //   9
  //   IC2-9: 74S32
  //   14
  //   3
  //   6
  //   11
  //   8
  //   7
  //   14
  //   3
  //   6
  //   11
  //   8
  //   7
  //   14
  //   3
  //   6
  //   11
  //   8
  //   7
  //   14
  //   3
  //   6
  //   11
  //   8
  //   7
  //   14
  //   1
  //   3
  //   2
  //   4
  //   6
  //   5
  //   13
  //   11
  //   12
  //   10
  //   8
  //   9
  //   7
  //   14
  //   1
  //   3
  //   2
  //   4
  //   6
  //   5
  //   13
  //   11
  //   12
  //   10
  //   8
  //   9
  //   7
  //   14
  //   1
  //   2
  //   4
  //   5
  //   13
  //   12
  //   10
  //   9
  //   7
  //   3
  //   14
  //   1
  //   2
  //   6
  //   11
  //   4
  //   5
  //   8
  //   3
  //   10
  //   9
  //   7
  //   6
  //   "0"
  //   8
  //   "1"
endmodule

module nand_demo (
  input  sim_control,
  input  sim_control_2
);

  wire nand_1_out, nand_2_out, nand_3_out, pull_resistor_1_node, simulated_spdt_switch_1_pole,
       simulated_spdt_switch_2_pole;

  Pull_Resistor #(.pull(1)) pull_resistor_1 (.node(pull_resistor_1_node));
  Pull_Resistor #(.pull(1)) pull_resistor_2 ();  // open: node
  LED #(.active("false")) led_1 (.in(simulated_spdt_switch_1_pole));
  simulated_SPDT_switch simulated_spdt_switch_1 (
    .throw1(pull_resistor_1_node), .throw0(1'b0), .pole(simulated_spdt_switch_1_pole), .control(sim_control));
  simulated_SPDT_switch simulated_spdt_switch_2 (
    .throw1(pull_resistor_1_node), .throw0(1'b0), .pole(simulated_spdt_switch_2_pole), .control(sim_control_2));
  Pull_Resistor #(.pull(1)) pull_resistor_3 ();  // open: node
  LED #(.active("false")) led_2 (.in(simulated_spdt_switch_2_pole));
  Pull_Resistor #(.pull(1)) pull_resistor_4 ();  // open: node
  LED #(.active("false")) led_3 (.in(nand_1_out));
  nand nand_1 (nand_1_out, simulated_spdt_switch_1_pole, simulated_spdt_switch_2_pole);
  Pull_Resistor #(.pull(1)) pull_resistor_5 ();  // open: node
  LED #(.active("false")) led_4 (.in(nand_2_out));
  nand nand_2 (nand_2_out, nand_1_out, nand_1_out);
  nand nand_3 (nand_3_out, nand_2_out, nand_2_out);

  // Notes on the sheet:
  //   "0"
  //   "0"
  //   4
  //   5
  //   14
  //   1
  //   3
  //   2
  //   7
  //   IC1: 74LS00
  //   "0"
  //   "1"
  //   9
  //   6
  //   10
  //   8
endmodule

module simulated_SPDT_switch (
  input  throw1,
  input  throw0,
  input  control,
  output pole
);

  Transistor #(.\type ("n"), .gate("br")) transistor_1 (.in(throw1), .out(pole), .gate(control));
  Transistor transistor_2 (.in(throw0), .out(pole), .gate(control));
endmodule
