// Logisim project rs.circ as structural Verilog: 1 circuit, main circuit main
module main (
  input  in_1,
  input  in_2,
  output out_3,
  output out_4,
  output out_5,
  output out_6
);

  nand nand_1 (out_4, in_1, out_5);
  nand nand_2 (out_5, out_4, in_2);

  assign out_3 = in_1;
  assign out_6 = in_2;
endmodule
