// Logisim project tran-gates-full-buffers.circ as structural Verilog: 4 circuits, main circuit not
module \not  (
  input  in_1,
  output out_2,
  output out_3,
  output out_4
);

  Transistor transistor_1 (.in(1'b1), .out(out_2), .gate(in_1));
  buf buffer_1 (out_3, out_2);
  buf buffer_2 (out_3, out_4);
  Transistor #(.\type ("n")) transistor_2 (.in(1'b0), .out(out_4), .gate(in_1));

  // Notes on the sheet:
  //   closes when input is 0---sending the 1 through to the output
  //   closes when input is 1---sending the zero through to the output
endmodule

module \nor  (
  input  in_1,
  input  in_2,
  output out_3,
  output out_4,
  output out_5,
  output out_6,
  output out_7
);

  wire buffer_1_out;

  Transistor transistor_1 (.in(1'b1), .out(out_3), .gate(in_1));
  buf buffer_1 (buffer_1_out, out_3);
  Transistor transistor_2 (.in(buffer_1_out), .out(out_4), .gate(in_2));
  buf buffer_2 (out_5, out_4);
  buf buffer_3 (out_5, out_6);
  Transistor #(.\type ("n")) transistor_3 (.in(1'b0), .out(out_6), .gate(in_1));
  buf buffer_4 (out_5, out_7);
  Transistor #(.\type ("n")) transistor_4 (.in(1'b0), .out(out_7), .gate(in_2));

  // Notes on the sheet:
  //   When BOTH inputs are 0, send the 1 to the output
  //   When either input is 1, send the 0 to the output
endmodule

module \nand  (
  input  in_1,
  input  in_2,
  output out_3,
  output out_4,
  output out_5,
  output out_6,
  output out_7
);

  wire buffer_3_out;

  Transistor transistor_1 (.in(1'b1), .out(out_3), .gate(in_1));
  buf buffer_1 (out_5, out_3);
  buf buffer_2 (out_5, out_6);
  Transistor #(.\type ("n")) transistor_2 (.in(buffer_3_out), .out(out_6), .gate(in_1));
  buf buffer_3 (buffer_3_out, out_7);
  Transistor #(.\type ("n")) transistor_3 (.in(1'b0), .out(out_7), .gate(in_2));
  Transistor transistor_4 (.in(1'b1), .out(out_4), .gate(in_2));
  buf buffer_4 (out_5, out_4);

  // Notes on the sheet:
  //   When BOTH inputs are 1, send the 0 to the output
  //   When either input is 0, send the 1 to the output
endmodule

module diode_and (
  input  in_1,
  input  in_2,
  output out_3,
  output out_4,
  output out_5
);

  diode diode_1 (._0_1_in(in_1), ._0_Z_out(out_3));
  diode diode_2 (._0_1_in(in_2), ._0_Z_out(out_5));
  Pull_Resistor #(.pull(1)) pull_resistor_1 (.node(out_4));
  buf buffer_1 (out_4, out_3);
  buf buffer_2 (out_4, out_5);

  // Notes on the sheet:
  //   (This uses my simulated diode, in diode.circ)
endmodule
