// Logisim project tran-gates.circ as structural Verilog: 5 circuits, main circuit cmos
module \cmos  (
  input  in_1,
  output out_2,
  output out_3,
  output out_4
);

  Transistor transistor_1 (.in(1'b1), .out(out_2), .gate(in_1));
  Transistor #(.\type ("n")) transistor_2 (.in(1'b0), .out(out_4), .gate(in_1));
endmodule

module \not  (
  input  in_1,
  output out_2,
  output out_3,
  output out_4
);

  Transistor transistor_1 (.in(1'b1), .out(out_2), .gate(in_1));
  Transistor #(.\type ("n")) transistor_2 (.in(1'b0), .out(out_4), .gate(in_1));
endmodule

module \nor  (
  input  in_1,
  input  in_2,
  output out_3,
  output out_4,
  output out_5,
  output out_6,
  output out_7
);

  Transistor transistor_1 (.in(1'b1), .out(out_3), .gate(in_1));
  Transistor transistor_2 (.out(out_4), .gate(in_2));  // open: in
  Transistor #(.\type ("n")) transistor_3 (.out(out_6), .gate(in_1));  // open: in
  Transistor #(.\type ("n")) transistor_4 (.in(1'b0), .out(out_7), .gate(in_2));
endmodule

module \nand  (
  input  in_1,
  input  in_2,
  output out_3,
  output out_4,
  output out_5,
  output out_6,
  output out_7
);

  Transistor transistor_1 (.in(1'b1), .out(out_3), .gate(in_1));
  Transistor transistor_2 (.out(out_4), .gate(in_2));  // open: in
  Transistor #(.\type ("n")) transistor_3 (.out(out_6), .gate(in_1));  // open: in
  Transistor #(.\type ("n")) transistor_4 (.in(1'b0), .out(out_7), .gate(in_2));
endmodule

module diode_and (
  input  in_1,
  input  in_2,
  output out_3
);

  wire diode_1__0_z_out, diode_2__0_z_out;

  diode diode_1 (._0_1_in(in_1), ._0_Z_out(diode_1__0_z_out));
  diode diode_2 (._0_1_in(in_2), ._0_Z_out(diode_2__0_z_out));
  Pull_Resistor #(.pull(1)) pull_resistor_1 ();  // open: node
endmodule
