// Logisim project 4adder-blank.circ as structural Verilog: 2 circuits, main circuit main
module main (
  input  [3:0] in_1,
  input  [3:0] in_2
);

  wire and_1_out, full_adder_1_c_out, full_adder_1_q, undriven, undriven_2, undriven_3, undriven_4,
       undriven_5, undriven_6, xor_1_out;
  wire [0:0] undriven_7;
  wire [3:0] undriven_8;

  Hex_Digit_Display hex_digit_display_1 (.value(in_1));  // open: dp
  Hex_Digit_Display hex_digit_display_2 (.value(in_2));  // open: dp
  and and_1 (and_1_out, undriven, undriven_2);
  xor xor_1 (xor_1_out, undriven_2, undriven);
  full_adder full_adder_1 (.C_in(undriven_3), .C_out(full_adder_1_c_out), .Q(full_adder_1_q));  // open: A, B
  full_adder full_adder_2 (.C_in(undriven_5), .B(undriven_4));  // open: A, C_out, Q
  full_adder full_adder_3 (.C_in(undriven_6));  // open: A, B, C_out, Q
  Hex_Digit_Display hex_digit_display_3 (.value({3'b000, undriven_7[0]}));  // open: dp
  Hex_Digit_Display hex_digit_display_4 (.value(undriven_8));  // open: dp
endmodule

module full_adder (
  input  C_in,
  input  A,
  input  B,
  output C_out,
  output Q
);

  wire decoder_1_out0, decoder_1_out1, decoder_1_out2, decoder_1_out3, decoder_1_out4, decoder_1_out5,
       decoder_1_out6, decoder_1_out7;

  Decoder #(.select(3), .enable("false")) decoder_1 (
    .out0(decoder_1_out0), .out1(decoder_1_out1), .out2(decoder_1_out2), .out3(decoder_1_out3),
    .out4(decoder_1_out4), .out5(decoder_1_out5), .out6(decoder_1_out6), .out7(decoder_1_out7),
    .sel({C_in, A, B}));
  or or_1 (C_out, decoder_1_out3, decoder_1_out5, decoder_1_out6, decoder_1_out7, 1'b0);
  or or_2 (Q, decoder_1_out2, decoder_1_out4, decoder_1_out1, decoder_1_out7, 1'b0);

  // Notes on the sheet:
  //   000
  //   001
  //   011
  //   010
  //   100
  //   110
  //   101
  //   111
  //   (1 if at least 2 inputs are 1)
  //   (1 if at exacty 1 input is, or if all three are)
endmodule
