// Logisim project 7seg-matrix.circ as structural Verilog: 1 circuit, main circuit main
module main (
  input  in_1,
  input  in_2,
  input  in_3,
  input  in_4,
  input  in_5,
  input  in_6,
  input  in_7,
  input  in_8,
  input  in_9,
  input  in_10
);

  wire decoder_1_out0, decoder_1_out1, decoder_1_out2, decoder_1_out3, decoder_1_out4, decoder_1_out5,
       decoder_1_out6, decoder_1_out7;

  Decoder #(.select(3), .enable("false")) decoder_1 (
    .out0(decoder_1_out0), .out1(decoder_1_out1), .out2(decoder_1_out2), .out3(decoder_1_out3),
    .out4(decoder_1_out4), .out5(decoder_1_out5), .out6(decoder_1_out6), .out7(decoder_1_out7),
    .sel({in_8, in_9, in_10}));
  _7_Segment_Display u_7_segment_display_1 (.g(1'b1));  // open: f, a, b, e, d, c, dp
  _7_Segment_Display u_7_segment_display_2 (.f(1'b1));  // open: g, a, b, e, d, c, dp
  _7_Segment_Display u_7_segment_display_3 (.b(1'b1));  // open: g, f, a, e, d, c, dp
  _7_Segment_Display u_7_segment_display_4 (.a(1'b1));  // open: g, f, b, e, d, c, dp
  _7_Segment_Display u_7_segment_display_5 (.c(1'b1));  // open: g, f, a, b, e, d, dp
  _7_Segment_Display u_7_segment_display_6 (.d(1'b1));  // open: g, f, a, b, e, c, dp
  _7_Segment_Display u_7_segment_display_7 (.e(1'b1));  // open: g, f, a, b, d, c, dp
  _7_Segment_Display u_7_segment_display_8 (
    .g(in_1), .f(in_2), .a(in_3), .b(in_4), .e(in_7), .d(in_6), .c(in_5));  // open: dp
endmodule
