// Logisim project decoder-somewhat-full.circ as structural Verilog: 1 circuit, main circuit main
module main (
  input  in_1,
  input  in_2,
  input  in_3,
  input  in_4,
  input  in_5,
  input  in_6,
  output recognizes__000,
  output recognizes__001,
  output recognizes__010,
  output recognizes__011
);

  wire and_5_out, and_6_out, decoder_1_out0, decoder_1_out7, not_1_out, not_2_out, not_3_out, not_4_out,
       not_5_out, not_6_out, not_7_out, not_8_out, or_1_out, undriven, undriven_2, undriven_3, undriven_4,
       undriven_5, undriven_6;

  not not_1 (not_1_out, in_1);
  not not_2 (not_2_out, in_2);
  not not_3 (not_3_out, in_3);
  not not_4 (not_4_out, in_1);
  not not_5 (not_5_out, in_2);
  not not_6 (not_6_out, in_1);
  not not_7 (not_7_out, in_3);
  not not_8 (not_8_out, in_1);
  and and_1 (recognizes__000, not_1_out, not_2_out, not_3_out);
  and and_2 (recognizes__001, not_4_out, not_5_out, in_3);
  and and_3 (recognizes__010, not_6_out, in_2, not_7_out);
  and and_4 (recognizes__011, not_8_out, in_2, in_3);
  and and_5 (and_5_out, ~undriven, ~undriven_2, ~undriven_3);  // AND_Gate
  and and_6 (and_6_out, ~undriven_4, ~undriven_5, undriven_6);  // AND_Gate
  Decoder #(.select(3), .enable("false")) decoder_1 (
    .out0(decoder_1_out0), .out7(decoder_1_out7), .sel({in_4, in_5, in_6}));  // open: out1, out2, out3, out4, out5, out6
  or or_1 (or_1_out, decoder_1_out0, decoder_1_out7);

  // Notes on the sheet:
  //   000
  //   001
  //   010
  //   011
  //   Etc.
  //   and so on, for 100 through 111
  //   And yes, we'd probably absorb the inverters into the AND inputs.   e.g.:
  //   a LogiSim splitter, taking
  //   three 1-bit wires to a 3-bit bundle
  //   LogiSim's baked-in version
  //   of the decoder on the left
  //   we can calculate an arbitrary binary
  //   function on k bits by sending the k bits
  //   into a decoder, and then OR-ing the outputs
  //   for the combos that should output 1
endmodule
