// Logisim project compare.circ as structural Verilog: 1 circuit, main circuit main
module main (
  input  in_1,
  input  in_2,
  input  in_3,
  input  in_4,
  input  in_5,
  input  in_6,
  input  in_7,
  input  in_8
);

  // Probe on {in_1, in_2, in_3, in_4}
  // Probe on {in_5, in_6, in_7, in_8}
  // Probe on nothing
endmodule
