// Logisim project demux.circ as structural Verilog: 1 circuit, main circuit main
module main (
  input  data_input,
  input  S2,
  input  in_3,
  input  S0,
  output Q0,
  output out_6,
  output out_7,
  output out_8,
  output out_9,
  output out_10,
  output out_11,
  output Q7
);

  wire decoder_1_out0, decoder_1_out1, decoder_1_out2, decoder_1_out3, decoder_1_out4, decoder_1_out5,
       decoder_1_out6, decoder_1_out7;

  Decoder #(.select(3), .enable("false")) decoder_1 (
    .out0(decoder_1_out0), .out1(decoder_1_out1), .out2(decoder_1_out2), .out3(decoder_1_out3),
    .out4(decoder_1_out4), .out5(decoder_1_out5), .out6(decoder_1_out6), .out7(decoder_1_out7),
    .sel({S2, in_3, S0}));

  // Notes on the sheet:
  //   control inputs
  //   data output
endmodule
