// Logisim project digits.circ as structural Verilog: 1 circuit, main circuit main
module main (
  input  in_1,
  input  in_2,
  input  in_3,
  input  in_4,
  input  in_5,
  input  in_6,
  input  in_7,
  input  in_8,
  input  in_9,
  input  in_10,
  input  in_11,
  input  in_12,
  input  in_13,
  input  in_14,
  input  in_15,
  input  in_16,
  input  in_17,
  input  in_18,
  input  in_19,
  input  in_20,
  input  in_21,
  input  in_22,
  input  in_23,
  input  in_24,
  input  in_25,
  input  in_26,
  input  in_27,
  input  in_28,
  input  in_29,
  input  in_30,
  input  in_31,
  input  in_32,
  input  in_33,
  input  in_34,
  input  in_35,
  input  in_36,
  input  in_37,
  input  in_38,
  input  in_39,
  input  in_40
);

  Hex_Digit_Display hex_digit_display_1 (.value({in_1, in_2, in_3, in_4}));  // open: dp
  Hex_Digit_Display hex_digit_display_2 (.value({in_21, in_22, in_23, in_24}));  // open: dp
  Hex_Digit_Display hex_digit_display_3 (.value({in_5, in_6, in_7, in_8}));  // open: dp
  Hex_Digit_Display hex_digit_display_4 (.value({in_25, in_26, in_27, in_28}));  // open: dp
  Hex_Digit_Display hex_digit_display_5 (.value({in_9, in_10, in_11, in_12}));  // open: dp
  Hex_Digit_Display hex_digit_display_6 (.value({in_29, in_30, in_31, in_32}));  // open: dp
  Hex_Digit_Display hex_digit_display_7 (.value({in_13, in_14, in_15, in_16}));  // open: dp
  Hex_Digit_Display hex_digit_display_8 (.value({in_33, in_34, in_35, in_36}));  // open: dp
  Hex_Digit_Display hex_digit_display_9 (.value({in_17, in_18, in_19, in_20}));  // open: dp
  Hex_Digit_Display hex_digit_display_10 (.value({in_37, in_38, in_39, in_40}));  // open: dp
endmodule
