// Logisim project drom.circ as structural Verilog: 4 circuits, main circuit diode
module main (
  input  in_1,
  input  in_2,
  input  in_3
);

  wire decoder_1_out0, decoder_1_out1, decoder_1_out2, decoder_1_out3, decoder_1_out4, decoder_1_out5,
       decoder_1_out6, decoder_1_out7, diode_1__0_z_out, not_1_out, not_2_out, not_3_out, not_4_out,
       not_5_out, not_6_out, not_7_out, not_8_out, pull_resistor_1_node, pull_resistor_2_node,
       pull_resistor_3_node, pull_resistor_4_node, pull_resistor_5_node, pull_resistor_6_node,
       pull_resistor_7_node, undriven;

  Decoder #(.select(3), .enable("false")) decoder_1 (
    .out0(decoder_1_out0), .out1(decoder_1_out1), .out2(decoder_1_out2), .out3(decoder_1_out3),
    .out4(decoder_1_out4), .out5(decoder_1_out5), .out6(decoder_1_out6), .out7(decoder_1_out7),
    .sel({in_1, in_2, in_3}));
  diode diode_1 (._0_1_in(undriven), ._0_Z_out(diode_1__0_z_out));
  _7_Segment_Display u_7_segment_display_1 (.g(1'b1));  // open: f, a, b, e, d, c, dp
  Pull_Resistor #(.pull(1)) pull_resistor_1 (.node(pull_resistor_1_node));
  not not_1 (not_1_out, decoder_1_out0);
  not not_2 (not_2_out, decoder_1_out1);
  not not_3 (not_3_out, decoder_1_out2);
  not not_4 (not_4_out, decoder_1_out3);
  not not_5 (not_5_out, decoder_1_out4);
  not not_6 (not_6_out, decoder_1_out5);
  not not_7 (not_7_out, decoder_1_out6);
  not not_8 (not_8_out, decoder_1_out7);
  _7_Segment_Display u_7_segment_display_2 (.f(1'b1));  // open: g, a, b, e, d, c, dp
  _7_Segment_Display u_7_segment_display_3 (.a(1'b1));  // open: g, f, b, e, d, c, dp
  Pull_Resistor #(.pull(1)) pull_resistor_2 (.node(pull_resistor_2_node));
  _7_Segment_Display u_7_segment_display_4 (.b(1'b1));  // open: g, f, a, e, d, c, dp
  Pull_Resistor #(.pull(1)) pull_resistor_3 (.node(pull_resistor_3_node));
  Pull_Resistor #(.pull(1)) pull_resistor_4 (.node(pull_resistor_4_node));
  _7_Segment_Display u_7_segment_display_5 (.c(1'b1));  // open: g, f, a, b, e, d, dp
  Pull_Resistor #(.pull(1)) pull_resistor_5 (.node(pull_resistor_5_node));
  _7_Segment_Display u_7_segment_display_6 (.e(1'b1));  // open: g, f, a, b, d, c, dp
  _7_Segment_Display u_7_segment_display_7 (.d(1'b1));  // open: g, f, a, b, e, c, dp
  Pull_Resistor #(.pull(1)) pull_resistor_6 (.node(pull_resistor_6_node));
  Pull_Resistor #(.pull(1)) pull_resistor_7 (.node(pull_resistor_7_node));
  _7_Segment_Display #(.active("false")) u_7_segment_display_8 (
    .g(pull_resistor_1_node), .f(pull_resistor_2_node), .a(pull_resistor_3_node), .b(pull_resistor_4_node),
    .e(pull_resistor_7_node), .d(pull_resistor_6_node), .c(pull_resistor_5_node));  // open: dp

  // Notes on the sheet:
  //   (changed
  //   to "active low")
  //   (changed
  //   to "active low")
endmodule

module _7seg (
  input  in_1,
  input  in_2,
  input  in_3,
  input  in_4,
  input  in_5,
  input  in_6,
  input  in_7,
  input  in_8,
  input  in_9,
  input  in_10
);

  Decoder #(.select(3), .enable("false")) decoder_1 (.sel({in_8, in_9, in_10}));  // open: out0, out1, out2, out3, out4, out5, out6, out7
  _7_Segment_Display u_7_segment_display_1 (
    .g(in_1), .f(in_2), .a(in_3), .b(in_4), .e(in_7), .d(in_6), .c(in_5));  // open: dp
endmodule

module diode_demo (
  input  in_1,
  output out_2,
  output out_3
);

  diode diode_1 (._0_1_in(in_1), ._0_Z_out(out_3));

  assign out_2 = in_1;

  // Notes on the sheet:
  //   (sws's rough logisim simulation of a diode.)
endmodule

module diode (
  input  _0_1_in,
  output _0_Z_out
);

  wire not_1_out, pull_resistor_1_node;

  Pull_Resistor #(.pull(1)) pull_resistor_1 (.node(pull_resistor_1_node));
  buf buffer_1 (pull_resistor_1_node, _0_1_in);
  assign _0_Z_out = not_1_out ? pull_resistor_1_node : 1'bz;  // Controlled_Buffer controlled_buffer_1
  not not_1 (not_1_out, pull_resistor_1_node);
endmodule
