// Logisim project full-add.circ as structural Verilog: 1 circuit, main circuit main
module main (
  input  C_in,
  input  A,
  input  B,
  output C_out,
  output Q
);

  wire decoder_1_out0, decoder_1_out1, decoder_1_out2, decoder_1_out3, decoder_1_out4, decoder_1_out5,
       decoder_1_out6, decoder_1_out7;

  Decoder #(.select(3), .enable("false")) decoder_1 (
    .out0(decoder_1_out0), .out1(decoder_1_out1), .out2(decoder_1_out2), .out3(decoder_1_out3),
    .out4(decoder_1_out4), .out5(decoder_1_out5), .out6(decoder_1_out6), .out7(decoder_1_out7),
    .sel({C_in, A, B}));

  // Notes on the sheet:
  //   000
  //   001
  //   011
  //   010
  //   100
  //   110
  //   101
  //   111
  //   (1 if at least 2 inputs are 1)
  //   (1 if at exacty 1 input is, or if all three are)
endmodule
