// Logisim project mux.circ as structural Verilog: 1 circuit, main circuit main
module main (
  input  _111,
  input  _110,
  input  _101,
  input  _100,
  input  _011,
  input  _010,
  input  _001,
  input  _000,
  input  S2,
  input  in_10,
  input  S0,
  output data_output
);

  wire and_1_out, and_2_out, and_3_out, and_4_out, and_5_out, and_6_out, and_7_out, and_8_out,
       decoder_1_out0, decoder_1_out1, decoder_1_out2, decoder_1_out3, decoder_1_out4, decoder_1_out5,
       decoder_1_out6, decoder_1_out7;

  Decoder #(.select(3), .enable("false")) decoder_1 (
    .out0(decoder_1_out0), .out1(decoder_1_out1), .out2(decoder_1_out2), .out3(decoder_1_out3),
    .out4(decoder_1_out4), .out5(decoder_1_out5), .out6(decoder_1_out6), .out7(decoder_1_out7),
    .sel({S2, in_10, S0}));
  and and_1 (and_1_out, _111, decoder_1_out7);
  and and_2 (and_2_out, _110, decoder_1_out6);
  and and_3 (and_3_out, _101, decoder_1_out5);
  and and_4 (and_4_out, _100, decoder_1_out4);
  and and_5 (and_5_out, _011, decoder_1_out3);
  and and_6 (and_6_out, _010, decoder_1_out2);
  and and_7 (and_7_out, _001, decoder_1_out1);
  and and_8 (and_8_out, _000, decoder_1_out0);
  or or_1 (data_output, and_1_out, and_2_out, and_3_out, and_4_out, and_5_out, and_6_out, and_7_out, and_8_out);

  // Notes on the sheet:
  //   data inputs
  //   control inputs
endmodule
