// Logisim project 4bitR.circ as structural Verilog: 1 circuit, main circuit main
module main (
  input  in_1,
  input  [3:0] in_2,
  output out_3
);

  wire [3:0] d_ff_4_q;

  Hex_Digit_Display hex_digit_display_1 (.value(in_2));  // open: dp
  Button button_1 (.out(out_3));
  D_Flip_Flop #(.trigger("high")) d_ff_1 (
    .clk(in_1), .D(in_2[3]), .Q(d_ff_4_q[3]), .preset(1'b0), .en(1'b1), .reset(out_3));  // open: Qn
  D_Flip_Flop #(.trigger("high")) d_ff_2 (
    .clk(in_1), .D(in_2[2]), .Q(d_ff_4_q[2]), .preset(1'b0), .en(1'b1), .reset(out_3));  // open: Qn
  D_Flip_Flop #(.trigger("high")) d_ff_3 (
    .clk(in_1), .D(in_2[1]), .Q(d_ff_4_q[1]), .preset(1'b0), .en(1'b1), .reset(out_3));  // open: Qn
  D_Flip_Flop #(.trigger("high")) d_ff_4 (
    .clk(in_1), .D(in_2[0]), .Q(d_ff_4_q[0]), .preset(1'b0), .en(1'b1), .reset(out_3));  // open: Qn
  Hex_Digit_Display hex_digit_display_2 (.value(d_ff_4_q));  // open: dp

  // Notes on the sheet:
  //   clock (high-level trigger)
  //   data
  //   reset (active high)
  //   1-bit level-triggered D "flip-flops"
  //   (but what everyone else calls "latches")
  //   Q
endmodule
