// Logisim project bus.circ as structural Verilog: 8 circuits, main circuit full-v2-smaller
module full_v2_smaller (
  input  [15:0] width_16,
  input  [15:0] in_2,
  input  write_from_input,
  input  R_W,
  input  M_EN,
  input  clk,
  input  read_r0,
  input  write_r0,
  input  read_r0_2,
  input  write_r1
);

  wire and_1_out, and_2_out, comparator_1_eq;
  wire [9:0] bit_extender_1_out;
  wire [15:0] _16_out, controlled_buffer_1_out, high_level_2_q, high_level_q, ram_1_data;

  assign controlled_buffer_1_out = write_from_input ? in_2 : 16'bz;  // Controlled_Buffer controlled_buffer_1
  // Probe on width_16
  // Probe on controlled_buffer_1_out
  // Probe on R_W
  Bit_Extender #(.in_width(16), .out_width(10)) bit_extender_1 (.in(width_16), .out(bit_extender_1_out));
  assign _16_out = width_16 & 16'hfc00;  // AND_Gate _16, 16 bits wide
  // Probe on high_level_q
  Register #(.width(16), .trigger("high")) high_level (
    .D(controlled_buffer_1_out), .Q(high_level_q), .clk(write_r0));  // open: en, clr
  // Probe on high_level_2_q
  Register #(.width(16), .trigger("high")) high_level_2 (
    .D(controlled_buffer_1_out), .Q(high_level_2_q), .clk(write_r1));  // open: en, clr
  // Probe on bit_extender_1_out
  Comparator #(.width(16)) comparator_1 (.a(_16_out), .b(16'h400), .eq(comparator_1_eq));  // open: gt, lt
  assign controlled_buffer_1_out = read_r0 ? high_level_q : 16'bz;  // Controlled_Buffer controlled_buffer_2
  assign controlled_buffer_1_out = read_r0_2 ? high_level_2_q : 16'bz;  // Controlled_Buffer controlled_buffer_3
  and and_1 (and_1_out, comparator_1_eq, M_EN);
  // Probe on ram_1_data
  RAM #(.addrWidth(10), .dataWidth(16), .bus("separate")) ram_1 (
    .addr(bit_extender_1_out), .din(controlled_buffer_1_out), .data(ram_1_data), .sel(and_1_out), .clk(clk));  // open: str, ld, clr
  and and_2 (and_2_out, ~R_W, M_EN, comparator_1_eq);  // AND_Gate
  assign controlled_buffer_1_out = and_2_out ? ram_1_data : 16'bz;  // Controlled_Buffer controlled_buffer_4

  // Notes on the sheet:
  //   address
  //   data in
  //   address bus
  //   data bus
  //   control bus
  //   fan-out 16, 12 in
  //   width 10
  //   width 16
  //   (RAM component: 1024 x 16))
  //   width 16
  //   data out
endmodule

module full_v2 (
  input  [15:0] width_16,
  input  [15:0] in_2,
  input  write_from_input,
  input  R_W,
  input  M_EN,
  input  clk,
  input  read_r0,
  input  write_r0,
  input  read_r0_2,
  input  write_r1
);

  wire and_1_out, and_2_out, and_3_out, and_4_out, comparator_1_eq, comparator_2_eq;
  wire [9:0] bit_extender_1_out, bit_extender_2_out;
  wire [15:0] _16_2_out, _16_out, controlled_buffer_1_out, high_level_2_q, high_level_q, ram_1_data,
       ram_2_data;

  assign controlled_buffer_1_out = write_from_input ? in_2 : 16'bz;  // Controlled_Buffer controlled_buffer_1
  // Probe on width_16
  // Probe on controlled_buffer_1_out
  // Probe on R_W
  Bit_Extender #(.in_width(16), .out_width(10)) bit_extender_1 (.in(width_16), .out(bit_extender_1_out));
  assign _16_out = width_16 & 16'hfc00;  // AND_Gate _16, 16 bits wide
  // Probe on high_level_q
  Register #(.width(16), .trigger("high")) high_level (
    .D(controlled_buffer_1_out), .Q(high_level_q), .clk(write_r0));  // open: en, clr
  // Probe on high_level_2_q
  Register #(.width(16), .trigger("high")) high_level_2 (
    .D(controlled_buffer_1_out), .Q(high_level_2_q), .clk(write_r1));  // open: en, clr
  // Probe on bit_extender_1_out
  Comparator #(.width(16)) comparator_1 (.a(_16_out), .b(16'h400), .eq(comparator_1_eq));  // open: gt, lt
  assign controlled_buffer_1_out = read_r0 ? high_level_q : 16'bz;  // Controlled_Buffer controlled_buffer_2
  assign controlled_buffer_1_out = read_r0_2 ? high_level_2_q : 16'bz;  // Controlled_Buffer controlled_buffer_3
  and and_1 (and_1_out, comparator_1_eq, M_EN, R_W);
  RAM #(.addrWidth(10), .dataWidth(16), .bus("separate")) ram_1 (
    .addr(bit_extender_1_out), .din(controlled_buffer_1_out), .data(ram_1_data), .sel(and_1_out), .clk(clk));  // open: str, ld, clr
  // Probe on ram_1_data
  and and_2 (and_2_out, ~R_W, M_EN, comparator_1_eq);  // AND_Gate
  assign controlled_buffer_1_out = and_2_out ? ram_1_data : 16'bz;  // Controlled_Buffer controlled_buffer_4
  // Probe on bit_extender_2_out
  Bit_Extender #(.in_width(16), .out_width(10)) bit_extender_2 (.in(width_16), .out(bit_extender_2_out));
  assign _16_2_out = width_16 & 16'hfc00;  // AND_Gate _16_2, 16 bits wide
  Comparator #(.width(16)) comparator_2 (.a(_16_2_out), .b(16'h500), .eq(comparator_2_eq));  // open: gt, lt
  and and_3 (and_3_out, comparator_2_eq, M_EN, R_W);
  RAM #(.addrWidth(10), .dataWidth(16), .bus("separate")) ram_2 (
    .addr(bit_extender_2_out), .din(controlled_buffer_1_out), .data(ram_2_data), .sel(and_3_out), .clk(clk));  // open: str, ld, clr
  and and_4 (and_4_out, ~R_W, M_EN, comparator_2_eq);  // AND_Gate
  assign controlled_buffer_1_out = and_4_out ? ram_2_data : 16'bz;  // Controlled_Buffer controlled_buffer_5
  // Probe on ram_2_data

  // Notes on the sheet:
  //   address
  //   data in
  //   address bus
  //   data bus
  //   control bus
  //   fan-out 16, 12 in
  //   width 10
  //   width 16
  //   (RAM component: 1024 x 16))
  //   width 16
  //   data out
  //   fan-out 16, 12 in
  //   width 10
  //   width 16
  //   (RAM component: 1024 x 16))
  //   width 16
  //   data out
endmodule

module regfile (
  input  write_r0,
  input  write_r1
);

  wire [15:0] high_level_2_q, high_level_q, undriven;

  // Probe on high_level_q
  Register #(.width(16), .trigger("high")) high_level (
    .D(undriven), .Q(high_level_q), .clk(write_r0));  // open: en, clr
  // Probe on high_level_2_q
  Register #(.width(16), .trigger("high")) high_level_2 (
    .D(undriven), .Q(high_level_2_q), .clk(write_r1));  // open: en, clr
endmodule

module _2_ram_chips_v2 (
  input  [15:0] width_16,
  input  [15:0] in_2,
  input  R_W,
  input  M_EN,
  input  clk
);

  wire and_1_out, and_2_out, and_3_out, and_4_out, comparator_1_eq, comparator_2_eq;
  wire [9:0] bit_extender_1_out, bit_extender_2_out;
  wire [15:0] _16_2_out, _16_out, controlled_buffer_1_out, ram_1_data, ram_2_data;

  assign controlled_buffer_1_out = R_W ? in_2 : 16'bz;  // Controlled_Buffer controlled_buffer_1
  // Probe on width_16
  // Probe on controlled_buffer_1_out
  // Probe on R_W
  Bit_Extender #(.in_width(16), .out_width(10)) bit_extender_1 (.in(width_16), .out(bit_extender_1_out));
  assign _16_out = width_16 & 16'hfc00;  // AND_Gate _16, 16 bits wide
  // Probe on bit_extender_1_out
  Comparator #(.width(16)) comparator_1 (.a(_16_out), .b(16'h400), .eq(comparator_1_eq));  // open: gt, lt
  and and_1 (and_1_out, comparator_1_eq, M_EN, R_W);
  // Probe on ram_1_data
  RAM #(.addrWidth(10), .dataWidth(16), .bus("separate")) ram_1 (
    .addr(bit_extender_1_out), .din(controlled_buffer_1_out), .data(ram_1_data), .sel(and_1_out), .clk(clk));  // open: str, ld, clr
  and and_2 (and_2_out, ~R_W, M_EN, comparator_1_eq);  // AND_Gate
  assign controlled_buffer_1_out = and_2_out ? ram_1_data : 16'bz;  // Controlled_Buffer controlled_buffer_2
  // Probe on bit_extender_2_out
  Bit_Extender #(.in_width(16), .out_width(10)) bit_extender_2 (.in(width_16), .out(bit_extender_2_out));
  assign _16_2_out = width_16 & 16'hfc00;  // AND_Gate _16_2, 16 bits wide
  Comparator #(.width(16)) comparator_2 (.a(_16_2_out), .b(16'h500), .eq(comparator_2_eq));  // open: gt, lt
  and and_3 (and_3_out, comparator_2_eq, M_EN, R_W);
  RAM #(.addrWidth(10), .dataWidth(16), .bus("separate")) ram_2 (
    .addr(bit_extender_2_out), .din(controlled_buffer_1_out), .data(ram_2_data), .sel(and_3_out), .clk(clk));  // open: str, ld, clr
  and and_4 (and_4_out, ~R_W, M_EN, comparator_2_eq);  // AND_Gate
  assign controlled_buffer_1_out = and_4_out ? ram_2_data : 16'bz;  // Controlled_Buffer controlled_buffer_3
  // Probe on ram_2_data

  // Notes on the sheet:
  //   address
  //   data in
  //   address bus
  //   data bus
  //   control bus
  //   fan-out 16, 12 in
  //   width 10
  //   width 16
  //   (RAM component: 1024 x 16))
  //   width 16
  //   data out
  //   fan-out 16, 12 in
  //   width 10
  //   width 16
  //   (RAM component: 1024 x 16))
  //   width 16
  //   data out
endmodule

module _2_ram_chips_v1 (
  input  [15:0] width_16,
  input  [15:0] in_2,
  input  R_W,
  input  M_EN,
  input  clk
);

  wire and_1_out, and_2_out, and_3_out, and_4_out, nor_1_out, nor_2_out;
  wire [15:0] controlled_buffer_1_out, ram_1_data, ram_2_data;

  assign controlled_buffer_1_out = R_W ? in_2 : 16'bz;  // Controlled_Buffer controlled_buffer_1
  // Probe on width_16
  // Probe on controlled_buffer_1_out
  // Probe on R_W
  nor nor_1 (nor_1_out, width_16[15], width_16[14], width_16[13], width_16[12], width_16[11], width_16[10]);
  // Probe on width_16[9:0]
  and and_1 (and_1_out, nor_1_out, M_EN, R_W);
  RAM #(.addrWidth(10), .dataWidth(16), .bus("separate")) ram_1 (
    .addr(width_16[9:0]), .din(controlled_buffer_1_out), .data(ram_1_data), .sel(and_1_out), .clk(clk));  // open: str, ld, clr
  // Probe on ram_1_data
  and and_2 (and_2_out, ~R_W, M_EN, nor_1_out);  // AND_Gate
  assign controlled_buffer_1_out = and_2_out ? ram_1_data : 16'bz;  // Controlled_Buffer controlled_buffer_2
  nor nor_2 (nor_2_out, width_16[15], width_16[14], width_16[13], width_16[12], width_16[11], ~width_16[10]);  // NOR_Gate
  // Probe on width_16[9:0]
  and and_3 (and_3_out, nor_2_out, M_EN, R_W);
  RAM #(.addrWidth(10), .dataWidth(16), .bus("separate")) ram_2 (
    .addr(width_16[9:0]), .din(controlled_buffer_1_out), .data(ram_2_data), .sel(and_3_out), .clk(clk));  // open: str, ld, clr
  and and_4 (and_4_out, ~R_W, M_EN, nor_2_out);  // AND_Gate
  assign controlled_buffer_1_out = and_4_out ? ram_2_data : 16'bz;  // Controlled_Buffer controlled_buffer_3
  // Probe on ram_2_data

  // Notes on the sheet:
  //   address
  //   data in
  //   address bus
  //   data bus
  //   control bus
  //   fan-out 16, 12 in
  //   width 10
  //   width 16
  //   (RAM component: 1024 x 16))
  //   width 16
  //   data out
  //   fan-out 16, 12 in
  //   width 10
  //   width 16
  //   (RAM component: 1024 x 16))
  //   width 16
  //   data out
endmodule

module _2_ram_chips_v0 (
  input  [15:0] width_16,
  input  [15:0] in_2
);

  wire button_1_out;

  Button button_1 (.out(button_1_out));
  // Probe on width_16[9:0]
  // Probe on in_2
  RAM #(.addrWidth(10), .dataWidth(16), .bus("separate")) ram_1 (
    .addr(width_16[9:0]), .din(in_2), .data(in_2), .clk(button_1_out));  // open: str, sel, ld, clr
  // Probe on in_2
  // Probe on width_16[9:0]
  RAM #(.addrWidth(10), .dataWidth(16), .bus("separate")) ram_2 (
    .addr(width_16[9:0]), .din(in_2), .data(in_2), .clk(button_1_out));  // open: str, sel, ld, clr
  // Probe on in_2

  // Notes on the sheet:
  //   address
  //   data in
  //   fan-out 16, 16 in
  //   address bus
  //   data bus
  //   control bus
  //   fan-out 16, 12 in
  //   width 10
  //   width 16
  //   (RAM component: 1024 x 16))
  //   width 16
  //   data out
  //   fan-out 16, 12 in
  //   width 10
  //   width 16
  //   (RAM component: 1024 x 16))
  //   width 16
  //   data out
endmodule

module ramchip_16bit_addr (
  input  [15:0] width_16,
  input  [15:0] in_2
);

  wire button_1_out;
  wire [15:0] ram_1_data;

  Button button_1 (.out(button_1_out));
  // Probe on width_16[9:0]
  // Probe on in_2
  RAM #(.addrWidth(10), .dataWidth(16), .bus("separate")) ram_1 (
    .addr(width_16[9:0]), .din(in_2), .data(ram_1_data), .clk(button_1_out));  // open: str, sel, ld, clr
  // Probe on ram_1_data

  // Notes on the sheet:
  //   address
  //   data in
  //   fan-out 16, 16 in
  //   address bus
  //   data bus
  //   control bus
  //   fan-out 16, 12 in
  //   width 10
  //   width 16
  //   (RAM component: 1024 x 16))
  //   width 16
  //   data out
endmodule

module ramchip_10bit_addr (
  input  [9:0] in_1,
  input  [15:0] in_2
);

  wire button_1_out;
  wire [15:0] ram_1_data;

  // Probe on in_1
  // Probe on in_2
  Button button_1 (.out(button_1_out));
  RAM #(.addrWidth(10), .dataWidth(16), .bus("separate")) ram_1 (
    .addr(in_1), .din(in_2), .data(ram_1_data), .clk(button_1_out));  // open: str, sel, ld, clr
  // Probe on ram_1_data

  // Notes on the sheet:
  //   address
  //   data in
  //   width 10
  //   width 16
  //   (RAM component: 1024 x 16))
  //   width 16
  //   data out
endmodule
