// Logisim project clocks.circ as structural Verilog
module clock6_full (
  output out_1
);

  wire clock_1_out, rising_edge_2_qn, rising_edge_3_qn, rising_edge_4_qn, rising_edge_qn;
  wire [3:0] rising_edge_q;

  // Probe on clock_1_out
  Clock clock_1 (.out(clock_1_out));
  LED led_1 (.in(rising_edge_q[0]));
  D_Flip_Flop rising_edge (
    .clk(clock_1_out), .D(rising_edge_qn), .Q(rising_edge_q[0]), .Qn(rising_edge_qn), .preset(1'b0),
    .en(1'b1), .reset(out_1));
  LED led_2 (.in(rising_edge_qn));
  D_Flip_Flop rising_edge_2 (
    .clk(rising_edge_qn), .D(rising_edge_2_qn), .Q(rising_edge_q[1]), .Qn(rising_edge_2_qn), .preset(1'b0),
    .en(1'b1), .reset(out_1));
  // Probe on rising_edge_q
  LED led_3 (.in(rising_edge_q[1]));
  LED led_4 (.in(rising_edge_2_qn));
  LED led_5 (.in(rising_edge_q[2]));
  D_Flip_Flop rising_edge_3 (
    .clk(rising_edge_2_qn), .D(rising_edge_3_qn), .Q(rising_edge_q[2]), .Qn(rising_edge_3_qn), .preset(1'b0),
    .en(1'b1), .reset(out_1));
  LED led_6 (.in(rising_edge_3_qn));
  D_Flip_Flop rising_edge_4 (
    .clk(rising_edge_3_qn), .D(rising_edge_4_qn), .Q(rising_edge_q[3]), .Qn(rising_edge_4_qn), .preset(1'b0),
    .en(1'b1), .reset(out_1));
  LED led_7 (.in(rising_edge_q[3]));
  LED led_8 (.in(rising_edge_4_qn));
  Hex_Digit_Display hex_digit_display_1 (.value(rising_edge_q));  // open: dp
  and and_1 (out_1, rising_edge_q[3], ~rising_edge_q[2], rising_edge_q[1], ~rising_edge_q[0]);  // AND_Gate

  // Notes on the sheet:
  //   clk
  //   Q0
  //   Q1
  //   Q2
  //   (LEDS light on 0)
  //   Q3
endmodule

module clock6_skeleton (
);

  wire clock_1_out, rising_edge_2_qn, rising_edge_3_qn, rising_edge_4_qn, rising_edge_qn;
  wire [3:0] rising_edge_q;

  // Probe on clock_1_out
  Clock clock_1 (.out(clock_1_out));
  LED led_1 (.in(rising_edge_q[0]));
  D_Flip_Flop rising_edge (
    .clk(clock_1_out), .D(rising_edge_qn), .Q(rising_edge_q[0]), .Qn(rising_edge_qn), .preset(1'b0),
    .en(1'b1), .reset(1'b0));
  LED led_2 (.in(rising_edge_qn));
  D_Flip_Flop rising_edge_2 (
    .clk(rising_edge_qn), .D(rising_edge_2_qn), .Q(rising_edge_q[1]), .Qn(rising_edge_2_qn), .preset(1'b0),
    .en(1'b1), .reset(1'b0));
  LED led_3 (.in(rising_edge_q[1]));
  LED led_4 (.in(rising_edge_2_qn));
  // Probe on rising_edge_q
  D_Flip_Flop rising_edge_3 (
    .clk(rising_edge_2_qn), .D(rising_edge_3_qn), .Q(rising_edge_q[2]), .Qn(rising_edge_3_qn), .preset(1'b0),
    .en(1'b1), .reset(1'b0));
  LED led_5 (.in(rising_edge_q[2]));
  LED led_6 (.in(rising_edge_3_qn));
  D_Flip_Flop rising_edge_4 (
    .clk(rising_edge_3_qn), .D(rising_edge_4_qn), .Q(rising_edge_q[3]), .Qn(rising_edge_4_qn), .preset(1'b0),
    .en(1'b1), .reset(1'b0));
  LED led_7 (.in(rising_edge_q[3]));
  LED led_8 (.in(rising_edge_4_qn));

  // Notes on the sheet:
  //   clk
  //   Q0
  //   Q1
  //   Q2
  //   Q3
  //   (LEDS light on 0)
endmodule

module clock5 (
);

  wire clock_1_out, rising_edge_2_qn, rising_edge_3_qn, rising_edge_4_qn, rising_edge_qn;
  wire [3:0] rising_edge_q;

  // Probe on clock_1_out
  Clock clock_1 (.out(clock_1_out));
  LED led_1 (.in(rising_edge_q[0]));
  D_Flip_Flop rising_edge (
    .clk(clock_1_out), .D(rising_edge_qn), .Q(rising_edge_q[0]), .Qn(rising_edge_qn), .preset(1'b0),
    .en(1'b1), .reset(1'b0));
  LED led_2 (.in(rising_edge_qn));
  LED led_3 (.in(rising_edge_q[1]));
  D_Flip_Flop rising_edge_2 (
    .clk(rising_edge_qn), .D(rising_edge_2_qn), .Q(rising_edge_q[1]), .Qn(rising_edge_2_qn), .preset(1'b0),
    .en(1'b1), .reset(1'b0));
  LED led_4 (.in(rising_edge_2_qn));
  // Probe on rising_edge_q
  LED led_5 (.in(rising_edge_q[2]));
  D_Flip_Flop rising_edge_3 (
    .clk(rising_edge_2_qn), .D(rising_edge_3_qn), .Q(rising_edge_q[2]), .Qn(rising_edge_3_qn), .preset(1'b0),
    .en(1'b1), .reset(1'b0));
  LED led_6 (.in(rising_edge_3_qn));
  D_Flip_Flop rising_edge_4 (
    .clk(rising_edge_3_qn), .D(rising_edge_4_qn), .Q(rising_edge_q[3]), .Qn(rising_edge_4_qn), .preset(1'b0),
    .en(1'b1), .reset(1'b0));
  LED led_7 (.in(rising_edge_q[3]));
  LED led_8 (.in(rising_edge_4_qn));

  // Notes on the sheet:
  //   clk
  //   Q0
  //   Q1
  //   Q2
  //   Q3
  //   (LEDS light on 0)
endmodule

module clock4 (
);

  wire clock_1_out, rising_edge_2_q, rising_edge_2_qn, rising_edge_3_q, rising_edge_3_qn, rising_edge_4_q,
       rising_edge_4_qn, rising_edge_q, rising_edge_qn;

  // Probe on clock_1_out
  Clock clock_1 (.out(clock_1_out));
  LED led_1 (.in(rising_edge_q));
  D_Flip_Flop rising_edge (
    .clk(clock_1_out), .D(rising_edge_qn), .Q(rising_edge_q), .Qn(rising_edge_qn), .preset(1'b0), .en(1'b1),
    .reset(1'b0));
  LED led_2 (.in(rising_edge_qn));
  LED led_3 (.in(rising_edge_2_q));
  D_Flip_Flop rising_edge_2 (
    .clk(rising_edge_qn), .D(rising_edge_2_qn), .Q(rising_edge_2_q), .Qn(rising_edge_2_qn), .preset(1'b0),
    .en(1'b1), .reset(1'b0));
  LED led_4 (.in(rising_edge_2_qn));
  LED led_5 (.in(rising_edge_3_q));
  D_Flip_Flop rising_edge_3 (
    .clk(rising_edge_2_qn), .D(rising_edge_3_qn), .Q(rising_edge_3_q), .Qn(rising_edge_3_qn), .preset(1'b0),
    .en(1'b1), .reset(1'b0));
  LED led_6 (.in(rising_edge_3_qn));
  D_Flip_Flop rising_edge_4 (
    .clk(rising_edge_3_qn), .D(rising_edge_4_qn), .Q(rising_edge_4_q), .Qn(rising_edge_4_qn), .preset(1'b0),
    .en(1'b1), .reset(1'b0));
  LED led_7 (.in(rising_edge_4_q));
  LED led_8 (.in(rising_edge_4_qn));

  // Notes on the sheet:
  //   clk
  //   Q0
  //   Q1
  //   Q2
  //   Q3
  //   (LEDS light on 0)
endmodule

module clock1 (
);

  wire clock_1_out, rising_edge_q, rising_edge_qn;

  // Probe on clock_1_out
  Clock clock_1 (.out(clock_1_out));
  LED led_1 (.in(rising_edge_q));
  D_Flip_Flop rising_edge (
    .clk(clock_1_out), .D(rising_edge_qn), .Q(rising_edge_q), .Qn(rising_edge_qn), .preset(1'b0), .en(1'b1),
    .reset(1'b0));
  LED led_2 (.in(rising_edge_qn));

  // Notes on the sheet:
  //   clk
  //   (LEDS light on 0)
endmodule

module clock0 (
);

  wire clock_1_out;

  // Probe on clock_1_out
  Clock clock_1 (.out(clock_1_out));

  // Notes on the sheet:
  //   clk
endmodule
