// Logisim project flashy.circ as structural Verilog: 3 circuits, main circuit 1987-full
module _1987_full (
);

  wire and_1_out, and_2_out, and_3_out, and_4_out, clock_out, reset_out;
  wire [3:0] d_ff_4_q, or_4_out;

  LED led_1 (.in(and_1_out));
  LED led_2 (.in(and_2_out));
  LED led_3 (.in(and_3_out));
  LED led_4 (.in(and_4_out));
  Hex_Digit_Display hex_digit_display_1 (.value(or_4_out));  // open: dp
  or or_1 (or_4_out[3], and_1_out, and_2_out, 1'b0);
  Button clock (.out(clock_out));
  Button reset (.out(reset_out));
  or or_2 (or_4_out[2], and_3_out, 1'b0, 1'b0);
  or or_3 (or_4_out[1], and_3_out, 1'b0, 1'b0);
  or or_4 (or_4_out[0], and_1_out, and_3_out, and_4_out);
  and and_1 (and_1_out, ~d_ff_4_q[3], ~d_ff_4_q[2], ~d_ff_4_q[1], d_ff_4_q[0]);  // AND_Gate
  and and_2 (and_2_out, d_ff_4_q[3], ~d_ff_4_q[2], ~d_ff_4_q[1], d_ff_4_q[0]);  // AND_Gate
  and and_3 (and_3_out, d_ff_4_q[3], ~d_ff_4_q[2], ~d_ff_4_q[1], ~d_ff_4_q[0]);  // AND_Gate
  and and_4 (and_4_out, ~d_ff_4_q[3], d_ff_4_q[2], d_ff_4_q[1], d_ff_4_q[0]);  // AND_Gate
  D_Flip_Flop d_ff_1 (
    .clk(clock_out), .D(or_4_out[3]), .Q(d_ff_4_q[3]), .preset(1'b0), .en(1'b1), .reset(reset_out));  // open: Qn
  D_Flip_Flop d_ff_2 (
    .clk(clock_out), .D(or_4_out[2]), .Q(d_ff_4_q[2]), .preset(1'b0), .en(1'b1), .reset(reset_out));  // open: Qn
  D_Flip_Flop d_ff_3 (
    .clk(clock_out), .D(or_4_out[1]), .Q(d_ff_4_q[1]), .preset(1'b0), .en(1'b1), .reset(reset_out));  // open: Qn
  D_Flip_Flop d_ff_4 (
    .clk(clock_out), .D(or_4_out[0]), .Q(d_ff_4_q[0]), .preset(reset_out), .en(1'b1), .reset(1'b0));  // open: Qn
  Hex_Digit_Display hex_digit_display_2 (.value(d_ff_4_q));  // open: dp

  // Notes on the sheet:
  //   3
  //   0
  //   3
  //   0
  //   3
  //   0
  //   3
  //   0
  //   these LEDs light on a "1"
  //   rising-edge
  //   3
  //   0
  //   3
  //   0
  //   3
  //   0
  //   3
  //   0
  //   3
  //   0
  //   3
  //   0
  //   3
  //   0
  //   3
  //   0
  //   (width 4)
endmodule

module _1987_skeleton (
  input  [3:0] _0
);

  wire and_1_out, and_2_out, and_3_out, and_4_out, clock_out, reset_out;
  wire [3:0] d_ff_4_q;

  LED led_1 (.in(and_1_out));
  LED led_2 (.in(and_2_out));
  LED led_3 (.in(and_3_out));
  LED led_4 (.in(and_4_out));
  Hex_Digit_Display hex_digit_display_1 (.value(_0));  // open: dp
  Button clock (.out(clock_out));
  Button reset (.out(reset_out));
  and and_1 (and_1_out, ~d_ff_4_q[3], ~d_ff_4_q[2], ~d_ff_4_q[1], d_ff_4_q[0]);  // AND_Gate
  and and_2 (and_2_out, d_ff_4_q[3], ~d_ff_4_q[2], ~d_ff_4_q[1], d_ff_4_q[0]);  // AND_Gate
  and and_3 (and_3_out, d_ff_4_q[3], ~d_ff_4_q[2], ~d_ff_4_q[1], ~d_ff_4_q[0]);  // AND_Gate
  and and_4 (and_4_out, ~d_ff_4_q[3], d_ff_4_q[2], d_ff_4_q[1], d_ff_4_q[0]);  // AND_Gate
  D_Flip_Flop d_ff_1 (
    .clk(clock_out), .D(_0[3]), .Q(d_ff_4_q[3]), .preset(1'b0), .en(1'b1), .reset(reset_out));  // open: Qn
  D_Flip_Flop d_ff_2 (
    .clk(clock_out), .D(_0[2]), .Q(d_ff_4_q[2]), .preset(1'b0), .en(1'b1), .reset(reset_out));  // open: Qn
  D_Flip_Flop d_ff_3 (
    .clk(clock_out), .D(_0[1]), .Q(d_ff_4_q[1]), .preset(1'b0), .en(1'b1), .reset(reset_out));  // open: Qn
  D_Flip_Flop d_ff_4 (
    .clk(clock_out), .D(_0[0]), .Q(d_ff_4_q[0]), .preset(1'b0), .en(1'b1), .reset(reset_out));  // open: Qn
  Hex_Digit_Display hex_digit_display_2 (.value(d_ff_4_q));  // open: dp

  // Notes on the sheet:
  //   3
  //   3
  //   0
  //   3
  //   0
  //   3
  //   0
  //   these LEDs light on a "1"
  //   rising-edge
  //   3
  //   0
  //   3
  //   0
  //   3
  //   0
  //   3
  //   0
  //   3
  //   0
  //   3
  //   0
  //   3
  //   0
  //   3
  //   0
  //   (width 4)
endmodule

module flippy (
  input  clock,
  output out_2
);

  wire not_1_out, reset_out;

  Button reset (.out(reset_out));
  D_Flip_Flop #(.trigger("high")) try_different_triggers (
    .clk(clock), .D(not_1_out), .Q(out_2), .preset(1'b0), .en(1'b1), .reset(reset_out));  // open: Qn
  not not_1 (not_1_out, out_2);
endmodule
