// Logisim project latch.circ as structural Verilog
module attempt_1 (
  input  Data,
  output Q,
  output Not_Q
);

  wire not_1_out;

  not not_1 (not_1_out, Data);
  nand nand_1 (Q, Data, Not_Q);
  nand nand_2 (Not_Q, Q, not_1_out);
endmodule

module attempt_2 (
  input  Clock,
  input  Data,
  output Q,
  output Not_Q
);

  wire nand_1_out, nand_2_out, not_1_out;

  not not_1 (not_1_out, Data);
  nand nand_1 (nand_1_out, Data, Clock);
  nand nand_2 (nand_2_out, Clock, not_1_out);
  nand nand_3 (Q, nand_1_out, Not_Q);
  nand nand_4 (Not_Q, Q, nand_2_out);
endmodule

module attempt_3 (
  input  active_low_reset,
  input  Clock,
  input  Data,
  output Q,
  output Not_Q
);

  wire nand_1_out, nand_2_out, not_1_out;

  not not_1 (not_1_out, Data);
  nand nand_1 (nand_1_out, Data, Clock);
  nand nand_2 (nand_2_out, Clock, not_1_out);
  nand nand_3 (Q, nand_1_out, Not_Q);
  nand nand_4 (Not_Q, Q, active_low_reset, nand_2_out);
endmodule

module attempt_4 (
  input  active_low_reset,
  input  Clock,
  input  Data,
  output Q,
  output Not_Q,
  output Q_2,
  output Not_Q_2
);

  wire nand_1_out, nand_2_out, not_1_out;

  not not_1 (not_1_out, Data);
  nand nand_1 (nand_1_out, Data, Clock);
  nand nand_2 (nand_2_out, Clock, not_1_out);
  nand nand_3 (Q, nand_1_out, Not_Q);
  nand nand_4 (Not_Q, Q, active_low_reset, nand_2_out);
  D_Flip_Flop #(.trigger("high")) d_ff_1 (
    .clk(Clock), .D(Data), .Q(Q_2), .Qn(Not_Q_2), .preset(1'b0), .en(1'b1), .reset(1'b0));

  // Notes on the sheet:
  //   (but other people call things with a level-trigger
  //   a LATCH, and use "flip-flop" for EDGE-triggered beasts)
  //   LogiSim calls this a "D Flip-Flop," 
  //     configured to have a high-level trigger
endmodule
