// Logisim project ram.circ as structural Verilog: 6 circuits, main circuit latchflop
module main (
  input  [2:0] in_1,
  input  ADDRESS,
  input  [3:0] in_3
);

  wire and_1_out, and_6_out, and_11_out, and_16_out, and_21_out, and_22_out, and_31_out, and_36_out,
       d_ff_1_q, d_ff_2_q, d_ff_3_q, d_ff_4_q, d_ff_5_q, d_ff_6_q, d_ff_7_q, d_ff_8_q, d_ff_9_q, d_ff_10_q,
       d_ff_11_q, d_ff_12_q, d_ff_13_q, d_ff_14_q, d_ff_15_q, d_ff_16_q, d_ff_17_q, d_ff_18_q, d_ff_19_q,
       d_ff_20_q, d_ff_21_q, d_ff_22_q, d_ff_23_q, d_ff_24_q, d_ff_25_q, d_ff_26_q, d_ff_27_q, d_ff_28_q,
       d_ff_29_q, d_ff_30_q, d_ff_31_q, d_ff_32_q, decoder_1_out0, decoder_1_out1, decoder_1_out2,
       decoder_1_out3, decoder_1_out4, decoder_1_out5, decoder_1_out6, decoder_1_out7;
  wire [3:0] or_4_out;
  wire [7:0] and_37_out, and_38_out, and_39_out, and_40_out;

  Hex_Digit_Display hex_digit_display_1 (.value({1'b0, in_1}));  // open: dp
  Hex_Digit_Display hex_digit_display_2 (.value(in_3));  // open: dp
  Decoder #(.select(3), .enable("false")) decoder_1 (
    .out0(decoder_1_out0), .out1(decoder_1_out1), .out2(decoder_1_out2), .out3(decoder_1_out3),
    .out4(decoder_1_out4), .out5(decoder_1_out5), .out6(decoder_1_out6), .out7(decoder_1_out7), .sel(in_1));
  and and_1 (and_1_out, ADDRESS, decoder_1_out0);
  and and_2 (and_37_out[7], decoder_1_out0, d_ff_1_q);
  D_Flip_Flop d_ff_1 (.clk(and_1_out), .D(in_3[3]), .Q(d_ff_1_q), .preset(1'b0), .en(1'b1), .reset(1'b0));  // open: Qn
  and and_3 (and_38_out[7], decoder_1_out0, d_ff_2_q);
  D_Flip_Flop d_ff_2 (.clk(and_1_out), .D(in_3[2]), .Q(d_ff_2_q), .preset(1'b0), .en(1'b1), .reset(1'b0));  // open: Qn
  and and_4 (and_39_out[7], decoder_1_out0, d_ff_3_q);
  D_Flip_Flop d_ff_3 (.clk(and_1_out), .D(in_3[1]), .Q(d_ff_3_q), .preset(1'b0), .en(1'b1), .reset(1'b0));  // open: Qn
  and and_5 (and_40_out[7], decoder_1_out0, d_ff_4_q);
  D_Flip_Flop d_ff_4 (.clk(and_1_out), .D(in_3[0]), .Q(d_ff_4_q), .preset(1'b0), .en(1'b1), .reset(1'b0));  // open: Qn
  and and_6 (and_6_out, ADDRESS, decoder_1_out1);
  and and_7 (and_37_out[6], decoder_1_out1, d_ff_5_q);
  D_Flip_Flop d_ff_5 (.clk(and_6_out), .D(in_3[3]), .Q(d_ff_5_q), .preset(1'b0), .en(1'b1), .reset(1'b0));  // open: Qn
  and and_8 (and_38_out[6], decoder_1_out1, d_ff_6_q);
  D_Flip_Flop d_ff_6 (.clk(and_6_out), .D(in_3[2]), .Q(d_ff_6_q), .preset(1'b0), .en(1'b1), .reset(1'b0));  // open: Qn
  and and_9 (and_39_out[6], decoder_1_out1, d_ff_7_q);
  D_Flip_Flop d_ff_7 (.clk(and_6_out), .D(in_3[1]), .Q(d_ff_7_q), .preset(1'b0), .en(1'b1), .reset(1'b0));  // open: Qn
  and and_10 (and_40_out[6], decoder_1_out1, d_ff_8_q);
  D_Flip_Flop d_ff_8 (.clk(and_6_out), .D(in_3[0]), .Q(d_ff_8_q), .preset(1'b0), .en(1'b1), .reset(1'b0));  // open: Qn
  and and_11 (and_11_out, ADDRESS, decoder_1_out2);
  and and_12 (and_37_out[5], decoder_1_out2, d_ff_9_q);
  D_Flip_Flop d_ff_9 (.clk(and_11_out), .D(in_3[3]), .Q(d_ff_9_q), .preset(1'b0), .en(1'b1), .reset(1'b0));  // open: Qn
  and and_13 (and_38_out[5], decoder_1_out2, d_ff_10_q);
  D_Flip_Flop d_ff_10 (
    .clk(and_11_out), .D(in_3[2]), .Q(d_ff_10_q), .preset(1'b0), .en(1'b1), .reset(1'b0));  // open: Qn
  and and_14 (and_39_out[5], decoder_1_out2, d_ff_11_q);
  D_Flip_Flop d_ff_11 (
    .clk(and_11_out), .D(in_3[1]), .Q(d_ff_11_q), .preset(1'b0), .en(1'b1), .reset(1'b0));  // open: Qn
  and and_15 (and_40_out[5], decoder_1_out2, d_ff_12_q);
  D_Flip_Flop d_ff_12 (
    .clk(and_11_out), .D(in_3[0]), .Q(d_ff_12_q), .preset(1'b0), .en(1'b1), .reset(1'b0));  // open: Qn
  and and_16 (and_16_out, ADDRESS, decoder_1_out3);
  and and_17 (and_37_out[4], decoder_1_out3, d_ff_13_q);
  D_Flip_Flop d_ff_13 (
    .clk(and_16_out), .D(in_3[3]), .Q(d_ff_13_q), .preset(1'b0), .en(1'b1), .reset(1'b0));  // open: Qn
  and and_18 (and_38_out[4], decoder_1_out3, d_ff_14_q);
  D_Flip_Flop d_ff_14 (
    .clk(and_16_out), .D(in_3[2]), .Q(d_ff_14_q), .preset(1'b0), .en(1'b1), .reset(1'b0));  // open: Qn
  and and_19 (and_39_out[4], decoder_1_out3, d_ff_15_q);
  D_Flip_Flop d_ff_15 (
    .clk(and_16_out), .D(in_3[1]), .Q(d_ff_15_q), .preset(1'b0), .en(1'b1), .reset(1'b0));  // open: Qn
  and and_20 (and_40_out[4], decoder_1_out3, d_ff_16_q);
  D_Flip_Flop d_ff_16 (
    .clk(and_16_out), .D(in_3[0]), .Q(d_ff_16_q), .preset(1'b0), .en(1'b1), .reset(1'b0));  // open: Qn
  and and_21 (and_21_out, ADDRESS, decoder_1_out4);
  D_Flip_Flop d_ff_17 (
    .clk(and_21_out), .D(in_3[3]), .Q(d_ff_17_q), .preset(1'b0), .en(1'b1), .reset(1'b0));  // open: Qn
  D_Flip_Flop d_ff_18 (
    .clk(and_21_out), .D(in_3[2]), .Q(d_ff_18_q), .preset(1'b0), .en(1'b1), .reset(1'b0));  // open: Qn
  D_Flip_Flop d_ff_19 (
    .clk(and_21_out), .D(in_3[1]), .Q(d_ff_19_q), .preset(1'b0), .en(1'b1), .reset(1'b0));  // open: Qn
  D_Flip_Flop d_ff_20 (
    .clk(and_21_out), .D(in_3[0]), .Q(d_ff_20_q), .preset(1'b0), .en(1'b1), .reset(1'b0));  // open: Qn
  and and_22 (and_22_out, ADDRESS, decoder_1_out5);
  and and_23 (and_37_out[3], decoder_1_out4, d_ff_17_q);
  and and_24 (and_38_out[3], decoder_1_out4, d_ff_18_q);
  and and_25 (and_39_out[3], decoder_1_out4, d_ff_19_q);
  and and_26 (and_40_out[3], decoder_1_out4, d_ff_20_q);
  D_Flip_Flop d_ff_21 (
    .clk(and_22_out), .D(in_3[3]), .Q(d_ff_21_q), .preset(1'b0), .en(1'b1), .reset(1'b0));  // open: Qn
  D_Flip_Flop d_ff_22 (
    .clk(and_22_out), .D(in_3[2]), .Q(d_ff_22_q), .preset(1'b0), .en(1'b1), .reset(1'b0));  // open: Qn
  D_Flip_Flop d_ff_23 (
    .clk(and_22_out), .D(in_3[1]), .Q(d_ff_23_q), .preset(1'b0), .en(1'b1), .reset(1'b0));  // open: Qn
  D_Flip_Flop d_ff_24 (
    .clk(and_22_out), .D(in_3[0]), .Q(d_ff_24_q), .preset(1'b0), .en(1'b1), .reset(1'b0));  // open: Qn
  and and_27 (and_37_out[2], decoder_1_out5, d_ff_21_q);
  and and_28 (and_38_out[2], decoder_1_out5, d_ff_22_q);
  and and_29 (and_39_out[2], decoder_1_out5, d_ff_23_q);
  and and_30 (and_40_out[2], decoder_1_out5, d_ff_24_q);
  and and_31 (and_31_out, ADDRESS, decoder_1_out6);
  D_Flip_Flop d_ff_25 (
    .clk(and_31_out), .D(in_3[3]), .Q(d_ff_25_q), .preset(1'b0), .en(1'b1), .reset(1'b0));  // open: Qn
  D_Flip_Flop d_ff_26 (
    .clk(and_31_out), .D(in_3[2]), .Q(d_ff_26_q), .preset(1'b0), .en(1'b1), .reset(1'b0));  // open: Qn
  D_Flip_Flop d_ff_27 (
    .clk(and_31_out), .D(in_3[1]), .Q(d_ff_27_q), .preset(1'b0), .en(1'b1), .reset(1'b0));  // open: Qn
  D_Flip_Flop d_ff_28 (
    .clk(and_31_out), .D(in_3[0]), .Q(d_ff_28_q), .preset(1'b0), .en(1'b1), .reset(1'b0));  // open: Qn
  and and_32 (and_37_out[1], decoder_1_out6, d_ff_25_q);
  and and_33 (and_38_out[1], decoder_1_out6, d_ff_26_q);
  and and_34 (and_39_out[1], decoder_1_out6, d_ff_27_q);
  and and_35 (and_40_out[1], decoder_1_out6, d_ff_28_q);
  and and_36 (and_36_out, ADDRESS, decoder_1_out7);
  and and_37 (and_37_out[0], decoder_1_out7, d_ff_29_q);
  D_Flip_Flop d_ff_29 (
    .clk(and_36_out), .D(in_3[3]), .Q(d_ff_29_q), .preset(1'b0), .en(1'b1), .reset(1'b0));  // open: Qn
  and and_38 (and_38_out[0], decoder_1_out7, d_ff_30_q);
  D_Flip_Flop d_ff_30 (
    .clk(and_36_out), .D(in_3[2]), .Q(d_ff_30_q), .preset(1'b0), .en(1'b1), .reset(1'b0));  // open: Qn
  and and_39 (and_39_out[0], decoder_1_out7, d_ff_31_q);
  D_Flip_Flop d_ff_31 (
    .clk(and_36_out), .D(in_3[1]), .Q(d_ff_31_q), .preset(1'b0), .en(1'b1), .reset(1'b0));  // open: Qn
  and and_40 (and_40_out[0], decoder_1_out7, d_ff_32_q);
  D_Flip_Flop d_ff_32 (
    .clk(and_36_out), .D(in_3[0]), .Q(d_ff_32_q), .preset(1'b0), .en(1'b1), .reset(1'b0));  // open: Qn
  or or_1 (or_4_out[3], and_37_out[0], and_37_out[1], and_37_out[2], and_37_out[3], and_37_out[4], and_37_out[5], and_37_out[6], and_37_out[7]);
  or or_2 (or_4_out[2], and_38_out[0], and_38_out[1], and_38_out[2], and_38_out[3], and_38_out[4], and_38_out[5], and_38_out[6], and_38_out[7]);
  or or_3 (or_4_out[1], and_39_out[0], and_39_out[1], and_39_out[2], and_39_out[3], and_39_out[4], and_39_out[5], and_39_out[6], and_39_out[7]);
  or or_4 (or_4_out[0], and_40_out[0], and_40_out[1], and_40_out[2], and_40_out[3], and_40_out[4], and_40_out[5], and_40_out[6], and_40_out[7]);
  Hex_Digit_Display hex_digit_display_3 (.value(or_4_out));  // open: dp

  // Notes on the sheet:
  //   WRITE
  //   DATA IN
  //   DATA OUT
endmodule

module two_nibbles_addr_bus (
  input  in_1,
  input  in_2,
  input  [3:0] in_3
);

  wire and_1_out, and_6_out, d_ff_1_q, d_ff_2_q, d_ff_3_q, d_ff_4_q, d_ff_5_q, d_ff_6_q, d_ff_7_q, d_ff_8_q,
       not_1_out;
  wire [1:0] and_7_out, and_8_out, and_9_out, and_10_out;
  wire [3:0] or_4_out;

  Hex_Digit_Display hex_digit_display_1 (.value(in_3));  // open: dp
  not not_1 (not_1_out, in_1);
  and and_1 (and_1_out, in_2, not_1_out);
  and and_2 (and_7_out[1], not_1_out, d_ff_1_q);
  D_Flip_Flop d_ff_1 (.clk(and_1_out), .D(in_3[3]), .Q(d_ff_1_q), .preset(1'b0), .en(1'b1), .reset(1'b0));  // open: Qn
  and and_3 (and_8_out[1], not_1_out, d_ff_2_q);
  D_Flip_Flop d_ff_2 (.clk(and_1_out), .D(in_3[2]), .Q(d_ff_2_q), .preset(1'b0), .en(1'b1), .reset(1'b0));  // open: Qn
  and and_4 (and_9_out[1], not_1_out, d_ff_3_q);
  D_Flip_Flop d_ff_3 (.clk(and_1_out), .D(in_3[1]), .Q(d_ff_3_q), .preset(1'b0), .en(1'b1), .reset(1'b0));  // open: Qn
  and and_5 (and_10_out[1], not_1_out, d_ff_4_q);
  D_Flip_Flop d_ff_4 (.clk(and_1_out), .D(in_3[0]), .Q(d_ff_4_q), .preset(1'b0), .en(1'b1), .reset(1'b0));  // open: Qn
  and and_6 (and_6_out, in_2, in_1);
  and and_7 (and_7_out[0], in_1, d_ff_5_q);
  D_Flip_Flop d_ff_5 (.clk(and_6_out), .D(in_3[3]), .Q(d_ff_5_q), .preset(1'b0), .en(1'b1), .reset(1'b0));  // open: Qn
  and and_8 (and_8_out[0], in_1, d_ff_6_q);
  D_Flip_Flop d_ff_6 (.clk(and_6_out), .D(in_3[2]), .Q(d_ff_6_q), .preset(1'b0), .en(1'b1), .reset(1'b0));  // open: Qn
  and and_9 (and_9_out[0], in_1, d_ff_7_q);
  D_Flip_Flop d_ff_7 (.clk(and_6_out), .D(in_3[1]), .Q(d_ff_7_q), .preset(1'b0), .en(1'b1), .reset(1'b0));  // open: Qn
  and and_10 (and_10_out[0], in_1, d_ff_8_q);
  D_Flip_Flop d_ff_8 (.clk(and_6_out), .D(in_3[0]), .Q(d_ff_8_q), .preset(1'b0), .en(1'b1), .reset(1'b0));  // open: Qn
  or or_1 (or_4_out[3], and_7_out[0], and_7_out[1]);
  or or_2 (or_4_out[2], and_8_out[0], and_8_out[1]);
  or or_3 (or_4_out[1], and_9_out[0], and_9_out[1]);
  or or_4 (or_4_out[0], and_10_out[0], and_10_out[1]);
  Hex_Digit_Display hex_digit_display_2 (.value(or_4_out));  // open: dp

  // Notes on the sheet:
  //   WRITE
  //   DATA IN
  //   WHICH
  //   DATA OUT
endmodule

module two_nibbles_push_bus (
  input  in_1,
  input  [3:0] in_2
);

  wire and_1_out, and_6_out, button_1_out, button_2_out, d_ff_1_q, d_ff_2_q, d_ff_3_q, d_ff_4_q, d_ff_5_q,
       d_ff_6_q, d_ff_7_q, d_ff_8_q;
  wire [1:0] and_7_out, and_8_out, and_9_out, and_10_out;
  wire [3:0] or_4_out;

  Hex_Digit_Display hex_digit_display_1 (.value(in_2));  // open: dp
  Button button_1 (.out(button_1_out));
  and and_1 (and_1_out, in_1, button_1_out);
  Button button_2 (.out(button_2_out));
  and and_2 (and_7_out[1], button_1_out, d_ff_1_q);
  D_Flip_Flop d_ff_1 (.clk(and_1_out), .D(in_2[3]), .Q(d_ff_1_q), .preset(1'b0), .en(1'b1), .reset(1'b0));  // open: Qn
  and and_3 (and_8_out[1], button_1_out, d_ff_2_q);
  D_Flip_Flop d_ff_2 (.clk(and_1_out), .D(in_2[2]), .Q(d_ff_2_q), .preset(1'b0), .en(1'b1), .reset(1'b0));  // open: Qn
  and and_4 (and_9_out[1], button_1_out, d_ff_3_q);
  D_Flip_Flop d_ff_3 (.clk(and_1_out), .D(in_2[1]), .Q(d_ff_3_q), .preset(1'b0), .en(1'b1), .reset(1'b0));  // open: Qn
  and and_5 (and_10_out[1], button_1_out, d_ff_4_q);
  D_Flip_Flop d_ff_4 (.clk(and_1_out), .D(in_2[0]), .Q(d_ff_4_q), .preset(1'b0), .en(1'b1), .reset(1'b0));  // open: Qn
  and and_6 (and_6_out, in_1, button_2_out);
  and and_7 (and_7_out[0], button_2_out, d_ff_5_q);
  D_Flip_Flop d_ff_5 (.clk(and_6_out), .D(in_2[3]), .Q(d_ff_5_q), .preset(1'b0), .en(1'b1), .reset(1'b0));  // open: Qn
  and and_8 (and_8_out[0], button_2_out, d_ff_6_q);
  D_Flip_Flop d_ff_6 (.clk(and_6_out), .D(in_2[2]), .Q(d_ff_6_q), .preset(1'b0), .en(1'b1), .reset(1'b0));  // open: Qn
  and and_9 (and_9_out[0], button_2_out, d_ff_7_q);
  D_Flip_Flop d_ff_7 (.clk(and_6_out), .D(in_2[1]), .Q(d_ff_7_q), .preset(1'b0), .en(1'b1), .reset(1'b0));  // open: Qn
  and and_10 (and_10_out[0], button_2_out, d_ff_8_q);
  D_Flip_Flop d_ff_8 (.clk(and_6_out), .D(in_2[0]), .Q(d_ff_8_q), .preset(1'b0), .en(1'b1), .reset(1'b0));  // open: Qn
  or or_1 (or_4_out[3], and_7_out[0], and_7_out[1]);
  or or_2 (or_4_out[2], and_8_out[0], and_8_out[1]);
  or or_3 (or_4_out[1], and_9_out[0], and_9_out[1]);
  or or_4 (or_4_out[0], and_10_out[0], and_10_out[1]);
  Hex_Digit_Display hex_digit_display_2 (.value(or_4_out));  // open: dp

  // Notes on the sheet:
  //   WRITE
  //   DATA IN
  //   WHICH
  //   DATA OUT
endmodule

module two_nibbles (
  input  in_1,
  input  [3:0] in_2
);

  wire and_1_out, and_2_out, and_3_out, and_4_out, and_5_out, and_6_out, and_7_out, and_8_out, and_9_out,
       and_10_out, button_1_out, button_2_out, d_ff_1_q, d_ff_2_q, d_ff_3_q, d_ff_4_q, d_ff_5_q, d_ff_6_q,
       d_ff_7_q, d_ff_8_q;
  wire [3:0] or_4_out;

  Hex_Digit_Display hex_digit_display_1 (.value(in_2));  // open: dp
  Button button_1 (.out(button_1_out));
  and and_1 (and_1_out, in_1, button_1_out);
  Button button_2 (.out(button_2_out));
  and and_2 (and_2_out, button_1_out, d_ff_1_q);
  D_Flip_Flop d_ff_1 (.clk(and_1_out), .D(in_2[3]), .Q(d_ff_1_q), .preset(1'b0), .en(1'b1), .reset(1'b0));  // open: Qn
  and and_3 (and_3_out, button_1_out, d_ff_2_q);
  D_Flip_Flop d_ff_2 (.clk(and_1_out), .D(in_2[2]), .Q(d_ff_2_q), .preset(1'b0), .en(1'b1), .reset(1'b0));  // open: Qn
  and and_4 (and_4_out, button_1_out, d_ff_3_q);
  D_Flip_Flop d_ff_3 (.clk(and_1_out), .D(in_2[1]), .Q(d_ff_3_q), .preset(1'b0), .en(1'b1), .reset(1'b0));  // open: Qn
  and and_5 (and_5_out, button_1_out, d_ff_4_q);
  D_Flip_Flop d_ff_4 (.clk(and_1_out), .D(in_2[0]), .Q(d_ff_4_q), .preset(1'b0), .en(1'b1), .reset(1'b0));  // open: Qn
  and and_6 (and_6_out, in_1, button_2_out);
  and and_7 (and_7_out, button_2_out, d_ff_5_q);
  D_Flip_Flop d_ff_5 (.clk(and_6_out), .D(in_2[3]), .Q(d_ff_5_q), .preset(1'b0), .en(1'b1), .reset(1'b0));  // open: Qn
  and and_8 (and_8_out, button_2_out, d_ff_6_q);
  D_Flip_Flop d_ff_6 (.clk(and_6_out), .D(in_2[2]), .Q(d_ff_6_q), .preset(1'b0), .en(1'b1), .reset(1'b0));  // open: Qn
  and and_9 (and_9_out, button_2_out, d_ff_7_q);
  D_Flip_Flop d_ff_7 (.clk(and_6_out), .D(in_2[1]), .Q(d_ff_7_q), .preset(1'b0), .en(1'b1), .reset(1'b0));  // open: Qn
  and and_10 (and_10_out, button_2_out, d_ff_8_q);
  D_Flip_Flop d_ff_8 (.clk(and_6_out), .D(in_2[0]), .Q(d_ff_8_q), .preset(1'b0), .en(1'b1), .reset(1'b0));  // open: Qn
  or or_1 (or_4_out[3], and_7_out, and_2_out);
  or or_2 (or_4_out[2], and_8_out, and_3_out);
  or or_3 (or_4_out[1], and_9_out, and_4_out);
  or or_4 (or_4_out[0], and_10_out, and_5_out);
  Hex_Digit_Display hex_digit_display_2 (.value(or_4_out));  // open: dp

  // Notes on the sheet:
  //   WRITE
  //   DATA IN
  //   WHICH
  //   DATA OUT
endmodule

module one_nibble (
  input  in_1,
  input  [3:0] in_2
);

  wire [3:0] d_ff_4_q;

  Hex_Digit_Display hex_digit_display_1 (.value(in_2));  // open: dp
  D_Flip_Flop d_ff_1 (.clk(in_1), .D(in_2[3]), .Q(d_ff_4_q[3]), .preset(1'b0), .en(1'b1), .reset(1'b0));  // open: Qn
  D_Flip_Flop d_ff_2 (.clk(in_1), .D(in_2[2]), .Q(d_ff_4_q[2]), .preset(1'b0), .en(1'b1), .reset(1'b0));  // open: Qn
  D_Flip_Flop d_ff_3 (.clk(in_1), .D(in_2[1]), .Q(d_ff_4_q[1]), .preset(1'b0), .en(1'b1), .reset(1'b0));  // open: Qn
  D_Flip_Flop d_ff_4 (.clk(in_1), .D(in_2[0]), .Q(d_ff_4_q[0]), .preset(1'b0), .en(1'b1), .reset(1'b0));  // open: Qn
  Hex_Digit_Display hex_digit_display_2 (.value(d_ff_4_q));  // open: dp

  // Notes on the sheet:
  //   WRITE
  //   DATA IN
  //   DATA OUT
endmodule

module latchflop (
  input  Clock,
  input  Data,
  output Q,
  output Not_Q,
  output Q_2,
  output Not_Q_2
);

  D_Flip_Flop #(.trigger("high")) d_ff_1 (
    .clk(Clock), .D(Data), .Q(Q), .Qn(Not_Q), .preset(1'b0), .en(1'b1), .reset(1'b0));
  D_Flip_Flop d_ff_2 (.clk(Clock), .D(Data), .Q(Q_2), .Qn(Not_Q_2), .preset(1'b0), .en(1'b1), .reset(1'b0));

  // Notes on the sheet:
  //   "latch"  vs  "flip-flop"
  //   (rising-edge trigger)
  //   (high-level trigger)
endmodule
