// Logisim project rs-one-push.circ as structural Verilog: 3 circuits, main circuit main
module main (
  input  in_1,
  output out_2,
  output out_3,
  output out_4
);

  nand nand_1 (out_3, in_1, out_4);
  nand nand_2 (out_4, out_3, in_1);

  assign out_2 = in_1;
endmodule

module main_with_delay (
  input  in_1,
  output out_2,
  output out_3,
  output out_4,
  output out_5,
  output out_6
);

  nand nand_1 (out_3, in_1, out_5);
  nand nand_2 (out_6, out_4, in_1);
  delay delay_1 (.In(out_3), .Out(out_4));
  delay delay_2 (.In(out_6), .Out(out_5));

  assign out_2 = in_1;

  // Notes on the sheet:
  //   remember to re-enable simulation)
  //   (to turn on delay, go to "Simulate -> Ticks Enabled")
  //   (but if you got an oscillation error on the main circuit,
endmodule

module delay (
  input  In,
  output Out
);

  wire clock_1_out, comparator_1_eq, xnor_1_out;
  wire [1:0] counter_1_q;

  xnor xnor_1 (xnor_1_out, In, Out);
  Counter #(.width(2), .max('h3)) counter_1 (
    .load(1'b0), .count(1'b1), .Q(counter_1_q), .clk(clock_1_out), .clr(xnor_1_out));  // open: D, carry
  Clock clock_1 (.out(clock_1_out));
  Comparator #(.width(2)) comparator_1 (.a(2'b10), .b(counter_1_q), .eq(comparator_1_eq));  // open: gt, lt
  D_Flip_Flop d_ff_1 (.clk(comparator_1_eq), .D(In), .Q(Out));  // open: Qn, preset, en, reset
endmodule
