// Logisim project rs-two-push.circ as structural Verilog: 1 circuit, main circuit main
module main (
  output out_1,
  output Q,
  output Not_Q,
  output out_4
);

  wire Reset_out, Set_out;

  Button Set (.out(Set_out));
  not not_1 (out_1, Set_out);
  Button Reset (.out(Reset_out));
  not not_2 (out_4, Reset_out);
  nand nand_1 (Q, out_1, Not_Q);
  nand nand_2 (Not_Q, Q, out_4);
endmodule
