// Logisim project traffic-lights.circ as structural Verilog
module microcode_skel_rom (
  input  in_1,
  output out_2,
  output out_3,
  output out_4,
  output out_5,
  output out_6,
  output out_7,
  output out_8,
  output out_9,
  output out_10,
  output out_11,
  output out_12,
  output on,
  output off,
  output out_15,
  output out_16,
  output out_17,
  output out_18,
  output out_19,
  output out_20,
  output out_21,
  output out_22,
  output out_23,
  output out_24
);

  wire decoder_1_out0, decoder_1_out1, decoder_1_out2, decoder_1_out3, decoder_1_out4, decoder_1_out5,
       decoder_1_out6, n3latch_alow_1_out_8, n3latch_alow_1_out_9, n3latch_alow_1_q1, n3latch_alow_2_out_8,
       n3latch_alow_2_out_9, n3latch_alow_2_q1;
  wire [0:0] rom_1_data;
  wire [2:0] _3_bit_counter_q;

  // Probe on on
  Button clock (.out(out_11));
  Button reset (.out(out_12));
  // Probe on {off, out_15, out_16, out_17}
  // Probe on {out_18, out_19, out_20, out_21}
  // Probe on {off, out_15, out_16, out_17}
  // Probe on on
  Counter #(.width(3), .max('h7)) _3_bit_counter (
    .Q(_3_bit_counter_q), .clk(out_11), .clr(out_9));  // open: load, D, count, carry
  and and_1 (out_9, out_8, ~out_11);  // AND_Gate
  // Probe on {out_22, out_23, out_24, rom_1_data[0]}
  // Probe on {out_18, out_19, out_20, out_21}
  // Probe on {out_22, out_23, out_24, rom_1_data[0]}
  or or_1 (out_8, ~rom_1_data[0], out_12);  // OR_Gate
  ROM #(.addrWidth(3), .dataWidth(13)) rom_1 (
    .addr(_3_bit_counter_q),
    .data({on, off, out_15, out_16, out_17, out_18, out_19, out_20, out_21, out_22, out_23, out_24, rom_1_data[0]}));  // open: sel
  Decoder #(.select(3), .disabled(0)) decoder_1 (
    .out0(decoder_1_out0), .out1(decoder_1_out1), .out2(decoder_1_out2), .out3(decoder_1_out3),
    .out4(decoder_1_out4), .out5(decoder_1_out5), .out6(decoder_1_out6), .sel(_3_bit_counter_q), .en(in_1));  // open: out7
  Pull_Resistor #(.pull(1)) pull_resistor_1 (.node(on));
  not not_1 (out_2, decoder_1_out0);
  not not_2 (out_3, decoder_1_out1);
  tiny_diode tiny_diode_1 (._0_1_in(out_4), ._0_Z_out(on));
  not not_3 (out_4, decoder_1_out2);
  not not_4 (out_5, decoder_1_out3);
  not not_5 (out_6, decoder_1_out4);
  not not_6 (out_7, decoder_1_out5);
  not not_7 (out_10, decoder_1_out6);
  Pull_Resistor #(.pull(1)) pull_resistor_2 (.node(off));
  Pull_Resistor #(.pull(1)) pull_resistor_3 (.node(out_15));
  tiny_diode tiny_diode_2 (._0_1_in(out_2), ._0_Z_out(off));
  tiny_diode tiny_diode_3 (._0_1_in(out_3), ._0_Z_out(out_15));
  Pull_Resistor #(.pull(1)) pull_resistor_4 (.node(out_17));
  Pull_Resistor #(.pull(1)) pull_resistor_5 (.node(out_16));
  tiny_diode tiny_diode_4 (._0_1_in(out_2), ._0_Z_out(out_17));
  tiny_diode tiny_diode_5 (._0_1_in(out_4), ._0_Z_out(out_16));
  Pull_Resistor #(.pull(1)) pull_resistor_6 (.node(out_19));
  Pull_Resistor #(.pull(1)) pull_resistor_7 (.node(out_18));
  tiny_diode tiny_diode_6 (._0_1_in(out_3), ._0_Z_out(out_18));
  tiny_diode tiny_diode_7 (._0_1_in(out_7), ._0_Z_out(out_19));
  Pull_Resistor #(.pull(1)) pull_resistor_8 (.node(out_21));
  Pull_Resistor #(.pull(1)) pull_resistor_9 (.node(out_20));
  tiny_diode tiny_diode_8 (._0_1_in(out_5), ._0_Z_out(out_20));
  tiny_diode tiny_diode_9 (._0_1_in(out_6), ._0_Z_out(out_21));
  Pull_Resistor #(.pull(1)) pull_resistor_10 (.node(out_23));
  Pull_Resistor #(.pull(1)) pull_resistor_11 (.node(out_22));
  tiny_diode tiny_diode_10 (._0_1_in(out_5), ._0_Z_out(out_23));
  tiny_diode tiny_diode_11 (._0_1_in(out_7), ._0_Z_out(out_22));
  Pull_Resistor #(.pull(1)) pull_resistor_12 (.node(out_24));
  Pull_Resistor #(.pull(1)) pull_resistor_13 (.node(rom_1_data[0]));
  tiny_diode tiny_diode_12 (._0_1_in(out_6), ._0_Z_out(out_24));
  tiny_diode tiny_diode_13 (._0_1_in(out_10), ._0_Z_out(rom_1_data[0]));
  _3latch_alow u_3latch_alow_1 (
    .On_1(on), .Off_1(off), .in_3(out_15), .in_4(out_16), .in_5(out_17), .in_6(out_18),
    .Q1(n3latch_alow_1_q1), .out_8(n3latch_alow_1_out_8), .out_9(n3latch_alow_1_out_9));
  LED #(.active("false")) led_1 (.in(n3latch_alow_1_q1));
  LED #(.active("false")) led_2 (.in(n3latch_alow_1_out_8));
  LED #(.active("false")) led_3 (.in(n3latch_alow_1_out_9));
  _3latch_alow u_3latch_alow_2 (
    .On_1(out_19), .Off_1(out_20), .in_3(out_21), .in_4(out_22), .in_5(out_23), .in_6(out_24),
    .Q1(n3latch_alow_2_q1), .out_8(n3latch_alow_2_out_8), .out_9(n3latch_alow_2_out_9));
  LED #(.active("false")) led_4 (.in(n3latch_alow_2_q1));
  LED #(.active("false")) led_5 (.in(n3latch_alow_2_out_8));
  LED #(.active("false")) led_6 (.in(n3latch_alow_2_out_9));

  // Notes on the sheet:
  //   contents of rom_1 (hex, n*v repeats v):
  //   16ff 1b7f dff 1fdb 1fed 1fb7 1ffe
  //   N R
  //   N Y
  //   N R
  //   on
  //   N Y
  //   N G
  //   on
  //   off
  //   off
  //   E R
  //   E R
  //   N G
  //   off
  //   on
  //   E Y
  //   E Y
  //   off
  //   on
  //   E G
  //   E G
  //   off
  //   on
  //   "Microcode"
  //   0. turn N red off, and n green on 
  //   1. turn N green off, N yellow on
  //   2. turn N yellow off, turn N red on
  //   3. turn E red off, turn E green on
  //   4. turn E green off, turn E yellow on
  //   5. turn E yellow off, turn E red on
  //   6. goto 0
  //   North/South
  //   East/West
endmodule

module microcode_skel_1 (
  input  in_1,
  output out_2,
  output out_3,
  output out_4,
  output out_5,
  output out_6,
  output out_7,
  output out_8,
  output out_9,
  output out_10,
  output out_11,
  output out_12,
  output on,
  output off,
  output out_15,
  output out_16,
  output out_17,
  output out_18,
  output out_19,
  output out_20,
  output out_21,
  output out_22,
  output out_23,
  output out_24
);

  wire decoder_1_out0, decoder_1_out1, decoder_1_out2, decoder_1_out3, decoder_1_out4, decoder_1_out5,
       decoder_1_out6, n3latch_alow_1_out_8, n3latch_alow_1_out_9, n3latch_alow_1_q1, n3latch_alow_2_out_8,
       n3latch_alow_2_out_9, n3latch_alow_2_q1;
  wire [0:0] pull_resistor_13_node;
  wire [2:0] _3_bit_counter_q;

  // Probe on on
  Button clock (.out(out_11));
  Button reset (.out(out_12));
  // Probe on {off, out_15, out_16, out_17}
  // Probe on {out_18, out_19, out_20, out_21}
  // Probe on {off, out_15, out_16, out_17}
  // Probe on on
  Counter #(.width(3), .max('h7)) _3_bit_counter (
    .Q(_3_bit_counter_q), .clk(out_11), .clr(out_9));  // open: load, D, count, carry
  and and_1 (out_9, out_8, ~out_11);  // AND_Gate
  // Probe on {out_22, out_23, out_24, pull_resistor_13_node[0]}
  // Probe on {out_22, out_23, out_24, pull_resistor_13_node[0]}
  // Probe on {out_18, out_19, out_20, out_21}
  or or_1 (out_8, ~pull_resistor_13_node[0], out_12);  // OR_Gate
  ROM #(.addrWidth(3), .dataWidth(13)) rom_1 (.addr(_3_bit_counter_q));  // open: data, sel
  Decoder #(.select(3), .disabled(0)) decoder_1 (
    .out0(decoder_1_out0), .out1(decoder_1_out1), .out2(decoder_1_out2), .out3(decoder_1_out3),
    .out4(decoder_1_out4), .out5(decoder_1_out5), .out6(decoder_1_out6), .sel(_3_bit_counter_q), .en(in_1));  // open: out7
  Pull_Resistor #(.pull(1)) pull_resistor_1 (.node(on));
  not not_1 (out_2, decoder_1_out0);
  not not_2 (out_3, decoder_1_out1);
  tiny_diode tiny_diode_1 (._0_1_in(out_4), ._0_Z_out(on));
  not not_3 (out_4, decoder_1_out2);
  not not_4 (out_5, decoder_1_out3);
  not not_5 (out_6, decoder_1_out4);
  not not_6 (out_7, decoder_1_out5);
  not not_7 (out_10, decoder_1_out6);
  Pull_Resistor #(.pull(1)) pull_resistor_2 (.node(out_15));
  Pull_Resistor #(.pull(1)) pull_resistor_3 (.node(off));
  tiny_diode tiny_diode_2 (._0_1_in(out_2), ._0_Z_out(off));
  tiny_diode tiny_diode_3 (._0_1_in(out_3), ._0_Z_out(out_15));
  Pull_Resistor #(.pull(1)) pull_resistor_4 (.node(out_16));
  Pull_Resistor #(.pull(1)) pull_resistor_5 (.node(out_17));
  tiny_diode tiny_diode_4 (._0_1_in(out_2), ._0_Z_out(out_17));
  tiny_diode tiny_diode_5 (._0_1_in(out_4), ._0_Z_out(out_16));
  Pull_Resistor #(.pull(1)) pull_resistor_6 (.node(out_19));
  Pull_Resistor #(.pull(1)) pull_resistor_7 (.node(out_18));
  tiny_diode tiny_diode_6 (._0_1_in(out_3), ._0_Z_out(out_18));
  tiny_diode tiny_diode_7 (._0_1_in(out_7), ._0_Z_out(out_19));
  Pull_Resistor #(.pull(1)) pull_resistor_8 (.node(out_20));
  Pull_Resistor #(.pull(1)) pull_resistor_9 (.node(out_21));
  tiny_diode tiny_diode_8 (._0_1_in(out_5), ._0_Z_out(out_20));
  tiny_diode tiny_diode_9 (._0_1_in(out_6), ._0_Z_out(out_21));
  Pull_Resistor #(.pull(1)) pull_resistor_10 (.node(out_22));
  Pull_Resistor #(.pull(1)) pull_resistor_11 (.node(out_23));
  tiny_diode tiny_diode_10 (._0_1_in(out_5), ._0_Z_out(out_23));
  tiny_diode tiny_diode_11 (._0_1_in(out_7), ._0_Z_out(out_22));
  Pull_Resistor #(.pull(1)) pull_resistor_12 (.node(out_24));
  Pull_Resistor #(.pull(1)) pull_resistor_13 (.node(pull_resistor_13_node[0]));
  tiny_diode tiny_diode_12 (._0_1_in(out_6), ._0_Z_out(out_24));
  tiny_diode tiny_diode_13 (._0_1_in(out_10), ._0_Z_out(pull_resistor_13_node[0]));
  LED #(.active("false")) led_1 (.in(n3latch_alow_1_q1));
  _3latch_alow u_3latch_alow_1 (
    .On_1(on), .Off_1(off), .in_3(out_15), .in_4(out_16), .in_5(out_17), .in_6(out_18),
    .Q1(n3latch_alow_1_q1), .out_8(n3latch_alow_1_out_8), .out_9(n3latch_alow_1_out_9));
  LED #(.active("false")) led_2 (.in(n3latch_alow_1_out_8));
  LED #(.active("false")) led_3 (.in(n3latch_alow_1_out_9));
  LED #(.active("false")) led_4 (.in(n3latch_alow_2_q1));
  _3latch_alow u_3latch_alow_2 (
    .On_1(out_19), .Off_1(out_20), .in_3(out_21), .in_4(out_22), .in_5(out_23), .in_6(out_24),
    .Q1(n3latch_alow_2_q1), .out_8(n3latch_alow_2_out_8), .out_9(n3latch_alow_2_out_9));
  LED #(.active("false")) led_5 (.in(n3latch_alow_2_out_8));
  LED #(.active("false")) led_6 (.in(n3latch_alow_2_out_9));

  // Notes on the sheet:
  //   N R
  //   N R
  //   N Y
  //   on
  //   N Y
  //   N G
  //   on
  //   off
  //   off
  //   E R
  //   E R
  //   N G
  //   off
  //   on
  //   E Y
  //   E Y
  //   off
  //   on
  //   E G
  //   E G
  //   off
  //   on
  //   "Microcode"
  //   0. turn N red off, and n green on 
  //   1. turn N green off, N yellow on
  //   2. turn N yellow off, turn N red on
  //   3. turn E red off, turn E green on
  //   4. turn E green off, turn E yellow on
  //   5. turn E yellow off, turn E red on
  //   6. goto 0
  //   North/South
  //   East/West
endmodule

module microcode_full (
  input  in_1,
  output out_2,
  output out_3,
  output out_4,
  output out_5,
  output out_6,
  output out_7,
  output out_8,
  output out_9,
  output out_10,
  output out_11,
  output out_12,
  output on,
  output off,
  output out_15,
  output out_16,
  output out_17,
  output out_18,
  output out_19,
  output out_20,
  output out_21,
  output out_22,
  output out_23,
  output out_24
);

  wire decoder_1_out0, decoder_1_out1, decoder_1_out2, decoder_1_out3, decoder_1_out4, decoder_1_out5,
       decoder_1_out6, n3latch_alow_1_out_8, n3latch_alow_1_out_9, n3latch_alow_1_q1, n3latch_alow_2_out_8,
       n3latch_alow_2_out_9, n3latch_alow_2_q1;
  wire [0:0] pull_resistor_12_node;
  wire [2:0] _3_bit_counter_q;

  // Probe on on
  Button clock (.out(out_11));
  Button reset (.out(out_12));
  // Probe on {out_18, out_19, out_20, out_21}
  // Probe on {off, out_15, out_16, out_17}
  // Probe on {off, out_15, out_16, out_17}
  // Probe on on
  Counter #(.width(3), .max('h7)) _3_bit_counter (
    .Q(_3_bit_counter_q), .clk(out_11), .clr(out_9));  // open: load, D, count, carry
  and and_1 (out_9, out_8, ~out_11);  // AND_Gate
  // Probe on {out_22, out_23, out_24, pull_resistor_12_node[0]}
  // Probe on {out_18, out_19, out_20, out_21}
  // Probe on {out_22, out_23, out_24, pull_resistor_12_node[0]}
  or or_1 (out_8, ~pull_resistor_12_node[0], out_12);  // OR_Gate
  Decoder #(.select(3), .disabled(0)) decoder_1 (
    .out0(decoder_1_out0), .out1(decoder_1_out1), .out2(decoder_1_out2), .out3(decoder_1_out3),
    .out4(decoder_1_out4), .out5(decoder_1_out5), .out6(decoder_1_out6), .sel(_3_bit_counter_q), .en(in_1));  // open: out7
  Pull_Resistor #(.pull(1)) pull_resistor_1 (.node(on));
  not not_1 (out_2, decoder_1_out0);
  not not_2 (out_3, decoder_1_out1);
  tiny_diode tiny_diode_1 (._0_1_in(out_4), ._0_Z_out(on));
  not not_3 (out_4, decoder_1_out2);
  not not_4 (out_5, decoder_1_out3);
  not not_5 (out_6, decoder_1_out4);
  not not_6 (out_7, decoder_1_out5);
  not not_7 (out_10, decoder_1_out6);
  Pull_Resistor #(.pull(1)) pull_resistor_2 (.node(out_15));
  Pull_Resistor #(.pull(1)) pull_resistor_3 (.node(off));
  tiny_diode tiny_diode_2 (._0_1_in(out_2), ._0_Z_out(off));
  tiny_diode tiny_diode_3 (._0_1_in(out_3), ._0_Z_out(out_15));
  Pull_Resistor #(.pull(1)) pull_resistor_4 (.node(out_17));
  Pull_Resistor #(.pull(1)) pull_resistor_5 (.node(out_16));
  tiny_diode tiny_diode_4 (._0_1_in(out_2), ._0_Z_out(out_17));
  tiny_diode tiny_diode_5 (._0_1_in(out_4), ._0_Z_out(out_16));
  Pull_Resistor #(.pull(1)) pull_resistor_6 (.node(out_19));
  Pull_Resistor #(.pull(1)) pull_resistor_7 (.node(out_18));
  tiny_diode tiny_diode_6 (._0_1_in(out_3), ._0_Z_out(out_18));
  tiny_diode tiny_diode_7 (._0_1_in(out_7), ._0_Z_out(out_19));
  Pull_Resistor #(.pull(1)) pull_resistor_8 (.node(out_21));
  Pull_Resistor #(.pull(1)) pull_resistor_9 (.node(out_20));
  tiny_diode tiny_diode_8 (._0_1_in(out_5), ._0_Z_out(out_20));
  tiny_diode tiny_diode_9 (._0_1_in(out_6), ._0_Z_out(out_21));
  Pull_Resistor #(.pull(1)) pull_resistor_10 (.node(out_22));
  Pull_Resistor #(.pull(1)) pull_resistor_11 (.node(out_23));
  tiny_diode tiny_diode_10 (._0_1_in(out_5), ._0_Z_out(out_23));
  tiny_diode tiny_diode_11 (._0_1_in(out_7), ._0_Z_out(out_22));
  Pull_Resistor #(.pull(1)) pull_resistor_12 (.node(pull_resistor_12_node[0]));
  Pull_Resistor #(.pull(1)) pull_resistor_13 (.node(out_24));
  tiny_diode tiny_diode_12 (._0_1_in(out_6), ._0_Z_out(out_24));
  tiny_diode tiny_diode_13 (._0_1_in(out_10), ._0_Z_out(pull_resistor_12_node[0]));
  LED #(.active("false")) led_1 (.in(n3latch_alow_1_q1));
  _3latch_alow u_3latch_alow_1 (
    .On_1(on), .Off_1(off), .in_3(out_15), .in_4(out_16), .in_5(out_17), .in_6(out_18),
    .Q1(n3latch_alow_1_q1), .out_8(n3latch_alow_1_out_8), .out_9(n3latch_alow_1_out_9));
  LED #(.active("false")) led_2 (.in(n3latch_alow_1_out_8));
  LED #(.active("false")) led_3 (.in(n3latch_alow_1_out_9));
  LED #(.active("false")) led_4 (.in(n3latch_alow_2_q1));
  _3latch_alow u_3latch_alow_2 (
    .On_1(out_19), .Off_1(out_20), .in_3(out_21), .in_4(out_22), .in_5(out_23), .in_6(out_24),
    .Q1(n3latch_alow_2_q1), .out_8(n3latch_alow_2_out_8), .out_9(n3latch_alow_2_out_9));
  LED #(.active("false")) led_5 (.in(n3latch_alow_2_out_8));
  LED #(.active("false")) led_6 (.in(n3latch_alow_2_out_9));

  // Notes on the sheet:
  //   N R
  //   N Y
  //   N R
  //   on
  //   N Y
  //   N G
  //   on
  //   off
  //   off
  //   E R
  //   E R
  //   N G
  //   on
  //   off
  //   E Y
  //   E Y
  //   on
  //   off
  //   E G
  //   E G
  //   off
  //   on
  //   "Microcode"
  //   0. turn N red off, and n green on 
  //   1. turn N green off, N yellow on
  //   2. turn N yellow off, turn N red on
  //   3. turn E red off, turn E green on
  //   4. turn E green off, turn E yellow on
  //   5. turn E yellow off, turn E red on
  //   6. goto 0
  //   North/South
  //   East/West
endmodule

module microcode_skel_0 (
  input  in_1,
  output out_2,
  output out_3,
  output out_4,
  output out_5,
  output out_6,
  output out_7,
  output out_8,
  output out_9,
  output out_10,
  output out_11,
  output out_12,
  output out_13,
  output on,
  output off,
  output on_2,
  output out_17,
  output out_18,
  output out_19,
  output out_20,
  output out_21,
  output out_22,
  output out_23,
  output out_24,
  output out_25
);

  wire decoder_1_out0, decoder_1_out1, decoder_1_out2, decoder_1_out3, decoder_1_out4, decoder_1_out5,
       decoder_1_out6, n3latch_alow_1_out_8, n3latch_alow_1_out_9, n3latch_alow_1_q1, n3latch_alow_2_out_8,
       n3latch_alow_2_out_9, n3latch_alow_2_q1, tiny_diode_1__0_z_out, undriven;
  wire [2:0] _3_bit_counter_q;

  // Probe on on
  tiny_diode tiny_diode_1 (._0_1_in(undriven), ._0_Z_out(tiny_diode_1__0_z_out));
  Button clock (.out(out_11));
  Button reset (.out(out_12));
  // Probe on {off, on_2, out_17, out_18}
  // Probe on {out_19, out_20, out_21, out_22}
  // Probe on on
  // Probe on {off, on_2, out_17, out_18}
  Counter #(.width(3), .max('h7)) _3_bit_counter (
    .Q(_3_bit_counter_q), .clk(out_11), .clr(out_9));  // open: load, D, count, carry
  and and_1 (out_9, out_8, ~out_11);  // AND_Gate
  // Probe on {out_23, out_24, out_25, out_13}
  // Probe on {out_19, out_20, out_21, out_22}
  // Probe on {out_23, out_24, out_25, out_13}
  or or_1 (out_8, ~out_13, out_12);  // OR_Gate
  Decoder #(.select(3), .disabled(0)) decoder_1 (
    .out0(decoder_1_out0), .out1(decoder_1_out1), .out2(decoder_1_out2), .out3(decoder_1_out3),
    .out4(decoder_1_out4), .out5(decoder_1_out5), .out6(decoder_1_out6), .sel(_3_bit_counter_q), .en(in_1));  // open: out7
  Pull_Resistor #(.pull(1)) pull_resistor_1 (.node(on));
  not not_1 (out_2, decoder_1_out0);
  not not_2 (out_3, decoder_1_out1);
  not not_3 (out_4, decoder_1_out2);
  not not_4 (out_5, decoder_1_out3);
  not not_5 (out_6, decoder_1_out4);
  not not_6 (out_7, decoder_1_out5);
  not not_7 (out_10, decoder_1_out6);
  Pull_Resistor #(.pull(1)) pull_resistor_2 (.node(on_2));
  Pull_Resistor #(.pull(1)) pull_resistor_3 (.node(off));
  Pull_Resistor #(.pull(1)) pull_resistor_4 (.node(out_18));
  Pull_Resistor #(.pull(1)) pull_resistor_5 (.node(out_17));
  Pull_Resistor #(.pull(1)) pull_resistor_6 (.node(out_20));
  Pull_Resistor #(.pull(1)) pull_resistor_7 (.node(out_19));
  Pull_Resistor #(.pull(1)) pull_resistor_8 (.node(out_21));
  Pull_Resistor #(.pull(1)) pull_resistor_9 (.node(out_22));
  Pull_Resistor #(.pull(1)) pull_resistor_10 (.node(out_23));
  Pull_Resistor #(.pull(1)) pull_resistor_11 (.node(out_24));
  Pull_Resistor #(.pull(1)) pull_resistor_12 (.node(out_25));
  Pull_Resistor #(.pull(1)) pull_resistor_13 (.node(out_13));
  LED #(.active("false")) led_1 (.in(n3latch_alow_1_q1));
  _3latch_alow u_3latch_alow_1 (
    .On_1(on), .Off_1(off), .in_3(on_2), .in_4(out_17), .in_5(out_18), .in_6(out_19), .Q1(n3latch_alow_1_q1),
    .out_8(n3latch_alow_1_out_8), .out_9(n3latch_alow_1_out_9));
  LED #(.active("false")) led_2 (.in(n3latch_alow_1_out_8));
  LED #(.active("false")) led_3 (.in(n3latch_alow_1_out_9));
  LED #(.active("false")) led_4 (.in(n3latch_alow_2_q1));
  _3latch_alow u_3latch_alow_2 (
    .On_1(out_20), .Off_1(out_21), .in_3(out_22), .in_4(out_23), .in_5(out_24), .in_6(out_25),
    .Q1(n3latch_alow_2_q1), .out_8(n3latch_alow_2_out_8), .out_9(n3latch_alow_2_out_9));
  LED #(.active("false")) led_5 (.in(n3latch_alow_2_out_8));
  LED #(.active("false")) led_6 (.in(n3latch_alow_2_out_9));

  // Notes on the sheet:
  //   N R
  //   N R
  //   N Y
  //   N Y
  //   N G
  //   on
  //   off
  //   off
  //   E R
  //   N G
  //   on
  //   E Y
  //   E R
  //   on
  //   off
  //   E Y
  //   E G
  //   on
  //   off
  //   off
  //   E G
  //   "Microcode"
  //   0. turn N red off, and n green on 
  //   1. turn N green off, N yellow on
  //   2. turn N yellow off, turn N red on
  //   3. turn E red off, turn E green on
  //   4. turn E green off, turn E yellow on
  //   5. turn E yellow off, turn E red on
  //   6. goto 0
  //   North/South
  //   East/West
endmodule

module latch_demo (
  output out_1,
  output out_2,
  output out_3,
  output out_4,
  output out_5,
  output out_6
);

  wire button_1_out, button_2_out, button_3_out, button_4_out, button_5_out, button_6_out,
       n3latch_alow_1_out_8, n3latch_alow_1_out_9, n3latch_alow_1_q1;

  Button button_1 (.out(button_1_out));
  Button button_2 (.out(button_2_out));
  Button button_3 (.out(button_3_out));
  Button button_4 (.out(button_4_out));
  Button button_5 (.out(button_5_out));
  Button button_6 (.out(button_6_out));
  not not_1 (out_1, button_1_out);
  not not_2 (out_2, button_2_out);
  not not_3 (out_3, button_3_out);
  not not_4 (out_4, button_4_out);
  not not_5 (out_5, button_5_out);
  not not_6 (out_6, button_6_out);
  LED #(.active("false")) led_1 (.in(n3latch_alow_1_q1));
  _3latch_alow u_3latch_alow_1 (
    .On_1(out_1), .Off_1(out_2), .in_3(out_3), .in_4(out_4), .in_5(out_5), .in_6(out_6),
    .Q1(n3latch_alow_1_q1), .out_8(n3latch_alow_1_out_8), .out_9(n3latch_alow_1_out_9));
  LED #(.active("false")) led_2 (.in(n3latch_alow_1_out_8));
  LED #(.active("false")) led_3 (.in(n3latch_alow_1_out_9));
endmodule

module _3latch_alow (
  input  On_1,
  input  Off_1,
  input  in_3,
  input  in_4,
  input  in_5,
  input  in_6,
  output Q1,
  output out_8,
  output out_9
);

  wire not_1_out, not_2_out, not_3_out, not_4_out, not_5_out, not_6_out;

  not not_1 (not_1_out, On_1);
  not not_2 (not_2_out, Off_1);
  not not_3 (not_3_out, in_3);
  not not_4 (not_4_out, in_4);
  not not_5 (not_5_out, in_5);
  not not_6 (not_6_out, in_6);
  D_Flip_Flop d_ff_1 (.clk(1'b0), .Qn(Q1), .preset(not_1_out), .en(1'b1), .reset(not_2_out));  // open: D, Q
  D_Flip_Flop d_ff_2 (.clk(1'b0), .Qn(out_8), .preset(not_3_out), .en(1'b1), .reset(not_4_out));  // open: D, Q
  D_Flip_Flop d_ff_3 (.clk(1'b0), .Qn(out_9), .preset(not_5_out), .en(1'b1), .reset(not_6_out));  // open: D, Q
endmodule

module fsm_full (
  output out_1,
  output out_2,
  output out_3,
  output out_4,
  output out_5,
  output out_6,
  output [2:0] out_7,
  output [2:0] out_8,
  output out_9,
  output out_10,
  output out_11,
  output out_12,
  output out_13,
  output out_14
);

  wire clock_1_out, decoder_1_out0, decoder_1_out1, decoder_1_out2, decoder_1_out3, decoder_1_out4,
       decoder_1_out5, reset_out;

  Button reset (.out(reset_out));
  Clock clock_1 (.out(clock_1_out));
  Register #(.width(3)) _3_bit_register (.D(out_8), .Q(out_7), .clk(clock_1_out), .clr(reset_out));  // open: en
  Decoder #(.select(3), .enable("false")) decoder_1 (
    .out0(decoder_1_out0), .out1(decoder_1_out1), .out2(decoder_1_out2), .out3(decoder_1_out3),
    .out4(decoder_1_out4), .out5(decoder_1_out5), .sel(out_7));  // open: out6, out7
  Pull_Resistor #(.pull(1)) pull_resistor_1 (.node(out_9));
  not not_1 (out_1, decoder_1_out0);
  not not_2 (out_2, decoder_1_out1);
  tiny_diode tiny_diode_1 (._0_1_in(out_3), ._0_Z_out(out_9));
  not not_3 (out_3, decoder_1_out2);
  tiny_diode tiny_diode_2 (._0_1_in(out_4), ._0_Z_out(out_9));
  not not_4 (out_4, decoder_1_out3);
  tiny_diode tiny_diode_3 (._0_1_in(out_5), ._0_Z_out(out_9));
  not not_5 (out_5, decoder_1_out4);
  tiny_diode tiny_diode_4 (._0_1_in(out_6), ._0_Z_out(out_9));
  not not_6 (out_6, decoder_1_out5);
  Pull_Resistor #(.pull(1)) pull_resistor_2 (.node(out_11));
  Pull_Resistor #(.pull(1)) pull_resistor_3 (.node(out_10));
  tiny_diode tiny_diode_5 (._0_1_in(out_1), ._0_Z_out(out_11));
  tiny_diode tiny_diode_6 (._0_1_in(out_2), ._0_Z_out(out_10));
  Pull_Resistor #(.pull(1)) pull_resistor_4 (.node(out_13));
  Pull_Resistor #(.pull(1)) pull_resistor_5 (.node(out_12));
  tiny_diode tiny_diode_7 (._0_1_in(out_1), ._0_Z_out(out_12));
  tiny_diode tiny_diode_8 (._0_1_in(out_2), ._0_Z_out(out_12));
  tiny_diode tiny_diode_9 (._0_1_in(out_3), ._0_Z_out(out_12));
  tiny_diode tiny_diode_10 (._0_1_in(out_5), ._0_Z_out(out_13));
  tiny_diode tiny_diode_11 (._0_1_in(out_6), ._0_Z_out(out_12));
  Pull_Resistor #(.pull(1)) pull_resistor_6 ();  // open: node
  Pull_Resistor #(.pull(1)) pull_resistor_7 (.node(out_14));
  tiny_diode tiny_diode_12 (._0_1_in(out_4), ._0_Z_out(out_14));
  Pull_Resistor #(.pull(1)) pull_resistor_8 ();  // open: node
  Pull_Resistor #(.pull(1)) pull_resistor_9 ();  // open: node
  Pull_Resistor #(.pull(1)) pull_resistor_10 ();  // open: node
  Pull_Resistor #(.pull(1)) pull_resistor_11 (.node(out_8[2]));
  tiny_diode tiny_diode_13 (._0_1_in(out_1), ._0_Z_out(out_8[2]));
  tiny_diode tiny_diode_14 (._0_1_in(out_2), ._0_Z_out(out_8[2]));
  tiny_diode tiny_diode_15 (._0_1_in(out_3), ._0_Z_out(out_8[2]));
  tiny_diode tiny_diode_16 (._0_1_in(out_6), ._0_Z_out(out_8[2]));
  Pull_Resistor #(.pull(1)) pull_resistor_12 (.node(out_8[1]));
  Pull_Resistor #(.pull(1)) pull_resistor_13 (.node(out_8[0]));
  tiny_diode tiny_diode_17 (._0_1_in(out_1), ._0_Z_out(out_8[1]));
  tiny_diode tiny_diode_18 (._0_1_in(out_2), ._0_Z_out(out_8[0]));
  tiny_diode tiny_diode_19 (._0_1_in(out_4), ._0_Z_out(out_8[1]));
  tiny_diode tiny_diode_20 (._0_1_in(out_4), ._0_Z_out(out_8[0]));
  tiny_diode tiny_diode_21 (._0_1_in(out_5), ._0_Z_out(out_8[1]));
  tiny_diode tiny_diode_22 (._0_1_in(out_6), ._0_Z_out(out_8[0]));
  tiny_diode tiny_diode_23 (._0_1_in(out_6), ._0_Z_out(out_8[1]));
  LED #(.active("false")) led_1 (.in(out_9));
  LED #(.active("false")) led_2 (.in(out_10));
  LED #(.active("false")) led_3 (.in(out_11));
  LED #(.active("false")) led_4 (.in(out_12));
  LED #(.active("false")) led_5 (.in(out_13));
  LED #(.active("false")) led_6 (.in(out_14));

  // Notes on the sheet:
  //   N
  //   E
  //   NG, ER
  //   NY, ER
endmodule

module fsm_skel_1 (
  output out_1,
  output out_2,
  output out_3,
  output out_4,
  output out_5,
  output out_6,
  output [2:0] out_7,
  output out_8,
  output out_9,
  output out_10,
  output [2:0] out_11,
  output out_12,
  output out_13,
  output out_14,
  output out_15,
  output out_16,
  output out_17
);

  wire clock_out, decoder_1_out0, decoder_1_out1, decoder_1_out2, decoder_1_out3, decoder_1_out4,
       decoder_1_out5, reset_out;

  Button clock (.out(clock_out));
  Button reset (.out(reset_out));
  Register #(.width(3)) _3_bit_register (
    .D({out_8, out_9, out_10}), .Q(out_7), .clk(clock_out), .clr(reset_out));  // open: en
  Decoder #(.select(3), .enable("false")) decoder_1 (
    .out0(decoder_1_out0), .out1(decoder_1_out1), .out2(decoder_1_out2), .out3(decoder_1_out3),
    .out4(decoder_1_out4), .out5(decoder_1_out5), .sel(out_7));  // open: out6, out7
  Pull_Resistor #(.pull(1)) pull_resistor_1 (.node(out_12));
  not not_1 (out_1, decoder_1_out0);
  not not_2 (out_2, decoder_1_out1);
  not not_3 (out_3, decoder_1_out2);
  not not_4 (out_4, decoder_1_out3);
  not not_5 (out_5, decoder_1_out4);
  not not_6 (out_6, decoder_1_out5);
  Pull_Resistor #(.pull(1)) pull_resistor_2 (.node(out_14));
  Pull_Resistor #(.pull(1)) pull_resistor_3 (.node(out_13));
  Pull_Resistor #(.pull(1)) pull_resistor_4 (.node(out_16));
  Pull_Resistor #(.pull(1)) pull_resistor_5 (.node(out_15));
  Pull_Resistor #(.pull(1)) pull_resistor_6 (.node(out_17));
  Pull_Resistor #(.pull(1)) pull_resistor_7 ();  // open: node
  Pull_Resistor #(.pull(1)) pull_resistor_8 ();  // open: node
  Pull_Resistor #(.pull(1)) pull_resistor_9 ();  // open: node
  Pull_Resistor #(.pull(1)) pull_resistor_10 ();  // open: node
  Pull_Resistor #(.pull(1)) pull_resistor_11 (.node(out_8));
  Pull_Resistor #(.pull(1)) pull_resistor_12 (.node(out_10));
  Pull_Resistor #(.pull(1)) pull_resistor_13 (.node(out_9));
  LED #(.active("false")) led_1 (.in(out_12));
  LED #(.active("false")) led_2 (.in(out_13));
  LED #(.active("false")) led_3 (.in(out_14));
  LED #(.active("false")) led_4 (.in(out_15));
  LED #(.active("false")) led_5 (.in(out_16));
  LED #(.active("false")) led_6 (.in(out_17));

  assign out_11 = {out_8, out_9, out_10};
endmodule

module fsm_skel_0 (
  output out_1,
  output out_2,
  output out_3,
  output out_4,
  output out_5,
  output out_6,
  output [2:0] out_7,
  output out_8,
  output out_9,
  output out_10,
  output out_11,
  output out_12,
  output out_13
);

  wire clock_out, decoder_1_out0, decoder_1_out1, decoder_1_out2, decoder_1_out3, decoder_1_out4,
       decoder_1_out5, reset_out;
  wire [2:0] undriven;

  Button clock (.out(clock_out));
  Button reset (.out(reset_out));
  Register #(.width(3)) _3_bit_register (.D(undriven), .Q(out_7), .clk(clock_out), .clr(reset_out));  // open: en
  Decoder #(.select(3), .enable("false")) decoder_1 (
    .out0(decoder_1_out0), .out1(decoder_1_out1), .out2(decoder_1_out2), .out3(decoder_1_out3),
    .out4(decoder_1_out4), .out5(decoder_1_out5), .sel(out_7));  // open: out6, out7
  Pull_Resistor #(.pull(1)) pull_resistor_1 (.node(out_8));
  not not_1 (out_1, decoder_1_out0);
  not not_2 (out_2, decoder_1_out1);
  not not_3 (out_3, decoder_1_out2);
  not not_4 (out_4, decoder_1_out3);
  not not_5 (out_5, decoder_1_out4);
  not not_6 (out_6, decoder_1_out5);
  Pull_Resistor #(.pull(1)) pull_resistor_2 (.node(out_9));
  Pull_Resistor #(.pull(1)) pull_resistor_3 (.node(out_10));
  tiny_diode tiny_diode_1 (._0_1_in(out_1), ._0_Z_out(out_8));
  Pull_Resistor #(.pull(1)) pull_resistor_4 (.node(out_11));
  Pull_Resistor #(.pull(1)) pull_resistor_5 (.node(out_12));
  Pull_Resistor #(.pull(1)) pull_resistor_6 (.node(out_13));
  Pull_Resistor #(.pull(1)) pull_resistor_7 ();  // open: node
  Pull_Resistor #(.pull(1)) pull_resistor_8 ();  // open: node
  Pull_Resistor #(.pull(1)) pull_resistor_9 ();  // open: node
  Pull_Resistor #(.pull(1)) pull_resistor_10 ();  // open: node
  Pull_Resistor #(.pull(1)) pull_resistor_11 ();  // open: node
  Pull_Resistor #(.pull(1)) pull_resistor_12 ();  // open: node
  Pull_Resistor #(.pull(1)) pull_resistor_13 ();  // open: node
  LED #(.active("false")) led_1 (.in(out_8));
  LED #(.active("false")) led_2 (.in(out_9));
  LED #(.active("false")) led_3 (.in(out_10));
  LED #(.active("false")) led_4 (.in(out_11));
  LED #(.active("false")) led_5 (.in(out_12));
  LED #(.active("false")) led_6 (.in(out_13));

  // Notes on the sheet:
  //   N/S
  //   E/W
endmodule

module tiny_diode (
  input  _0_1_in,
  output _0_Z_out
);

  wire not_1_out, pull_resistor_1_node;

  Pull_Resistor #(.pull(1)) pull_resistor_1 (.node(pull_resistor_1_node));
  buf buffer_1 (pull_resistor_1_node, _0_1_in);
  assign _0_Z_out = not_1_out ? pull_resistor_1_node : 1'bz;  // Controlled_Buffer controlled_buffer_1
  not not_1 (not_1_out, pull_resistor_1_node);
endmodule

module basic_light (
  input  in_1,
  input  in_2,
  input  in_3,
  input  in_4,
  input  in_5,
  input  in_6
);

  LED #(.active("false")) R (.in(in_1));
  LED #(.active("false")) Y (.in(in_2));
  LED #(.active("false")) G (.in(in_3));
  LED #(.active("false")) R_2 (.in(in_4));
  LED #(.active("false")) Y_2 (.in(in_5));
  LED #(.active("false")) G_2 (.in(in_6));

  // Notes on the sheet:
  //   (LEDs configured to light with a "0," like real ones)
endmodule
