// Logisim project io.circ as structural Verilog
module out (
);

  wire clock_out, reset_out;
  wire [7:0] register_1_q;

  Register register_1 (.Q(register_1_q));  // open: D, en, clk, clr
  TTY #(.rows(1)) tty_1 (.data(register_1_q[6:0]), .clk(clock_out), .clr(reset_out));  // open: we
  Button clock (.out(clock_out));
  Button reset (.out(reset_out));

  // Notes on the sheet:
  //   (LogiSim TTY)
endmodule

module in (
  output data_ready
);

  wire clock_out, reset_out;
  wire [6:0] keyboard_1_data;

  Keyboard keyboard_1 (.clk(clock_out), .clr(reset_out), .avail(data_ready), .data(keyboard_1_data));  // open: re
  Button clock (.out(clock_out));
  Button reset (.out(reset_out));
  // Probe on keyboard_1_data

  // Notes on the sheet:
  //   (LogiSim keyboard)
endmodule
